// Logisim project MYPart.circ as structural Verilog: 17 circuits, main circuit main
module main (
  input  [6:0] KeyBoard,
  output [1:0] compas,
  output [2:0] S3,
  output [2:0] S2,
  output [2:0] S1,
  output [2:0] S0,
  output [4:0] mult,
  output [2:0] POST_KEY,
  output [2:0] DOOR,
  output Key_tact,
  output SECRET,
  output [1:0] MONSTER_pos,
  output USE
);

  wire and_4_out, cdm_8_mark5_1_data_inst, cdm_8_mark5_1_mem_cycle, code, controlled_inverter_1_out,
       counter_1_carry, data, End, generated, go, IAck, IOsel, IRQ, keyborat_1_was_readed, not_1_out,
       or_1_out, R_W, rClc, reset, tck;
  wire [2:0] IOaddr, level, vec;
  wire [7:0] cdm_8_mark5_1_data_out, cdm_8_mark5_1_pc, cdm_8_mark5_1_ps, cdm_8_mark5_1_r0, cdm_8_mark5_1_r1,
       cdm_8_mark5_1_r2, cdm_8_mark5_1_r3, cdm_8_mark5_1_sp, controlled_buffer_2_out, IOdat, kPx, kPy,
       lab_gen_1_bus_1, lab_gen_1_bus_2, lab_gen_1_bus_3, lab_gen_1_bus_4, lab_gen_1_bus_5, lab_gen_1_bus_6,
       lab_gen_1_bus_7, lab_gen_1_bus_8, MPx, MPy, Px, Py, rnd;
  wire [7:3] cdm_8_mark5_1_addr;

  Pull_Resistor pull_resistor_1 (.node(code));
  Pull_Resistor pull_resistor_2 (.node(IRQ));
  Pull_Resistor pull_resistor_3 (.node(data));
  // Probe on cdm_8_mark5_1_r0
  Clock clock_1 (.out(rClc));
  and and_1 (tck, rClc, ~End, generated);  // AND_Gate
  Counter #(.width(2), .max('h2)) counter_1 (
    .carry(counter_1_carry), .clk(controlled_inverter_1_out), .clr(or_1_out));  // open: load, D, count, Q
  or or_1 (or_1_out, reset, Key_tact);
  assign controlled_inverter_1_out = keyborat_1_was_readed ? ~tck : 1'bz;  // Controlled_Inverter controlled_inverter_1
  Pull_Resistor pull_resistor_4 (.node(controlled_inverter_1_out));
  // Probe on cdm_8_mark5_1_r3
  // Probe on cdm_8_mark5_1_r2
  // Probe on cdm_8_mark5_1_r1
  // Probe on cdm_8_mark5_1_sp
  // Probe on cdm_8_mark5_1_pc
  and and_2 (Key_tact, counter_1_carry, tck);
  // Probe on cdm_8_mark5_1_ps
  Decoder #(.disabled(0)) decoder_1 (
    .out0(code), .out1(data), .sel(cdm_8_mark5_1_data_inst), .en(cdm_8_mark5_1_mem_cycle));
  CdM_8_mark5 cdm_8_mark5_1 (
    .clock(tck), .addr({cdm_8_mark5_1_addr, IOaddr}), .mem_read(R_W), .mem_cycle(cdm_8_mark5_1_mem_cycle),
    .data_inst(cdm_8_mark5_1_data_inst), .data_out(cdm_8_mark5_1_data_out),
    .data_in(controlled_buffer_2_out), .r0(cdm_8_mark5_1_r0), .r1(cdm_8_mark5_1_r1), .r2(cdm_8_mark5_1_r2),
    .r3(cdm_8_mark5_1_r3), .PC(cdm_8_mark5_1_pc), .SP(cdm_8_mark5_1_sp), .PS(cdm_8_mark5_1_ps), .IAck(IAck),
    .IRQ(IRQ), .vec(vec), .reset(reset));
  not not_1 (not_1_out, R_W);
  assign IOdat = not_1_out ? cdm_8_mark5_1_data_out : 8'bz;  // Controlled_Buffer controlled_buffer_1
  assign controlled_buffer_2_out = R_W ? IOdat : 8'bz;  // Controlled_Buffer controlled_buffer_2
  KeyBorat keyborat_1 (
    .ADDRESS(IOaddr), .SEL(IOsel), .R_W(R_W), .was_readed(keyborat_1_was_readed), .DATA(IOdat), .USE(USE),
    .reset(reset), .keyboard(KeyBoard), .GO(go));
  RNDon_don rndon_don_1 (
    .ADDRESS(IOaddr), .SEL(IOsel), .R_W(R_W), .DATA(IOdat), .seed(level), .rnd_out(rnd), .clc(rClc),
    .rst(reset));
  and and_3 (IOsel, cdm_8_mark5_1_addr[3], cdm_8_mark5_1_addr[4], cdm_8_mark5_1_addr[5], cdm_8_mark5_1_addr[7], cdm_8_mark5_1_addr[6], data);
  and and_4 (and_4_out, ~IOsel, data);  // AND_Gate
  ROM rom_1 (.addr({cdm_8_mark5_1_addr, IOaddr}), .data(IOdat), .sel(code));
  RAM ram_1 (.addr({cdm_8_mark5_1_addr, IOaddr}), .data(IOdat), .sel(and_4_out), .clk(tck), .ld(R_W), .clr(reset));
  Lab_gen lab_gen_1 (
    .gen_finished(generated), .rnd_in(rnd), .ADDRESS(IOaddr), .SEL(IOsel), .R_W(R_W), .DATA_OUT(IOdat),
    .DATA_INPUT(IOdat), .reset(reset), .bus_1(lab_gen_1_bus_1), .bus_2(lab_gen_1_bus_2),
    .bus_3(lab_gen_1_bus_3), .bus_4(lab_gen_1_bus_4), .bus_5(lab_gen_1_bus_5), .bus_6(lab_gen_1_bus_6),
    .bus_7(lab_gen_1_bus_7), .bus_8(lab_gen_1_bus_8));
  Maskarade maskarade_1 (
    .bus_1(lab_gen_1_bus_1), .bus_2(lab_gen_1_bus_2), .bus_3(lab_gen_1_bus_3), .bus_4(lab_gen_1_bus_4),
    .bus_5(lab_gen_1_bus_5), .bus_6(lab_gen_1_bus_6), .bus_7(lab_gen_1_bus_7), .bus_8(lab_gen_1_bus_8),
    .Px(Px), .Py(Py), .ADDRESS(IOaddr), .SEL(IOsel), .R_W(R_W), .DATA_OUT(IOdat), .DATA_INPUT(IOdat),
    .out3(S3), .out2(S2), .out1(S1), .out0(S0), .compass(compas), .reset(reset), .tact(tck), .go(go),
    .mons(mult[0]), .kPosX(kPx), .kPosY(kPy), .MPosX(MPx), .MPosY(MPy));
  walk_engine walk_engine_1 (
    .Px(Px), .Py(Py), .out1(S1), .compass(compas), .ADDRESS(IOaddr), .SEL(IOsel), .R_W(R_W), .DATA_OUT(IOdat));
  MapEntity mapentity_1 (
    .PlayerX(Px), .PlayerY(Py), .compass(compas), .UsePressed(USE), .S1(S1), .mult(mult),
    .POST_KEY(POST_KEY), .DOOR(DOOR), .Hdoor(SECRET), .MONSTER_pos(MONSTER_pos), .ADDRESS(IOaddr),
    .SEL(IOsel), .R_W(R_W), .DATA_INPUT(IOdat), .difficulty(2'b01), .reset(reset), .kPosY(kPy), .kPosX(kPx),
    .MposX(MPx), .MposY(MPy), .level(level));
  or or_2 (End, mult[4], mult[3], mult[2]);

  // Other names for the same wires on the sheet: compass[1:0] = compas; mons = mult[0]

  // Notes on the sheet:
  //   contents of rom_1 (hex, n*v repeats v):
  //   d1 1 d0 70 a1 d1 1 d0 6f a1 d0 fa a0 d3 6f d1 76 7d ec 36 d0 fd b1 d2 7 46 ae 8f d0 fb a2 b0 d1 ff
  //   8d 94 e3 28 ee 22 d2 8 79 e1 30 8b ee 14 ad 8f d1 76 ee 11 d0 fa d1 71 b6 a2 8d b6 a2 8d b6 a2 8d b6
  //   a2 8d b6 a2 8d b6 a2 d0 0 d1 0 d2 0 d3 0 d1 fe d2 0 b8 a4 d0 70 b0 a4 d0 6f b0 a4 d0 6e b0 a4 ee 69
  //   ee 8c d2 0 ee 67 d4 9*0 d0 f8 b2 d3 6e bf d1 1 47 f e1 87 d1 6f ee 89 d1 70 a6 ee 53 d0 fc b2 a e0
  //   a9 9 b d2 8 76 e1 9b ee a9 d2 6 76 e1 a4 ee 77 ee a9 d0 6e a1 ee 53 ee 69
endmodule

module KeyBorat (
  input  [2:0] ADDRESS,
  input  SEL,
  input  R_W,
  input  reset,
  input  [6:0] keyboard,
  output [7:0] DATA,
  output was_readed,
  output GO,
  output USE
);

  wire comparator_2_eq, comparator_4_eq, comparator_5_eq, comparator_6_eq, comparator_7_eq, comparator_8_eq,
       comparator_9_eq, comparator_10_eq, comparator_11_eq, comparator_12_eq, comparator_13_eq,
       comparator_14_eq, comparator_15_eq, comparator_16_eq, comparator_17_eq, comparator_18_eq,
       comparator_19_eq, comparator_20_eq, comparator_21_eq, comparator_22_eq, IO_3R, IO_3W, not_1_out,
       or_2_out, pull_resistor_1_node, pull_resistor_3_node;
  wire [2:1] A_out;
  wire [3:0] controlled_buffer_2_out, controlled_buffer_4_out, controlled_buffer_10_out, Prev_rot;
  wire [7:0] bit_extender_1_out, data_out;

  and u_IO_3R (IO_3R, R_W, SEL, ~ADDRESS[0], ~ADDRESS[1], ADDRESS[2]);  // AND_Gate
  or or_1 (was_readed, reset, IO_3R);
  and u_IO_3W (IO_3W, ~R_W, SEL, ~ADDRESS[0], ~ADDRESS[1], ADDRESS[2]);  // AND_Gate
  assign bit_extender_1_out = {{1{1'b0}}, keyboard};  // Bit_Extender bit_extender_1
  Pull_Resistor pull_resistor_1 (.node(pull_resistor_1_node));
  Comparator comparator_1 (.a(8'h77), .b(bit_extender_1_out), .eq(pull_resistor_1_node));  // open: gt, lt
  Comparator comparator_2 (.a(8'h57), .b(bit_extender_1_out), .eq(comparator_2_eq));  // open: gt, lt
  Pull_Resistor pull_resistor_2 (.node(comparator_2_eq));
  Pull_Resistor pull_resistor_3 (.node(pull_resistor_3_node));
  Comparator comparator_3 (.a(8'h61), .b(bit_extender_1_out), .eq(pull_resistor_3_node));  // open: gt, lt
  Comparator comparator_4 (.a(8'h41), .b(bit_extender_1_out), .eq(comparator_4_eq));  // open: gt, lt
  Pull_Resistor pull_resistor_4 (.node(comparator_4_eq));
  Comparator comparator_5 (.a(8'h64), .b(bit_extender_1_out), .eq(comparator_5_eq));  // open: gt, lt
  Pull_Resistor pull_resistor_5 (.node(comparator_5_eq));
  Comparator comparator_6 (.a(8'h44), .b(bit_extender_1_out), .eq(comparator_6_eq));  // open: gt, lt
  Pull_Resistor pull_resistor_6 (.node(comparator_6_eq));
  Comparator comparator_7 (.a(8'h65), .b(bit_extender_1_out), .eq(comparator_7_eq));  // open: gt, lt
  Pull_Resistor pull_resistor_7 (.node(comparator_7_eq));
  Comparator comparator_8 (.a(8'h45), .b(bit_extender_1_out), .eq(comparator_8_eq));  // open: gt, lt
  Pull_Resistor pull_resistor_8 (.node(comparator_8_eq));
  or W (GO, pull_resistor_1_node, comparator_2_eq);
  or A (A_out[1], pull_resistor_3_node, comparator_4_eq);
  or D (A_out[2], comparator_5_eq, comparator_6_eq);
  or E (USE, comparator_7_eq, comparator_8_eq);
  assign DATA = IO_3R ? data_out : 8'bz;  // Controlled_Buffer controlled_buffer_1
  Comparator #(.width(4)) comparator_9 (.a(4'b0010), .b({USE, A_out, GO}), .eq(comparator_9_eq));  // open: gt, lt
  Comparator #(.width(4)) comparator_10 (.a(4'b0100), .b({USE, A_out, GO}), .eq(comparator_10_eq));  // open: gt, lt
  Comparator #(.width(4)) comparator_11 (.a(4'b0001), .b({USE, A_out, GO}), .eq(comparator_11_eq));  // open: gt, lt
  assign controlled_buffer_2_out = comparator_11_eq ? 4'b0110 : 4'bz;  // Controlled_Buffer controlled_buffer_2
  Comparator #(.width(4)) comparator_12 (.a(4'b1000), .b({USE, A_out, GO}), .eq(comparator_12_eq));  // open: gt, lt
  assign controlled_buffer_2_out = comparator_12_eq ? 4'b1000 : 4'bz;  // Controlled_Buffer controlled_buffer_3
  or or_2 (or_2_out, A_out[1], A_out[2]);
  Comparator #(.width(4)) comparator_13 (.a(4'b0000), .b(Prev_rot), .eq(comparator_13_eq));  // open: gt, lt
  Comparator #(.width(4)) comparator_14 (.a(4'b0100), .b(Prev_rot), .eq(comparator_14_eq));  // open: gt, lt
  Comparator #(.width(4)) comparator_15 (.a(4'b0011), .b(Prev_rot), .eq(comparator_15_eq));  // open: gt, lt
  Comparator #(.width(4)) comparator_16 (.a(4'b0010), .b(Prev_rot), .eq(comparator_16_eq));  // open: gt, lt
  Comparator #(.width(4)) comparator_17 (.a(4'b0001), .b(Prev_rot), .eq(comparator_17_eq));  // open: gt, lt
  // Probe on controlled_buffer_2_out
  assign controlled_buffer_4_out = comparator_13_eq ? 4'b0011 : 4'bz;  // Controlled_Buffer controlled_buffer_4
  assign controlled_buffer_4_out = comparator_14_eq ? 4'b0011 : 4'bz;  // Controlled_Buffer controlled_buffer_5
  assign controlled_buffer_4_out = comparator_15_eq ? 4'b0010 : 4'bz;  // Controlled_Buffer controlled_buffer_6
  assign controlled_buffer_4_out = comparator_16_eq ? 4'b0001 : 4'bz;  // Controlled_Buffer controlled_buffer_7
  assign controlled_buffer_4_out = comparator_17_eq ? 4'b0100 : 4'bz;  // Controlled_Buffer controlled_buffer_8
  assign controlled_buffer_2_out = comparator_9_eq ? controlled_buffer_4_out : 4'bz;  // Controlled_Buffer controlled_buffer_9
  Register #(.width(4)) register_1 (
    .D(controlled_buffer_2_out), .Q(Prev_rot), .clk(not_1_out), .clr(reset));  // open: en
  not not_1 (not_1_out, or_2_out);
  Comparator #(.width(4)) comparator_18 (.a(4'b0000), .b(Prev_rot), .eq(comparator_18_eq));  // open: gt, lt
  assign controlled_buffer_10_out = comparator_18_eq ? 4'b0001 : 4'bz;  // Controlled_Buffer controlled_buffer_10
  Comparator #(.width(4)) comparator_19 (.a(4'b0100), .b(Prev_rot), .eq(comparator_19_eq));  // open: gt, lt
  assign controlled_buffer_10_out = comparator_19_eq ? 4'b0001 : 4'bz;  // Controlled_Buffer controlled_buffer_11
  Comparator #(.width(4)) comparator_20 (.a(4'b0001), .b(Prev_rot), .eq(comparator_20_eq));  // open: gt, lt
  assign controlled_buffer_10_out = comparator_20_eq ? 4'b0010 : 4'bz;  // Controlled_Buffer controlled_buffer_12
  Comparator #(.width(4)) comparator_21 (.a(4'b0010), .b(Prev_rot), .eq(comparator_21_eq));  // open: gt, lt
  assign controlled_buffer_10_out = comparator_21_eq ? 4'b0011 : 4'bz;  // Controlled_Buffer controlled_buffer_13
  Comparator #(.width(4)) comparator_22 (.a(4'b0011), .b(Prev_rot), .eq(comparator_22_eq));  // open: gt, lt
  assign controlled_buffer_10_out = comparator_22_eq ? 4'b0100 : 4'bz;  // Controlled_Buffer controlled_buffer_14
  assign controlled_buffer_2_out = comparator_10_eq ? controlled_buffer_10_out : 4'bz;  // Controlled_Buffer controlled_buffer_15
  // Probe on Prev_rot
  assign data_out = {{4{1'b0}}, controlled_buffer_2_out};  // Bit_Extender bit_extender_2

  // Notes on the sheet:
  //   I/O interface
  //   address: 100
endmodule

module Lab_gen (
  input  [2:0] ADDRESS,
  input  SEL,
  input  R_W,
  input  [7:0] DATA_INPUT,
  input  [7:0] rnd_in,
  input  reset,
  output [7:0] DATA_OUT,
  output [7:0] bus_1,
  output [7:0] bus_2,
  output [7:0] bus_3,
  output [7:0] bus_4,
  output [7:0] bus_5,
  output [7:0] bus_6,
  output [7:0] bus_7,
  output [7:0] bus_8,
  output gen_finished
);

  wire add, and_3_out, and_4_out, and_5_out, and_6_out, and_7_out, and_8_out, and_9_out, and_10_out,
       and_11_out, and_12_out, and_13_out, and_14_out, and_15_out, and_16_out, and_17_out, and_18_out,
       and_19_out, clc, clock_1_out, comparator_1_eq, comparator_2_eq, comparator_3_eq, comparator_4_eq,
       counter_1_carry, counter_2_carry, demultiplexer_1_out0, demultiplexer_1_out1, demultiplexer_1_out2,
       demultiplexer_1_out3, demultiplexer_1_out4, demultiplexer_1_out5, demultiplexer_1_out6,
       demultiplexer_1_out7, demultiplexer_2_out0, demultiplexer_2_out1, demultiplexer_2_out2,
       demultiplexer_2_out3, demultiplexer_2_out4, demultiplexer_2_out5, demultiplexer_2_out6,
       demultiplexer_2_out7, IO_3R, IO_3W, isY, not_1_out, not_2_out, not_3_out, not_4_out, not_5_out,
       not_6_out, not_7_out, not_8_out, not_9_out, not_10_out, not_11_out, not_12_out, not_13_out,
       not_14_out, not_15_out, not_16_out, not_18_out, not_20_out;
  wire [1:0] controlled_buffer_1_out, controlled_buffer_3_out, controlled_buffer_5_out,
       controlled_buffer_6_out, controlled_buffer_9_out, controlled_buffer_11_out, controlled_buffer_12_out,
       controlled_buffer_15_out, controlled_buffer_16_out, controlled_buffer_19_out,
       controlled_buffer_20_out, controlled_buffer_23_out, controlled_buffer_24_out;
  wire [2:0] adder_2_out, adder_3_out, and_20_out, and_21_out, controlled_buffer_27_out,
       controlled_buffer_29_out, controlled_buffer_31_out, controlled_buffer_33_out, counter_1_q, curX, curY,
       subtractor_1_out, subtractor_2_out;
  wire [2:2] not_17_out, not_19_out;
  wire [7:0] data_out_t, register_1_q;

  and and_1 (gen_finished, counter_1_carry, counter_2_carry);
  Clock clock_1 (.out(clock_1_out));
  and and_2 (clc, clock_1_out, not_1_out);
  not not_1 (not_1_out, gen_finished);
  Counter #(.width(3), .max('h6)) counter_1 (
    .count(clc), .Q(counter_1_q), .carry(counter_1_carry), .clk(clc), .clr(reset));  // open: load, D
  Counter #(.width(3), .max('h7), .trigger("falling")) counter_2 (
    .count(clc), .Q(curY), .carry(counter_2_carry), .clk(counter_1_carry), .clr(reset));  // open: load, D
  and u_IO_3R (IO_3R, R_W, SEL, ADDRESS[0], ADDRESS[1], ~ADDRESS[2]);  // AND_Gate
  and u_IO_3W (IO_3W, ~R_W, SEL, ADDRESS[0], ADDRESS[1], ~ADDRESS[2]);  // AND_Gate
  Adder #(.width(3)) adder_1 (.a(counter_1_q), .b(3'b001), .out(curX));  // open: cin, cout
  not not_2 (not_2_out, gen_finished);
  assign controlled_buffer_1_out = not_2_out ? rnd_in[7:6] : 2'bz;  // Controlled_Buffer controlled_buffer_1
  and and_3 (and_3_out, ~curX[0], ~curX[1], ~curX[2]);  // AND_Gate
  and and_4 (and_4_out, ~curY[0], ~curY[1], ~curY[2]);  // AND_Gate
  and and_5 (and_5_out, curX[0], curX[1], curX[2]);
  and and_6 (and_6_out, curY[0], curY[1], curY[2]);
  assign DATA_OUT = IO_3R ? data_out_t : 8'bz;  // Controlled_Buffer controlled_buffer_2
  and and_7 (and_7_out, and_3_out, and_4_out);
  and and_8 (and_8_out, ~and_3_out, and_4_out);  // AND_Gate
  and and_9 (and_9_out, and_3_out, ~and_6_out);  // AND_Gate
  and and_10 (and_10_out, and_5_out, and_6_out);
  and and_11 (and_11_out, and_5_out, and_4_out);
  buf and_12 (and_12_out, and_5_out);  // AND_Gate
  buf and_13 (and_13_out, and_6_out);  // AND_Gate
  and and_14 (and_14_out, and_3_out, and_6_out);
  and and_15 (and_15_out, ~and_10_out, ~and_11_out, ~and_14_out, ~and_7_out);  // AND_Gate
  and and_16 (and_16_out, and_15_out, and_8_out);
  and and_17 (and_17_out, and_15_out, and_9_out);
  and and_18 (and_18_out, and_15_out, and_12_out);
  and and_19 (and_19_out, and_15_out, and_13_out);
  Pull_Resistor pull_resistor_1 (.node(controlled_buffer_1_out[0]));
  assign controlled_buffer_3_out = not_3_out ? controlled_buffer_1_out : 2'bz;  // Controlled_Buffer controlled_buffer_3
  not not_3 (not_3_out, and_7_out);
  assign controlled_buffer_3_out = and_7_out ? controlled_buffer_5_out : 2'bz;  // Controlled_Buffer controlled_buffer_4
  assign controlled_buffer_5_out = not_4_out ? 2'b01 : 2'bz;  // Controlled_Buffer controlled_buffer_5
  not not_4 (not_4_out, controlled_buffer_1_out[0]);
  assign controlled_buffer_6_out = not_5_out ? 2'b00 : 2'bz;  // Controlled_Buffer controlled_buffer_6
  assign controlled_buffer_5_out = controlled_buffer_1_out[0] ? 2'b11 : 2'bz;  // Controlled_Buffer controlled_buffer_7
  not not_5 (not_5_out, controlled_buffer_1_out[0]);
  assign controlled_buffer_6_out = controlled_buffer_1_out[0] ? 2'b10 : 2'bz;  // Controlled_Buffer controlled_buffer_8
  assign controlled_buffer_9_out = not_6_out ? controlled_buffer_3_out : 2'bz;  // Controlled_Buffer controlled_buffer_9
  not not_6 (not_6_out, and_10_out);
  assign controlled_buffer_9_out = and_10_out ? controlled_buffer_6_out : 2'bz;  // Controlled_Buffer controlled_buffer_10
  Comparator #(.width(2)) comparator_1 (.a(2'b10), .b(controlled_buffer_9_out), .eq(comparator_1_eq));  // open: gt, lt
  Comparator #(.width(2)) comparator_2 (.a(2'b00), .b(controlled_buffer_11_out), .eq(comparator_2_eq));  // open: gt, lt
  Comparator #(.width(2)) comparator_3 (.a(2'b01), .b(controlled_buffer_15_out), .eq(comparator_3_eq));  // open: gt, lt
  Comparator #(.width(2)) comparator_4 (.a(2'b11), .b(controlled_buffer_19_out), .eq(comparator_4_eq));  // open: gt, lt
  assign controlled_buffer_11_out = not_7_out ? controlled_buffer_9_out : 2'bz;  // Controlled_Buffer controlled_buffer_11
  not not_7 (not_7_out, and_16_out);
  assign controlled_buffer_12_out = not_8_out ? controlled_buffer_9_out : 2'bz;  // Controlled_Buffer controlled_buffer_12
  assign controlled_buffer_11_out = and_16_out ? controlled_buffer_12_out : 2'bz;  // Controlled_Buffer controlled_buffer_13
  not not_8 (not_8_out, comparator_1_eq);
  assign controlled_buffer_12_out = comparator_1_eq ? 2'b00 : 2'bz;  // Controlled_Buffer controlled_buffer_14
  assign controlled_buffer_15_out = not_9_out ? controlled_buffer_11_out : 2'bz;  // Controlled_Buffer controlled_buffer_15
  not not_9 (not_9_out, and_17_out);
  assign controlled_buffer_16_out = not_10_out ? controlled_buffer_11_out : 2'bz;  // Controlled_Buffer controlled_buffer_16
  assign controlled_buffer_15_out = and_17_out ? controlled_buffer_16_out : 2'bz;  // Controlled_Buffer controlled_buffer_17
  not not_10 (not_10_out, comparator_2_eq);
  assign controlled_buffer_16_out = comparator_2_eq ? 2'b01 : 2'bz;  // Controlled_Buffer controlled_buffer_18
  assign controlled_buffer_19_out = not_11_out ? controlled_buffer_15_out : 2'bz;  // Controlled_Buffer controlled_buffer_19
  not not_11 (not_11_out, and_18_out);
  assign controlled_buffer_20_out = not_12_out ? controlled_buffer_15_out : 2'bz;  // Controlled_Buffer controlled_buffer_20
  assign controlled_buffer_19_out = and_18_out ? controlled_buffer_20_out : 2'bz;  // Controlled_Buffer controlled_buffer_21
  not not_12 (not_12_out, comparator_3_eq);
  assign controlled_buffer_20_out = comparator_3_eq ? 2'b00 : 2'bz;  // Controlled_Buffer controlled_buffer_22
  assign controlled_buffer_23_out = not_13_out ? controlled_buffer_19_out : 2'bz;  // Controlled_Buffer controlled_buffer_23
  not not_13 (not_13_out, and_19_out);
  assign controlled_buffer_24_out = not_14_out ? controlled_buffer_19_out : 2'bz;  // Controlled_Buffer controlled_buffer_24
  assign controlled_buffer_23_out = and_19_out ? controlled_buffer_24_out : 2'bz;  // Controlled_Buffer controlled_buffer_25
  not not_14 (not_14_out, comparator_4_eq);
  assign controlled_buffer_24_out = comparator_4_eq ? 2'b10 : 2'bz;  // Controlled_Buffer controlled_buffer_26
  Multiplexer #(.select(2), .width(2)) multiplexer_1 (
    .in0(2'b00), .in1(2'b01), .in2(2'b10), .in3(2'b11), .out({isY, add}), .sel(controlled_buffer_23_out));  // open: en
  Register #(.trigger("high")) register_1 (.D(DATA_INPUT), .Q(register_1_q), .clk(IO_3W), .clr(reset));  // open: en
  Adder #(.width(3)) adder_2 (.a(curX), .b(3'b001), .out(adder_2_out));  // open: cin, cout
  Subtractor #(.width(3)) subtractor_1 (.a(curX), .b(3'b001), .out(subtractor_1_out));  // open: bin, bout
  Multiplexer #(.select(3), .width(8)) multiplexer_2 (
    .in0(bus_1), .in1(bus_2), .in2(bus_3), .in3(bus_4), .in4(bus_5), .in5(bus_6), .in6(bus_7), .in7(bus_8),
    .out(data_out_t), .sel(register_1_q[2:0]));  // open: en
  assign controlled_buffer_27_out = add ? adder_2_out : 3'bz;  // Controlled_Buffer controlled_buffer_27
  not not_15 (not_15_out, add);
  assign controlled_buffer_27_out = not_15_out ? subtractor_1_out : 3'bz;  // Controlled_Buffer controlled_buffer_28
  assign controlled_buffer_29_out = not_16_out ? controlled_buffer_27_out : 3'bz;  // Controlled_Buffer controlled_buffer_29
  not not_16 (not_16_out, isY);
  assign controlled_buffer_29_out = isY ? curX : 3'bz;  // Controlled_Buffer controlled_buffer_30
  not not_17 (not_17_out[2], clc);
  Demultiplexer #(.select(3)) demultiplexer_1 (
    .out0(demultiplexer_1_out0), .out1(demultiplexer_1_out1), .out2(demultiplexer_1_out2),
    .out3(demultiplexer_1_out3), .out4(demultiplexer_1_out4), .out5(demultiplexer_1_out5),
    .out6(demultiplexer_1_out6), .out7(demultiplexer_1_out7), .in(1'b1), .sel(and_20_out));  // open: en
  // Probe on and_20_out
  assign and_20_out = controlled_buffer_29_out & {3{not_17_out[2]}};  // AND_Gate and_20, 3 bits wide
  Adder #(.width(3)) adder_3 (.a(curY), .b(3'b001), .out(adder_3_out));  // open: cin, cout
  Subtractor #(.width(3)) subtractor_2 (.a(curY), .b(3'b001), .out(subtractor_2_out));  // open: bin, bout
  simplestTrigger simplesttrigger_1 (.y(demultiplexer_1_out0), .out(bus_1[7]), .x(demultiplexer_2_out0), .res(reset));
  simplestTrigger simplesttrigger_2 (.y(demultiplexer_1_out1), .out(bus_2[7]), .x(demultiplexer_2_out0), .res(reset));
  simplestTrigger simplesttrigger_3 (.y(demultiplexer_1_out2), .out(bus_3[7]), .x(demultiplexer_2_out0), .res(reset));
  simplestTrigger simplesttrigger_4 (.y(demultiplexer_1_out3), .out(bus_4[7]), .x(demultiplexer_2_out0), .res(reset));
  simplestTrigger simplesttrigger_5 (.y(demultiplexer_1_out4), .out(bus_5[7]), .x(demultiplexer_2_out0), .res(reset));
  simplestTrigger simplesttrigger_6 (.y(demultiplexer_1_out5), .out(bus_6[7]), .x(demultiplexer_2_out0), .res(reset));
  simplestTrigger simplesttrigger_7 (.y(demultiplexer_1_out6), .out(bus_7[7]), .x(demultiplexer_2_out0), .res(reset));
  simplestTrigger simplesttrigger_8 (.y(demultiplexer_1_out7), .out(bus_8[7]), .x(demultiplexer_2_out0), .res(reset));
  assign controlled_buffer_31_out = add ? adder_3_out : 3'bz;  // Controlled_Buffer controlled_buffer_31
  not not_18 (not_18_out, add);
  assign controlled_buffer_31_out = not_18_out ? subtractor_2_out : 3'bz;  // Controlled_Buffer controlled_buffer_32
  not not_19 (not_19_out[2], clc);
  assign controlled_buffer_33_out = isY ? controlled_buffer_31_out : 3'bz;  // Controlled_Buffer controlled_buffer_33
  not not_20 (not_20_out, isY);
  assign controlled_buffer_33_out = not_20_out ? curY : 3'bz;  // Controlled_Buffer controlled_buffer_34
  simplestTrigger simplesttrigger_9 (.y(demultiplexer_1_out0), .out(bus_1[5]), .x(demultiplexer_2_out2), .res(reset));
  simplestTrigger simplesttrigger_10 (.y(demultiplexer_1_out0), .out(bus_1[6]), .x(demultiplexer_2_out1), .res(reset));
  simplestTrigger simplesttrigger_11 (.y(demultiplexer_1_out1), .out(bus_2[6]), .x(demultiplexer_2_out1), .res(reset));
  simplestTrigger simplesttrigger_12 (.y(demultiplexer_1_out1), .out(bus_2[5]), .x(demultiplexer_2_out2), .res(reset));
  simplestTrigger simplesttrigger_13 (.y(demultiplexer_1_out2), .out(bus_3[5]), .x(demultiplexer_2_out2), .res(reset));
  simplestTrigger simplesttrigger_14 (.y(demultiplexer_1_out2), .out(bus_3[6]), .x(demultiplexer_2_out1), .res(reset));
  simplestTrigger simplesttrigger_15 (.y(demultiplexer_1_out3), .out(bus_4[6]), .x(demultiplexer_2_out1), .res(reset));
  simplestTrigger simplesttrigger_16 (.y(demultiplexer_1_out3), .out(bus_4[5]), .x(demultiplexer_2_out2), .res(reset));
  simplestTrigger simplesttrigger_17 (.y(demultiplexer_1_out4), .out(bus_5[6]), .x(demultiplexer_2_out1), .res(reset));
  simplestTrigger simplesttrigger_18 (.y(demultiplexer_1_out4), .out(bus_5[5]), .x(demultiplexer_2_out2), .res(reset));
  simplestTrigger simplesttrigger_19 (.y(demultiplexer_1_out5), .out(bus_6[5]), .x(demultiplexer_2_out2), .res(reset));
  simplestTrigger simplesttrigger_20 (.y(demultiplexer_1_out5), .out(bus_6[6]), .x(demultiplexer_2_out1), .res(reset));
  simplestTrigger simplesttrigger_21 (.y(demultiplexer_1_out6), .out(bus_7[5]), .x(demultiplexer_2_out2), .res(reset));
  simplestTrigger simplesttrigger_22 (.y(demultiplexer_1_out6), .out(bus_7[6]), .x(demultiplexer_2_out1), .res(reset));
  simplestTrigger simplesttrigger_23 (.y(demultiplexer_1_out7), .out(bus_8[5]), .x(demultiplexer_2_out2), .res(reset));
  simplestTrigger simplesttrigger_24 (.y(demultiplexer_1_out7), .out(bus_8[6]), .x(demultiplexer_2_out1), .res(reset));
  assign and_21_out = {3{not_19_out[2]}} & controlled_buffer_33_out;  // AND_Gate and_21, 3 bits wide
  // Probe on and_21_out
  simplestTrigger simplesttrigger_25 (.y(demultiplexer_1_out0), .out(bus_1[4]), .x(demultiplexer_2_out3), .res(reset));
  simplestTrigger simplesttrigger_26 (.y(demultiplexer_1_out1), .out(bus_2[4]), .x(demultiplexer_2_out3), .res(reset));
  simplestTrigger simplesttrigger_27 (.y(demultiplexer_1_out2), .out(bus_3[4]), .x(demultiplexer_2_out3), .res(reset));
  simplestTrigger simplesttrigger_28 (.y(demultiplexer_1_out3), .out(bus_4[4]), .x(demultiplexer_2_out3), .res(reset));
  simplestTrigger simplesttrigger_29 (.y(demultiplexer_1_out4), .out(bus_5[4]), .x(demultiplexer_2_out3), .res(reset));
  simplestTrigger simplesttrigger_30 (.y(demultiplexer_1_out5), .out(bus_6[4]), .x(demultiplexer_2_out3), .res(reset));
  simplestTrigger simplesttrigger_31 (.y(demultiplexer_1_out6), .out(bus_7[4]), .x(demultiplexer_2_out3), .res(reset));
  simplestTrigger simplesttrigger_32 (.y(demultiplexer_1_out7), .out(bus_8[4]), .x(demultiplexer_2_out3), .res(reset));
  Demultiplexer #(.select(3)) demultiplexer_2 (
    .out0(demultiplexer_2_out0), .out1(demultiplexer_2_out1), .out2(demultiplexer_2_out2),
    .out3(demultiplexer_2_out3), .out4(demultiplexer_2_out4), .out5(demultiplexer_2_out5),
    .out6(demultiplexer_2_out6), .out7(demultiplexer_2_out7), .in(1'b1), .sel(and_21_out));  // open: en
  simplestTrigger simplesttrigger_33 (.y(demultiplexer_1_out0), .out(bus_1[3]), .x(demultiplexer_2_out4), .res(reset));
  simplestTrigger simplesttrigger_34 (.y(demultiplexer_1_out1), .out(bus_2[3]), .x(demultiplexer_2_out4), .res(reset));
  simplestTrigger simplesttrigger_35 (.y(demultiplexer_1_out2), .out(bus_3[3]), .x(demultiplexer_2_out4), .res(reset));
  simplestTrigger simplesttrigger_36 (.y(demultiplexer_1_out3), .out(bus_4[3]), .x(demultiplexer_2_out4), .res(reset));
  simplestTrigger simplesttrigger_37 (.y(demultiplexer_1_out4), .out(bus_5[3]), .x(demultiplexer_2_out4), .res(reset));
  simplestTrigger simplesttrigger_38 (.y(demultiplexer_1_out5), .out(bus_6[3]), .x(demultiplexer_2_out4), .res(reset));
  simplestTrigger simplesttrigger_39 (.y(demultiplexer_1_out6), .out(bus_7[3]), .x(demultiplexer_2_out4), .res(reset));
  simplestTrigger simplesttrigger_40 (.y(demultiplexer_1_out7), .out(bus_8[3]), .x(demultiplexer_2_out4), .res(reset));
  simplestTrigger simplesttrigger_41 (.y(demultiplexer_1_out0), .out(bus_1[2]), .x(demultiplexer_2_out5), .res(reset));
  simplestTrigger simplesttrigger_42 (.y(demultiplexer_1_out0), .out(bus_1[1]), .x(demultiplexer_2_out6), .res(reset));
  simplestTrigger simplesttrigger_43 (.y(demultiplexer_1_out1), .out(bus_2[1]), .x(demultiplexer_2_out6), .res(reset));
  simplestTrigger simplesttrigger_44 (.y(demultiplexer_1_out1), .out(bus_2[2]), .x(demultiplexer_2_out5), .res(reset));
  simplestTrigger simplesttrigger_45 (.y(demultiplexer_1_out2), .out(bus_3[1]), .x(demultiplexer_2_out6), .res(reset));
  simplestTrigger simplesttrigger_46 (.y(demultiplexer_1_out2), .out(bus_3[2]), .x(demultiplexer_2_out5), .res(reset));
  simplestTrigger simplesttrigger_47 (.y(demultiplexer_1_out3), .out(bus_4[1]), .x(demultiplexer_2_out6), .res(reset));
  simplestTrigger simplesttrigger_48 (.y(demultiplexer_1_out3), .out(bus_4[2]), .x(demultiplexer_2_out5), .res(reset));
  simplestTrigger simplesttrigger_49 (.y(demultiplexer_1_out4), .out(bus_5[1]), .x(demultiplexer_2_out6), .res(reset));
  simplestTrigger simplesttrigger_50 (.y(demultiplexer_1_out4), .out(bus_5[2]), .x(demultiplexer_2_out5), .res(reset));
  simplestTrigger simplesttrigger_51 (.y(demultiplexer_1_out5), .out(bus_6[2]), .x(demultiplexer_2_out5), .res(reset));
  simplestTrigger simplesttrigger_52 (.y(demultiplexer_1_out5), .out(bus_6[1]), .x(demultiplexer_2_out6), .res(reset));
  simplestTrigger simplesttrigger_53 (.y(demultiplexer_1_out6), .out(bus_7[1]), .x(demultiplexer_2_out6), .res(reset));
  simplestTrigger simplesttrigger_54 (.y(demultiplexer_1_out6), .out(bus_7[2]), .x(demultiplexer_2_out5), .res(reset));
  simplestTrigger simplesttrigger_55 (.y(demultiplexer_1_out7), .out(bus_8[2]), .x(demultiplexer_2_out5), .res(reset));
  simplestTrigger simplesttrigger_56 (.y(demultiplexer_1_out7), .out(bus_8[1]), .x(demultiplexer_2_out6), .res(reset));
  simplestTrigger simplesttrigger_57 (.y(demultiplexer_1_out0), .out(bus_1[0]), .x(demultiplexer_2_out7), .res(reset));
  simplestTrigger simplesttrigger_58 (.y(demultiplexer_1_out1), .out(bus_2[0]), .x(demultiplexer_2_out7), .res(reset));
  simplestTrigger simplesttrigger_59 (.y(demultiplexer_1_out2), .out(bus_3[0]), .x(demultiplexer_2_out7), .res(reset));
  simplestTrigger simplesttrigger_60 (.y(demultiplexer_1_out3), .out(bus_4[0]), .x(demultiplexer_2_out7), .res(reset));
  simplestTrigger simplesttrigger_61 (.y(demultiplexer_1_out4), .out(bus_5[0]), .x(demultiplexer_2_out7), .res(reset));
  simplestTrigger simplesttrigger_62 (.y(demultiplexer_1_out5), .out(bus_6[0]), .x(demultiplexer_2_out7), .res(reset));
  simplestTrigger simplesttrigger_63 (.y(demultiplexer_1_out6), .out(bus_7[0]), .x(demultiplexer_2_out7), .res(reset));
  simplestTrigger simplesttrigger_64 (.y(demultiplexer_1_out7), .out(bus_8[0]), .x(demultiplexer_2_out7), .res(reset));

  // Other names for the same wires on the sheet: _07 = bus_1[0]; _06 = bus_1[1]; _05 = bus_1[2]; _04 = bus_1[3];
  //   _03 = bus_1[4]; _02 = bus_1[5]; _01 = bus_1[6]; _00 = bus_1[7]; _17 = bus_2[0]; _16 = bus_2[1]; _15 = bus_2[2];
  //   _14 = bus_2[3]; _13 = bus_2[4]; _12 = bus_2[5]; _11 = bus_2[6]; _10 = bus_2[7]; _27 = bus_3[0]; _26 = bus_3[1];
  //   _25 = bus_3[2]; _24 = bus_3[3]; _23 = bus_3[4]; _22 = bus_3[5]; _21 = bus_3[6]; _20 = bus_3[7]; _37 = bus_4[0];
  //   _36 = bus_4[1]; _35 = bus_4[2]; _34 = bus_4[3]; _33 = bus_4[4]; _32 = bus_4[5]; _31 = bus_4[6]; _30 = bus_4[7];
  //   _47 = bus_5[0]; _46 = bus_5[1]; _45 = bus_5[2]; _44 = bus_5[3]; _43 = bus_5[4]; _42 = bus_5[5]; _41 = bus_5[6];
  //   _40 = bus_5[7]; _57 = bus_6[0]; _56 = bus_6[1]; _55 = bus_6[2]; _54 = bus_6[3]; _53 = bus_6[4]; _52 = bus_6[5];
  //   _51 = bus_6[6]; _50 = bus_6[7]; _67 = bus_7[0]; _66 = bus_7[1]; _65 = bus_7[2]; _64 = bus_7[3]; _63 = bus_7[4];
  //   _62 = bus_7[5]; _61 = bus_7[6]; _60 = bus_7[7]; _77 = bus_8[0]; _76 = bus_8[1]; _75 = bus_8[2]; _74 = bus_8[3];
  //   _73 = bus_8[4]; _72 = bus_8[5]; _71 = bus_8[6]; _70 = bus_8[7]; data_in[7:0] = DATA_INPUT; end = gen_finished;
  //   res = reset

  // Notes on the sheet:
  //   XxY
  //   I/O interface
  //   address: 011
  //   XxY
  //   0x0
  //   Xx0
  //   0xX
  //   7x7
  //   7x0
  //   7xX
  //   Xx7
  //   0x7
  //   рандом, 2 бита
  //   углы
  //   0x0
  //   0x7
  //   7x0
  //   7x7
  //   не углы
  //   Xx0
  //   0xX
  //   7xX
  //   Xx7
  //   1 или 3
  //   0 или 2
  //   не 2
  //   не 0
  //   не 1
  //   не 3
  //   X
  //   Y
endmodule

module Maskarade (
  input  [2:0] ADDRESS,
  input  SEL,
  input  R_W,
  input  [7:0] DATA_INPUT,
  input  reset,
  input  [7:0] bus_1,
  input  [7:0] bus_2,
  input  [7:0] bus_3,
  input  [7:0] bus_4,
  input  [7:0] bus_5,
  input  [7:0] bus_6,
  input  [7:0] bus_7,
  input  [7:0] bus_8,
  input  [7:0] kPosX,
  input  tact,
  input  [7:0] kPosY,
  input  mons,
  input  go,
  output [7:0] DATA_OUT,
  output [2:0] out3,
  output [2:0] out2,
  output [2:0] out1,
  output [2:0] out0,
  output [7:0] Px,
  output [7:0] Py,
  output [1:0] compass,
  output [7:0] MPosX,
  output [7:0] MPosY
);

  wire and_1_out, and_2_out, and_3_out, and_4_out, and_5_out, and_6_out, and_7_out, and_8_out, chang,
       comparator_1_eq, comparator_2_eq, comparator_3_eq, counter_4_carry, demultiplexer_2_out0,
       demultiplexer_2_out1, demultiplexer_2_out2, demultiplexer_3_out0, demultiplexer_3_out1,
       demultiplexer_3_out2, go_t, IO_3R, IO_3W, isanywire_1_output, or_1_out, x_is, y_is;
  wire [1:0] counter_1_q, counter_2_q, counter_5_q, now;
  wire [2:0] multiplexer_1_out, multiplexer_2_out, multiplexer_3_out, multiplexer_4_out,
       take_3_by_x_lr_1_out0, take_3_by_x_lr_1_out1, take_3_by_x_lr_1_out2, take_3_by_x_lr_1_out3,
       take_3_by_x_ud_1_out0, take_3_by_x_ud_1_out1, take_3_by_x_ud_1_out2, take_3_by_x_ud_1_out3;
  wire [7:0] data_out_t, demultiplexer_1_out1, demultiplexer_1_out2, demultiplexer_1_out3, register_1_q,
       register_2_q, register_6_q, register_7_q, register_8_q, register_9_q, take_3_by_y_lr_1_out0,
       take_3_by_y_lr_1_out1, take_3_by_y_lr_1_out2, take_3_by_y_ud_1_out0, take_3_by_y_ud_1_out1,
       take_3_by_y_ud_1_out2, take_3_by_y_ud_1_out3;
  wire [7:2] register_5_q;

  Counter #(.width(2), .max('h3), .ongoal("stay")) counter_1 (
    .Q(counter_1_q), .clk(tact), .clr(and_1_out));  // open: load, D, count, carry
  and and_1 (and_1_out, go_t, chang);
  Counter #(.width(2), .max('h3), .ongoal("stay")) counter_2 (
    .Q(counter_2_q), .clk(tact), .clr(and_2_out));  // open: load, D, count, carry
  and and_2 (and_2_out, go_t, chang);
  Counter #(.width(1), .max('h1), .ongoal("stay"), .trigger("falling")) counter_3 (
    .Q(go_t), .clk(go), .clr(and_3_out));  // open: load, D, count, carry
  and and_3 (and_3_out, now[1], now[0]);
  and u_IO_3R (IO_3R, R_W, SEL, ~ADDRESS[0], ADDRESS[1], ADDRESS[2]);  // AND_Gate
  and u_IO_3W (IO_3W, ~R_W, SEL, ~ADDRESS[0], ADDRESS[1], ADDRESS[2]);  // AND_Gate
  Demultiplexer #(.select(2), .width(8)) demultiplexer_1 (
    .out1(demultiplexer_1_out1), .out2(demultiplexer_1_out2), .out3(demultiplexer_1_out3), .in(DATA_INPUT),
    .sel(now), .en(IO_3W));  // open: out0
  Counter #(.width(2), .max('h3), .trigger("falling")) counter_4 (
    .Q(now), .carry(counter_4_carry), .clk(IO_3W), .clr(reset));  // open: load, D, count
  Demultiplexer #(.select(2), .disabled(0), .enable("false")) demultiplexer_2 (
    .out0(demultiplexer_2_out0), .out1(demultiplexer_2_out1), .out2(demultiplexer_2_out2), .in(1'b1),
    .sel(counter_1_q));  // open: out3
  Demultiplexer #(.select(2), .disabled(0), .enable("false")) demultiplexer_3 (
    .out0(demultiplexer_3_out0), .out1(demultiplexer_3_out1), .out2(demultiplexer_3_out2), .in(1'b1),
    .sel(counter_2_q));  // open: out3
  MyAddress2pin myaddress2pin_1 (.address(now), .data(2'b01), .allow(IO_3W), .change(x_is));
  MyAddress2pin myaddress2pin_2 (.address(now), .data(2'b10), .allow(IO_3W), .change(y_is));
  Register register_1 (.D(Px), .Q(register_1_q), .clk(demultiplexer_2_out2), .clr(reset));  // open: en
  Register register_2 (.D(Py), .Q(register_2_q), .clk(demultiplexer_3_out2), .clr(reset));  // open: en
  assign DATA_OUT = IO_3R ? data_out_t : 8'bz;  // Controlled_Buffer controlled_buffer_1
  Register #(.trigger("high")) register_3 (.D(demultiplexer_1_out1), .Q(Px), .clk(x_is), .clr(reset));  // open: en
  Register #(.trigger("high")) register_4 (.D(demultiplexer_1_out2), .Q(Py), .clk(y_is), .clr(reset));  // open: en
  Register #(.trigger("high")) register_5 (
    .D(demultiplexer_1_out3), .Q({register_5_q, compass}), .clk(isanywire_1_output), .clr(reset));  // open: en
  isAnyWire isanywire_1 (.\input (demultiplexer_1_out3), .\output (isanywire_1_output));
  Register register_6 (.D(register_7_q), .Q(register_6_q), .clk(demultiplexer_2_out0), .clr(reset));  // open: en
  Register register_7 (.D(register_1_q), .Q(register_7_q), .clk(demultiplexer_2_out1), .clr(reset));  // open: en
  Comparator comparator_1 (.a(register_1_q), .b(Px), .eq(comparator_1_eq));  // open: gt, lt
  Comparator comparator_2 (.a(Py), .b(register_2_q), .eq(comparator_2_eq));  // open: gt, lt
  Register register_8 (.D(register_2_q), .Q(register_8_q), .clk(demultiplexer_3_out1), .clr(reset));  // open: en
  not not_1 (chang, and_4_out);
  and and_4 (and_4_out, comparator_1_eq, comparator_2_eq);
  Register register_9 (.D(register_8_q), .Q(register_9_q), .clk(demultiplexer_3_out0), .clr(reset));  // open: en
  and and_5 (and_5_out, compass[1], ~compass[0]);  // AND_Gate
  Take_3_by_Y_LR take_3_by_y_lr_1 (
    .x0(bus_1), .x1(bus_2), .x2(bus_3), .x3(bus_4), .x4(bus_5), .x5(bus_6), .x6(bus_7), .x7(bus_8),
    .posY(Py), .out0(take_3_by_y_lr_1_out0), .out1(take_3_by_y_lr_1_out1), .out2(take_3_by_y_lr_1_out2));
  Take_3_by_Y_UD take_3_by_y_ud_1 (
    .x0(bus_1), .x1(bus_2), .x2(bus_3), .x3(bus_4), .x4(bus_5), .x5(bus_6), .x6(bus_7), .x7(bus_8),
    .posY(Py), .DU(and_6_out), .out0(take_3_by_y_ud_1_out0), .out1(take_3_by_y_ud_1_out1),
    .out2(take_3_by_y_ud_1_out2), .out3(take_3_by_y_ud_1_out3));
  and and_6 (and_6_out, ~compass[1], ~compass[0]);  // AND_Gate
  and and_7 (and_7_out, ~compass[1], ~and_5_out);  // AND_Gate
  Take_3_by_X_LR take_3_by_x_lr_1 (
    .in0(take_3_by_y_lr_1_out0), .in1(take_3_by_y_lr_1_out1), .in2(take_3_by_y_lr_1_out2), .posX(Px),
    .LR(and_7_out), .out0(take_3_by_x_lr_1_out0), .out1(take_3_by_x_lr_1_out1), .out2(take_3_by_x_lr_1_out2),
    .out3(take_3_by_x_lr_1_out3));
  Take_3_by_X_UD take_3_by_x_ud_1 (
    .in0(take_3_by_y_ud_1_out0), .in1(take_3_by_y_ud_1_out1), .in2(take_3_by_y_ud_1_out2),
    .in3(take_3_by_y_ud_1_out3), .posX(Px), .DU(and_6_out), .out0(take_3_by_x_ud_1_out0),
    .out1(take_3_by_x_ud_1_out1), .out2(take_3_by_x_ud_1_out2), .out3(take_3_by_x_ud_1_out3));
  or or_1 (or_1_out, and_6_out, and_5_out);
  Counter #(.width(2), .max('h2), .ongoal("stay"), .trigger("falling")) counter_5 (
    .Q(counter_5_q), .clk(and_8_out), .clr(reset));  // open: load, D, count, carry
  and and_8 (and_8_out, mons, go_t, chang);
  Register #(.width(3), .trigger("high")) register_10 (
    .D(multiplexer_1_out), .Q(out3), .clk(counter_4_carry));  // open: en, clr
  Multiplexer #(.width(3), .disabled(0), .enable("false")) multiplexer_1 (
    .in0(take_3_by_x_lr_1_out0), .in1(take_3_by_x_ud_1_out0), .out(multiplexer_1_out), .sel(or_1_out));
  Register #(.width(3), .trigger("high")) register_11 (
    .D(multiplexer_2_out), .Q(out2), .clk(counter_4_carry));  // open: en, clr
  Multiplexer #(.width(3), .disabled(0), .enable("false")) multiplexer_2 (
    .in0(take_3_by_x_lr_1_out1), .in1(take_3_by_x_ud_1_out1), .out(multiplexer_2_out), .sel(or_1_out));
  Register #(.width(3), .trigger("high")) register_12 (
    .D(multiplexer_3_out), .Q(out1), .clk(counter_4_carry));  // open: en, clr
  Multiplexer #(.width(3), .disabled(0), .enable("false")) multiplexer_3 (
    .in0(take_3_by_x_lr_1_out2), .in1(take_3_by_x_ud_1_out2), .out(multiplexer_3_out), .sel(or_1_out));
  Register #(.width(3), .trigger("high")) register_13 (
    .D(multiplexer_4_out), .Q(out0), .clk(counter_4_carry));  // open: en, clr
  Multiplexer #(.width(3), .disabled(0), .enable("false")) multiplexer_4 (
    .in0(take_3_by_x_lr_1_out3), .in1(take_3_by_x_ud_1_out3), .out(multiplexer_4_out), .sel(or_1_out));
  Comparator #(.width(2)) comparator_3 (.a(2'b10), .b(counter_5_q), .eq(comparator_3_eq));  // open: gt, lt
  Multiplexer #(.width(8), .disabled(0), .enable("false")) multiplexer_5 (
    .in0(kPosX), .in1(register_6_q), .out(MPosX), .sel(comparator_3_eq));
  Multiplexer #(.width(8), .disabled(0), .enable("false")) multiplexer_6 (
    .in0(kPosY), .in1(register_9_q), .out(MPosY), .sel(comparator_3_eq));

  // Other names for the same wires on the sheet: data_in[7:0] = DATA_INPUT

  // Notes on the sheet:
  //   I/O interface
  //   address: 110
  //   Не забывать пустое обращение
  //   Px
  //   Py
  //   look
  //   up
  //   down
  //   по X
  //   по Y
  //   предпредыдущий ход
  //   2 назад
  //   left
endmodule

module RNDon_don (
  input  [2:0] ADDRESS,
  input  SEL,
  input  R_W,
  input  clc,
  input  rst,
  input  [2:0] seed,
  output [7:0] DATA,
  output [7:0] rnd_out
);

  wire IO_3R, IO_3W, or_1_out;
  wire [7:0] random_1_out, random_2_out, random_3_out, random_4_out, random_5_out, random_6_out,
       random_7_out, random_8_out;

  and u_IO_3R (IO_3R, R_W, SEL, ADDRESS[0], ~ADDRESS[1], ADDRESS[2]);  // AND_Gate
  and u_IO_3W (IO_3W, ~R_W, SEL, ADDRESS[0], ~ADDRESS[1], ADDRESS[2]);  // AND_Gate
  assign DATA = IO_3R ? rnd_out : 8'bz;  // Controlled_Buffer controlled_buffer_1
  or or_1 (or_1_out, IO_3R, clc);
  Random #(.seed(30)) random_1 (.clk(or_1_out), .next(or_1_out), .out(random_1_out), .clr(rst));
  Random #(.seed(11)) random_2 (.clk(or_1_out), .next(or_1_out), .out(random_2_out), .clr(rst));
  Random #(.seed(228481)) random_3 (.clk(or_1_out), .next(or_1_out), .out(random_3_out), .clr(rst));
  Random #(.seed(228481)) random_4 (.clk(or_1_out), .next(or_1_out), .out(random_4_out), .clr(rst));
  Random #(.seed(5789856)) random_5 (.clk(or_1_out), .next(or_1_out), .out(random_5_out), .clr(rst));
  Random #(.seed(656456)) random_6 (.clk(or_1_out), .next(or_1_out), .out(random_6_out), .clr(rst));
  Random #(.seed(754678)) random_7 (.clk(or_1_out), .next(or_1_out), .out(random_7_out), .clr(rst));
  Random #(.seed(878456)) random_8 (.clk(or_1_out), .next(or_1_out), .out(random_8_out), .clr(rst));
  Multiplexer #(.select(3), .width(8)) multiplexer_1 (
    .in0(random_1_out), .in1(random_2_out), .in2(random_3_out), .in3(random_4_out), .in4(random_5_out),
    .in5(random_6_out), .in6(random_7_out), .in7(random_8_out), .out(rnd_out), .sel(seed));  // open: en

  // Other names for the same wires on the sheet: data_out[7:0] = rnd_out

  // Notes on the sheet:
  //   I/O interface
  //   address: 101
endmodule

module walk_engine (
  input  [2:0] ADDRESS,
  input  SEL,
  input  R_W,
  input  [7:0] Px,
  input  [7:0] Py,
  input  [2:0] out1,
  input  [1:0] compass,
  output [7:0] DATA_OUT
);

  wire add, adder_1_cout, IO_3R, IO_3W, isY, not_2_out, not_3_out, not_4_out;
  wire [7:0] adder_1_out, controlled_buffer_2_out, controlled_buffer_4_out, data_out_t, subtractor_1_out;

  and u_IO_3R (IO_3R, R_W, SEL, ~ADDRESS[0], ~ADDRESS[1], ~ADDRESS[2]);  // AND_Gate
  and u_IO_3W (IO_3W, ~R_W, SEL, ~ADDRESS[0], ~ADDRESS[1], ~ADDRESS[2]);  // AND_Gate
  assign DATA_OUT = IO_3R ? data_out_t : 8'bz;  // Controlled_Buffer controlled_buffer_1
  xor xor_1 (add, compass[1], compass[0]);
  not not_1 (isY, compass[0]);
  // Probe on Px
  // Probe on Py
  assign controlled_buffer_2_out = not_2_out ? Px : 8'bz;  // Controlled_Buffer controlled_buffer_2
  not not_2 (not_2_out, isY);
  assign controlled_buffer_2_out = isY ? Py : 8'bz;  // Controlled_Buffer controlled_buffer_3
  Adder adder_1 (.a(controlled_buffer_2_out), .b(8'h1), .out(adder_1_out), .cout(adder_1_cout));  // open: cin
  Subtractor subtractor_1 (
    .a(controlled_buffer_2_out), .b(8'h1), .out(subtractor_1_out), .bin(adder_1_cout));  // open: bout
  assign controlled_buffer_4_out = add ? adder_1_out : 8'bz;  // Controlled_Buffer controlled_buffer_4
  not not_3 (not_3_out, add);
  assign controlled_buffer_4_out = not_3_out ? subtractor_1_out : 8'bz;  // Controlled_Buffer controlled_buffer_5
  // Probe on data_out_t
  assign data_out_t = out1[1] ? controlled_buffer_4_out : 8'bz;  // Controlled_Buffer controlled_buffer_6
  not not_4 (not_4_out, out1[1]);
  assign data_out_t = not_4_out ? controlled_buffer_2_out : 8'bz;  // Controlled_Buffer controlled_buffer_7

  // Other names for the same wires on the sheet: c0 = compass[0]; c1 = compass[1]; MA = out1[1]

  // Notes on the sheet:
  //   I/O interface
  //   address:000
endmodule

module Map_reader (
  input  [2:0] ADDRESS,
  input  SEL,
  input  R_W,
  input  [7:0] DATA_INPUT,
  output [7:0] bus_1,
  output [7:0] bus_2,
  output [7:0] bus_3,
  output [7:0] bus_4,
  output [7:0] bus_5,
  output [7:0] bus_6,
  output [7:0] bus_7,
  output [7:0] bus_8
);

  wire IO_3R, IO_3W, isanywire_1_output, isanywire_2_output, isanywire_3_output, isanywire_4_output,
       isanywire_5_output, isanywire_6_output, isanywire_7_output, isanywire_8_output;
  wire [3:0] counter_1_q;
  wire [7:0] demultiplexer_1_out1, demultiplexer_1_out2, demultiplexer_1_out3, demultiplexer_1_out4,
       demultiplexer_1_out5, demultiplexer_1_out6, demultiplexer_1_out7, demultiplexer_1_out8;

  and u_IO_3R (IO_3R, R_W, SEL, ADDRESS[0], ADDRESS[1], ADDRESS[2]);
  and u_IO_3W (IO_3W, ~R_W, SEL, ADDRESS[0], ADDRESS[1], ADDRESS[2]);  // AND_Gate
  Demultiplexer #(.select(4), .width(8)) demultiplexer_1 (
    .out1(demultiplexer_1_out1), .out2(demultiplexer_1_out2), .out3(demultiplexer_1_out3),
    .out4(demultiplexer_1_out4), .out5(demultiplexer_1_out5), .out6(demultiplexer_1_out6),
    .out7(demultiplexer_1_out7), .out8(demultiplexer_1_out8), .in(DATA_INPUT), .sel(counter_1_q), .en(IO_3W));  // open: out0, out9, out10, out11, out12, out13, out14, out15
  Counter #(.width(4), .max('h8), .trigger("falling")) counter_1 (
    .Q(counter_1_q), .clk(IO_3W));  // open: load, D, count, carry, clr
  isAnyWire isanywire_1 (.\input (demultiplexer_1_out1), .\output (isanywire_1_output));
  isAnyWire isanywire_2 (.\input (demultiplexer_1_out2), .\output (isanywire_2_output));
  isAnyWire isanywire_3 (.\input (demultiplexer_1_out3), .\output (isanywire_3_output));
  isAnyWire isanywire_4 (.\input (demultiplexer_1_out4), .\output (isanywire_4_output));
  isAnyWire isanywire_5 (.\input (demultiplexer_1_out5), .\output (isanywire_5_output));
  isAnyWire isanywire_6 (.\input (demultiplexer_1_out6), .\output (isanywire_6_output));
  isAnyWire isanywire_7 (.\input (demultiplexer_1_out7), .\output (isanywire_7_output));
  isAnyWire isanywire_8 (.\input (demultiplexer_1_out8), .\output (isanywire_8_output));
  Register #(.trigger("high")) register_1 (
    .D(demultiplexer_1_out1), .Q(bus_1), .clk(isanywire_1_output));  // open: en, clr
  Register #(.trigger("high")) register_2 (
    .D(demultiplexer_1_out2), .Q(bus_2), .clk(isanywire_2_output));  // open: en, clr
  Register #(.trigger("high")) register_3 (
    .D(demultiplexer_1_out3), .Q(bus_3), .clk(isanywire_3_output));  // open: en, clr
  Register #(.trigger("high")) register_4 (
    .D(demultiplexer_1_out4), .Q(bus_4), .clk(isanywire_4_output));  // open: en, clr
  Register #(.trigger("high")) register_5 (
    .D(demultiplexer_1_out5), .Q(bus_5), .clk(isanywire_5_output));  // open: en, clr
  Register #(.trigger("high")) register_6 (
    .D(demultiplexer_1_out6), .Q(bus_6), .clk(isanywire_6_output));  // open: en, clr
  Register #(.trigger("high")) register_7 (
    .D(demultiplexer_1_out7), .Q(bus_7), .clk(isanywire_7_output));  // open: en, clr
  Register #(.trigger("high")) register_8 (
    .D(demultiplexer_1_out8), .Q(bus_8), .clk(isanywire_8_output));  // open: en, clr

  // Other names for the same wires on the sheet: data_in[7:0] = DATA_INPUT

  // Notes on the sheet:
  //   I/O interface
  //   address: 111
  //   Не забывать пустое обращение
endmodule

module MapEntity (
  input  [2:0] ADDRESS,
  input  SEL,
  input  R_W,
  input  [7:0] DATA_INPUT,
  input  [7:0] PlayerX,
  input  [7:0] PlayerY,
  input  [1:0] compass,
  input  UsePressed,
  input  [2:0] S1,
  input  [1:0] difficulty,
  input  [7:0] MposX,
  input  [7:0] MposY,
  output [4:0] mult,
  output [2:0] POST_KEY,
  output [2:0] DOOR,
  output [7:0] kPosX,
  output [7:0] kPosY,
  output Hdoor,
  output reset,
  output [2:0] level,
  output [1:0] MONSTER_pos
);

  wire add, and_9_out, and_11_out, comparator_1_eq, comparator_2_eq, comparator_3_eq, comparator_4_eq,
       comparator_5_eq, comparator_6_eq, comparator_7_eq, comparator_8_eq, comparator_9_eq, comparator_10_eq,
       comparator_11_eq, comparator_12_eq, comparator_13_eq, happy_end, hide, IO_3R, IO_3W, isY,
       myaddress3pin_1_change, myaddress3pin_2_change, myaddress3pin_3_change, myaddress3pin_4_change,
       myaddress3pin_5_change, myaddress3pin_6_change, not_1_out, not_2_out, not_3_out, not_5_out, not_6_out,
       not_7_out, not_8_out, not_9_out, not_10_out, not_11_out, not_12_out, not_13_out, not_14_out,
       not_15_out, not_16_out, not_18_out, not_19_out, or_1_out, or_3_out, or_4_out;
  wire [1:0] and_3_out;
  wire [2:0] counter_1_q;
  wire [7:0] adder_1_out, adder_2_out, controlled_buffer_1_out, controlled_buffer_3_out,
       controlled_buffer_5_out, controlled_buffer_7_out, controlled_buffer_11_out, controlled_buffer_13_out,
       controlled_buffer_15_out, controlled_buffer_17_out, controlled_buffer_19_out,
       controlled_buffer_21_out, controlled_buffer_25_out, controlled_buffer_27_out,
       controlled_buffer_29_out, counter_4_q, demultiplexer_1_out1, demultiplexer_1_out2,
       demultiplexer_1_out3, demultiplexer_1_out4, demultiplexer_1_out5, demultiplexer_1_out6, Dx, Dy, Hdx,
       Hdy, multiplexer_4_out, PLook0, PLook1, register_3_q, register_4_q, subtractor_1_out, subtractor_2_out;
  wire [7:3] counter_3_q;

  and u_IO_3R (IO_3R, R_W, SEL, ~ADDRESS[0], ADDRESS[1], ~ADDRESS[2]);  // AND_Gate
  and u_IO_3W (IO_3W, ~R_W, SEL, ~ADDRESS[0], ADDRESS[1], ~ADDRESS[2]);  // AND_Gate
  Demultiplexer #(.select(3), .width(8)) demultiplexer_1 (
    .out1(demultiplexer_1_out1), .out2(demultiplexer_1_out2), .out3(demultiplexer_1_out3),
    .out4(demultiplexer_1_out4), .out5(demultiplexer_1_out5), .out6(demultiplexer_1_out6), .in(DATA_INPUT),
    .sel(counter_1_q), .en(IO_3W));  // open: out0, out7
  Counter #(.width(3), .max('h6), .trigger("falling")) counter_1 (
    .Q(counter_1_q), .clk(IO_3W));  // open: load, D, count, carry, clr
  MyAddress3pin myaddress3pin_1 (.address(counter_1_q), .data(3'b010), .allow(IO_3W), .change(myaddress3pin_1_change));
  MyAddress3pin myaddress3pin_2 (.address(counter_1_q), .data(3'b001), .allow(IO_3W), .change(myaddress3pin_2_change));
  MyAddress3pin myaddress3pin_3 (.address(counter_1_q), .data(3'b100), .allow(IO_3W), .change(myaddress3pin_3_change));
  MyAddress3pin myaddress3pin_4 (.address(counter_1_q), .data(3'b011), .allow(IO_3W), .change(myaddress3pin_4_change));
  MyAddress3pin myaddress3pin_5 (.address(counter_1_q), .data(3'b110), .allow(IO_3W), .change(myaddress3pin_5_change));
  MyAddress3pin myaddress3pin_6 (.address(counter_1_q), .data(3'b101), .allow(IO_3W), .change(myaddress3pin_6_change));
  assign controlled_buffer_1_out = not_1_out ? MposX : 8'bz;  // Controlled_Buffer controlled_buffer_1
  not not_1 (not_1_out, isY);
  assign controlled_buffer_1_out = isY ? MposY : 8'bz;  // Controlled_Buffer controlled_buffer_2
  assign controlled_buffer_3_out = not_2_out ? MposY : 8'bz;  // Controlled_Buffer controlled_buffer_3
  not not_2 (not_2_out, isY);
  assign controlled_buffer_3_out = isY ? MposX : 8'bz;  // Controlled_Buffer controlled_buffer_4
  assign controlled_buffer_5_out = not_3_out ? PlayerY : 8'bz;  // Controlled_Buffer controlled_buffer_5
  not not_3 (not_3_out, isY);
  assign controlled_buffer_5_out = isY ? PlayerX : 8'bz;  // Controlled_Buffer controlled_buffer_6
  not not_4 (isY, compass[0]);
  Comparator comparator_1 (.a(PLook0), .b(controlled_buffer_1_out), .eq(comparator_1_eq));  // open: gt, lt
  Comparator comparator_2 (
    .a(controlled_buffer_3_out), .b(controlled_buffer_5_out), .eq(comparator_2_eq));  // open: gt, lt
  Comparator comparator_3 (.a(MposX), .b(PlayerX), .eq(comparator_3_eq));  // open: gt, lt
  Comparator comparator_4 (.a(MposY), .b(PlayerY), .eq(comparator_4_eq));  // open: gt, lt
  assign controlled_buffer_7_out = not_5_out ? PlayerX : 8'bz;  // Controlled_Buffer controlled_buffer_7
  not not_5 (not_5_out, isY);
  assign controlled_buffer_7_out = isY ? PlayerY : 8'bz;  // Controlled_Buffer controlled_buffer_8
  Register #(.trigger("high")) register_1 (
    .D(demultiplexer_1_out2), .Q(Dx), .clk(myaddress3pin_1_change));  // open: en, clr
  Register #(.trigger("high")) register_2 (
    .D(demultiplexer_1_out1), .Q(Dy), .clk(myaddress3pin_2_change));  // open: en, clr
  Register #(.trigger("high")) register_3 (
    .D(demultiplexer_1_out4), .Q(register_3_q), .clk(myaddress3pin_3_change));  // open: en, clr
  Register #(.trigger("high")) register_4 (
    .D(demultiplexer_1_out3), .Q(register_4_q), .clk(myaddress3pin_4_change));  // open: en, clr
  Register #(.trigger("high")) register_5 (
    .D(demultiplexer_1_out6), .Q(kPosX), .clk(myaddress3pin_5_change));  // open: en, clr
  Register #(.trigger("high")) register_6 (
    .D(demultiplexer_1_out5), .Q(kPosY), .clk(myaddress3pin_6_change));  // open: en, clr
  xor xor_1 (add, compass[1], compass[0]);
  Comparator comparator_5 (.a(PLook1), .b(controlled_buffer_1_out), .eq(comparator_5_eq));  // open: gt, lt
  Adder adder_1 (.a(controlled_buffer_7_out), .b(8'h1), .out(adder_1_out));  // open: cin, cout
  Subtractor subtractor_1 (.a(controlled_buffer_7_out), .b(8'h1), .out(subtractor_1_out));  // open: bin, bout
  Multiplexer #(.width(8), .disabled(0), .enable("false")) multiplexer_1 (
    .in0(register_3_q), .in1(8'h80), .out(Hdx), .sel(hide));
  Multiplexer #(.width(8), .disabled(0), .enable("false")) multiplexer_2 (
    .in0(register_4_q), .in1(8'h80), .out(Hdy), .sel(hide));
  and and_1 (and_3_out[1], comparator_5_eq, S1[1]);
  and and_2 (mult[2], comparator_3_eq, DOOR[1], comparator_4_eq);
  assign PLook0 = add ? adder_1_out : 8'bz;  // Controlled_Buffer controlled_buffer_9
  not not_6 (not_6_out, add);
  assign PLook0 = not_6_out ? subtractor_1_out : 8'bz;  // Controlled_Buffer controlled_buffer_10
  assign controlled_buffer_11_out = not_7_out ? kPosX : 8'bz;  // Controlled_Buffer controlled_buffer_11
  not not_7 (not_7_out, isY);
  assign controlled_buffer_11_out = isY ? kPosY : 8'bz;  // Controlled_Buffer controlled_buffer_12
  assign controlled_buffer_13_out = not_8_out ? kPosY : 8'bz;  // Controlled_Buffer controlled_buffer_13
  not not_8 (not_8_out, isY);
  assign controlled_buffer_13_out = isY ? kPosX : 8'bz;  // Controlled_Buffer controlled_buffer_14
  assign controlled_buffer_15_out = not_9_out ? PlayerY : 8'bz;  // Controlled_Buffer controlled_buffer_15
  not not_9 (not_9_out, isY);
  assign controlled_buffer_15_out = isY ? PlayerX : 8'bz;  // Controlled_Buffer controlled_buffer_16
  assign controlled_buffer_17_out = not_10_out ? Dx : 8'bz;  // Controlled_Buffer controlled_buffer_17
  not not_10 (not_10_out, isY);
  assign controlled_buffer_17_out = isY ? Dy : 8'bz;  // Controlled_Buffer controlled_buffer_18
  assign controlled_buffer_19_out = not_11_out ? Dy : 8'bz;  // Controlled_Buffer controlled_buffer_19
  not not_11 (not_11_out, isY);
  assign controlled_buffer_19_out = isY ? Dx : 8'bz;  // Controlled_Buffer controlled_buffer_20
  assign controlled_buffer_21_out = not_12_out ? PlayerY : 8'bz;  // Controlled_Buffer controlled_buffer_21
  not not_12 (not_12_out, isY);
  assign controlled_buffer_21_out = isY ? PlayerX : 8'bz;  // Controlled_Buffer controlled_buffer_22
  or or_1 (or_1_out, comparator_1_eq, and_3_out[1]);
  and and_3 (and_3_out[0], or_1_out, comparator_2_eq);
  Adder adder_2 (.a(PLook0), .b(8'h1), .out(adder_2_out));  // open: cin, cout
  not not_13 (not_13_out, add);
  Subtractor subtractor_2 (.a(PLook0), .b(8'h1), .out(subtractor_2_out));  // open: bin, bout
  Comparator comparator_6 (.a(PLook0), .b(controlled_buffer_11_out), .eq(comparator_6_eq));  // open: gt, lt
  Comparator comparator_7 (
    .a(controlled_buffer_13_out), .b(controlled_buffer_15_out), .eq(comparator_7_eq));  // open: gt, lt
  Comparator comparator_8 (.a(PLook0), .b(controlled_buffer_17_out), .eq(comparator_8_eq));  // open: gt, lt
  Comparator comparator_9 (
    .a(controlled_buffer_19_out), .b(controlled_buffer_21_out), .eq(comparator_9_eq));  // open: gt, lt
  assign PLook1 = add ? adder_2_out : 8'bz;  // Controlled_Buffer controlled_buffer_23
  assign PLook1 = not_13_out ? subtractor_2_out : 8'bz;  // Controlled_Buffer controlled_buffer_24
  Comparator comparator_10 (.a(PLook1), .b(controlled_buffer_11_out), .eq(comparator_10_eq));  // open: gt, lt
  Comparator comparator_11 (.a(PLook1), .b(controlled_buffer_17_out), .eq(comparator_11_eq));  // open: gt, lt
  Multiplexer #(.width(2), .disabled(0), .enable("false")) multiplexer_3 (
    .in0(2'b00), .in1(and_3_out), .out(MONSTER_pos), .sel(DOOR[1]));
  or or_2 (mult[1], MONSTER_pos[1], MONSTER_pos[0]);
  and and_4 (POST_KEY[1], comparator_10_eq, S1[1]);
  and and_5 (DOOR[2], comparator_11_eq, S1[1]);
  assign controlled_buffer_25_out = not_14_out ? Hdx : 8'bz;  // Controlled_Buffer controlled_buffer_25
  not not_14 (not_14_out, isY);
  assign controlled_buffer_25_out = isY ? Hdy : 8'bz;  // Controlled_Buffer controlled_buffer_26
  assign controlled_buffer_27_out = not_15_out ? Hdy : 8'bz;  // Controlled_Buffer controlled_buffer_27
  not not_15 (not_15_out, isY);
  assign controlled_buffer_27_out = isY ? Hdx : 8'bz;  // Controlled_Buffer controlled_buffer_28
  assign controlled_buffer_29_out = not_16_out ? PlayerY : 8'bz;  // Controlled_Buffer controlled_buffer_29
  not not_16 (not_16_out, isY);
  assign controlled_buffer_29_out = isY ? PlayerX : 8'bz;  // Controlled_Buffer controlled_buffer_30
  or or_3 (or_3_out, comparator_6_eq, POST_KEY[1]);
  and and_6 (POST_KEY[0], or_3_out, comparator_7_eq);
  or or_4 (or_4_out, comparator_8_eq, DOOR[2]);
  and and_7 (DOOR[0], or_4_out, comparator_9_eq);
  Comparator comparator_12 (
    .a(controlled_buffer_27_out), .b(controlled_buffer_29_out), .eq(comparator_12_eq));  // open: gt, lt
  not not_17 (POST_KEY[2], DOOR[1]);
  Comparator comparator_13 (.a(PLook0), .b(controlled_buffer_25_out), .eq(comparator_13_eq));  // open: gt, lt
  and and_8 (Hdoor, comparator_13_eq, comparator_12_eq);
  not not_18 (not_18_out, DOOR[1]);
  not not_19 (not_19_out, hide);
  and and_9 (and_9_out, UsePressed, not_18_out, POST_KEY[0]);
  and and_10 (reset, UsePressed, DOOR[0], DOOR[1]);
  Register #(.width(1)) register_7 (.D(and_11_out), .Q(hide), .clk(and_11_out), .clr(reset));  // open: en
  and and_11 (and_11_out, not_19_out, UsePressed, Hdoor);
  Counter #(.width(1), .max('h1)) counter_2 (.Q(DOOR[1]), .clk(and_9_out), .clr(reset));  // open: load, D, count, carry
  Counter counter_3 (.Q({counter_3_q, level}), .clk(reset));  // open: load, D, count, carry, clr
  Counter counter_4 (.Q(counter_4_q), .clk(and_11_out));  // open: load, D, count, carry, clr
  Comparator #(.mode("unsigned")) comparator_14 (
    .a({counter_3_q, level}), .b(multiplexer_4_out), .eq(mult[3]));  // open: gt, lt
  Comparator #(.mode("unsigned")) comparator_15 (
    .a(counter_4_q), .b(multiplexer_4_out), .eq(happy_end));  // open: gt, lt
  Multiplexer #(.select(2), .width(8), .disabled(0), .enable("false")) multiplexer_4 (
    .in0(8'h1), .in1(8'h3), .in2(8'h5), .in3(8'h7), .out(multiplexer_4_out), .sel(difficulty));
  and and_12 (mult[4], mult[3], happy_end);

  assign mult[0] = DOOR[1];

  // Other names for the same wires on the sheet: data_in[7:0] = DATA_INPUT; IsDoor = DOOR[0]; h_door = Hdoor;
  //   Kx[7:0] = kPosX; Ky[7:0] = kPosY; HaveKey = DOOR[1]; lookAtMonster = mult[1]; DeathByMonster = mult[2];
  //   hungry_end = mult[3]; Mx[7:0] = MposX; My[7:0] = MposY; inFrontOfKey = POST_KEY[0]; Px[7:0] = PlayerX;
  //   Py[7:0] = PlayerY; canSee = S1[1]; use = UsePressed

  // Notes on the sheet:
  //   I/O interface
  //   address:010
  //   dPosX
  //   dPosY
  //   HdPosX
  //   HdPosY
  //   kPosX
  //   kPosY
  //   have_key
  //   look at monster
  //   Death_by_Monster
  //   hungry_death
  //   win
endmodule

module isAnyWire (
  input  [7:0] \input ,
  output \output 
);

  Pull_Resistor pull_resistor_1 (.node(\input [0]));
  Pull_Resistor pull_resistor_2 (.node(\input [1]));
  Pull_Resistor pull_resistor_3 ();  // open: node
  Pull_Resistor pull_resistor_4 ();  // open: node
  Pull_Resistor pull_resistor_5 (.node(\input [2]));
  Pull_Resistor pull_resistor_6 ();  // open: node
  Pull_Resistor pull_resistor_7 (.node(\input [3]));
  Pull_Resistor pull_resistor_8 (.node(\input [4]));
  Pull_Resistor pull_resistor_9 ();  // open: node
  Pull_Resistor pull_resistor_10 ();  // open: node
  Pull_Resistor pull_resistor_11 (.node(\input [5]));
  Pull_Resistor pull_resistor_12 ();  // open: node
  Pull_Resistor pull_resistor_13 (.node(\input [7]));
  Pull_Resistor pull_resistor_14 ();  // open: node
  Pull_Resistor pull_resistor_15 (.node(\input [7]));
  Pull_Resistor pull_resistor_16 ();  // open: node
  or or_1 (\output , \input [0], \input [1], \input [2], \input [3], \input [4], \input [5], \input [7], \input [7]);

  assign \input [6] = \input [7];
endmodule

module Take_3_by_Y_LR (
  input  [7:0] x0,
  input  [7:0] x1,
  input  [7:0] x2,
  input  [7:0] x3,
  input  [7:0] x4,
  input  [7:0] x5,
  input  [7:0] x6,
  input  [7:0] x7,
  input  [7:0] posY,
  output [7:0] out0,
  output [7:0] out1,
  output [7:0] out2
);

  wire adder_1_cout, not_1_out, not_2_out, subtractor_1_bout;
  wire [2:0] adder_1_out, subtractor_1_out;
  wire [7:0] multiplexer_1_out, multiplexer_3_out;

  Adder #(.width(3)) adder_1 (.a(posY[2:0]), .b(3'b001), .out(adder_1_out), .cout(adder_1_cout));  // open: cin
  Subtractor #(.width(3)) subtractor_1 (
    .a(posY[2:0]), .b(3'b001), .out(subtractor_1_out), .bout(subtractor_1_bout));  // open: bin
  Multiplexer #(.select(3), .width(8)) multiplexer_1 (
    .in0(x0), .in1(x1), .in2(x2), .in3(x3), .in4(x4), .in5(x5), .in6(x6), .in7(x7), .out(multiplexer_1_out),
    .sel(adder_1_out));  // open: en
  Multiplexer #(.select(3), .width(8)) multiplexer_2 (
    .in0(x0), .in1(x1), .in2(x2), .in3(x3), .in4(x4), .in5(x5), .in6(x6), .in7(x7), .out(out1),
    .sel(posY[2:0]));  // open: en
  Multiplexer #(.select(3), .width(8)) multiplexer_3 (
    .in0(x0), .in1(x1), .in2(x2), .in3(x3), .in4(x4), .in5(x5), .in6(x6), .in7(x7), .out(multiplexer_3_out),
    .sel(subtractor_1_out));  // open: en
  assign out2 = not_1_out ? multiplexer_1_out : 8'bz;  // Controlled_Buffer controlled_buffer_1
  not not_1 (not_1_out, adder_1_cout);
  assign out2 = adder_1_cout ? {8{1'b0}} : 8'bz;  // Controlled_Buffer controlled_buffer_2
  assign out0 = not_2_out ? multiplexer_3_out : 8'bz;  // Controlled_Buffer controlled_buffer_3
  assign out0 = subtractor_1_bout ? {8{1'b0}} : 8'bz;  // Controlled_Buffer controlled_buffer_4
  not not_2 (not_2_out, subtractor_1_bout);
endmodule

module Take_3_by_X_LR (
  input  [7:0] in0,
  input  [7:0] in1,
  input  [7:0] in2,
  input  [7:0] posX,
  input  LR,
  output [2:0] out0,
  output [2:0] out1,
  output [2:0] out2,
  output [2:0] out3
);

  wire not_1_out;
  wire [2:0] subtractor_1_out;
  wire [3:0] multiplexer_1_out, multiplexer_2_out, multiplexer_3_out, multiplexer_4_out, multiplexer_5_out,
       multiplexer_6_out, multiplexer_7_out, multiplexer_8_out, multiplexer_9_out;

  not not_1 (not_1_out, LR);
  Subtractor #(.width(3)) subtractor_1 (.a(3'b111), .b(posX[2:0]), .out(subtractor_1_out));  // open: bin, bout
  Multiplexer #(.select(3), .width(4), .enable("false")) multiplexer_1 (
    .in0({in0[0], 3'b000}), .in1({in0[1:0], 2'b00}), .in2({in0[2:0], 1'b0}), .in3(in0[3:0]), .in4(in0[4:1]),
    .in5(in0[5:2]), .in6(in0[6:3]), .in7(in0[7:4]), .out(multiplexer_1_out), .sel(subtractor_1_out));
  Multiplexer #(.select(3), .width(4), .enable("false")) multiplexer_2 (
    .in0(in0[3:0]), .in1(in0[4:1]), .in2(in0[5:2]), .in3(in0[6:3]), .in4(in0[7:4]), .in5({1'b0, in0[7:5]}),
    .in6({2'b00, in0[7:6]}), .in7({3'b000, in0[7]}), .out(multiplexer_2_out), .sel(subtractor_1_out));
  Multiplexer #(.select(3), .width(4), .enable("false")) multiplexer_3 (
    .in0({in1[0], 3'b000}), .in1({in1[1:0], 2'b00}), .in2({in1[2:0], 1'b0}), .in3(in1[3:0]), .in4(in1[4:1]),
    .in5(in1[5:2]), .in6(in1[6:3]), .in7(in1[7:4]), .out(multiplexer_3_out), .sel(subtractor_1_out));
  Multiplexer #(.select(3), .width(4), .enable("false")) multiplexer_4 (
    .in0(in1[3:0]), .in1(in1[4:1]), .in2(in1[5:2]), .in3(in1[6:3]), .in4(in1[7:4]), .in5({1'b0, in1[7:5]}),
    .in6({2'b00, in1[7:6]}), .in7({3'b000, in1[7]}), .out(multiplexer_4_out), .sel(subtractor_1_out));
  Multiplexer #(.select(3), .width(4), .enable("false")) multiplexer_5 (
    .in0({in2[0], 3'b000}), .in1({in2[1:0], 2'b00}), .in2({in2[2:0], 1'b0}), .in3(in2[3:0]), .in4(in2[4:1]),
    .in5(in2[5:2]), .in6(in2[6:3]), .in7(in2[7:4]), .out(multiplexer_5_out), .sel(subtractor_1_out));
  Multiplexer #(.select(3), .width(4), .enable("false")) multiplexer_6 (
    .in0(in2[3:0]), .in1(in2[4:1]), .in2(in2[5:2]), .in3(in2[6:3]), .in4(in2[7:4]), .in5({1'b0, in2[7:5]}),
    .in6({2'b00, in2[7:6]}), .in7({3'b000, in2[7]}), .out(multiplexer_6_out), .sel(subtractor_1_out));
  Multiplexer #(.width(4), .enable("false")) multiplexer_7 (
    .in0(multiplexer_1_out), .in1(multiplexer_2_out), .out(multiplexer_7_out), .sel(not_1_out));
  Multiplexer #(.width(4), .enable("false")) multiplexer_8 (
    .in0(multiplexer_3_out), .in1(multiplexer_4_out), .out(multiplexer_8_out), .sel(not_1_out));
  Multiplexer #(.width(4), .enable("false")) multiplexer_9 (
    .in0(multiplexer_5_out), .in1(multiplexer_6_out), .out(multiplexer_9_out), .sel(not_1_out));
  Multiplexer #(.width(3), .enable("false")) multiplexer_10 (
    .in0({multiplexer_7_out[0], multiplexer_8_out[0], multiplexer_9_out[0]}),
    .in1({multiplexer_9_out[3], multiplexer_8_out[3], multiplexer_7_out[3]}), .out(out0), .sel(not_1_out));
  Multiplexer #(.width(3), .enable("false")) multiplexer_11 (
    .in0({multiplexer_7_out[1], multiplexer_8_out[1], multiplexer_9_out[1]}),
    .in1({multiplexer_9_out[2], multiplexer_8_out[2], multiplexer_7_out[2]}), .out(out1), .sel(not_1_out));
  Multiplexer #(.width(3), .enable("false")) multiplexer_12 (
    .in0({multiplexer_7_out[2], multiplexer_8_out[2], multiplexer_9_out[2]}),
    .in1({multiplexer_9_out[1], multiplexer_8_out[1], multiplexer_7_out[1]}), .out(out2), .sel(not_1_out));
  Multiplexer #(.width(3), .enable("false")) multiplexer_13 (
    .in0({multiplexer_7_out[3], multiplexer_8_out[3], multiplexer_9_out[3]}),
    .in1({multiplexer_9_out[0], multiplexer_8_out[0], multiplexer_7_out[0]}), .out(out3), .sel(not_1_out));

  // Notes on the sheet:
  //   0 = right
  //   1 = left
endmodule

module Take_3_by_Y_UD (
  input  [7:0] x0,
  input  [7:0] x1,
  input  [7:0] x2,
  input  [7:0] x3,
  input  [7:0] x4,
  input  [7:0] x5,
  input  [7:0] x6,
  input  [7:0] x7,
  input  [7:0] posY,
  input  DU,
  output [7:0] out0,
  output [7:0] out1,
  output [7:0] out2,
  output [7:0] out3
);

  wire adder_1_cout, adder_2_cout, adder_3_cout, not1, not2, not3, not_1_out, not_2_out, not_3_out,
       subtractor_1_bout, subtractor_2_bout, subtractor_3_bout;
  wire [2:0] _1, _2, _3, adder_1_out, adder_2_out, adder_3_out, subtractor_1_out, subtractor_2_out,
       subtractor_3_out;
  wire [7:0] multiplexer_7_out, multiplexer_8_out, multiplexer_9_out;

  Adder #(.width(3)) adder_1 (.a(posY[2:0]), .b(3'b011), .out(adder_1_out), .cout(adder_1_cout));  // open: cin
  Adder #(.width(3)) adder_2 (.a(posY[2:0]), .b(3'b010), .out(adder_2_out), .cout(adder_2_cout));  // open: cin
  Adder #(.width(3)) adder_3 (.a(posY[2:0]), .b(3'b001), .out(adder_3_out), .cout(adder_3_cout));  // open: cin
  Multiplexer #(.width(3), .enable("false")) multiplexer_1 (
    .in0(adder_3_out), .in1(subtractor_1_out), .out(_1), .sel(DU));
  Subtractor #(.width(3)) subtractor_1 (
    .a(posY[2:0]), .b(3'b001), .out(subtractor_1_out), .bout(subtractor_1_bout));  // open: bin
  Subtractor #(.width(3)) subtractor_2 (
    .a(posY[2:0]), .b(3'b010), .out(subtractor_2_out), .bout(subtractor_2_bout));  // open: bin
  Subtractor #(.width(3)) subtractor_3 (
    .a(posY[2:0]), .b(3'b011), .out(subtractor_3_out), .bout(subtractor_3_bout));  // open: bin
  Multiplexer #(.width(3), .enable("false")) multiplexer_2 (
    .in0(adder_2_out), .in1(subtractor_2_out), .out(_2), .sel(DU));
  Multiplexer #(.width(3), .enable("false")) multiplexer_3 (
    .in0(adder_1_out), .in1(subtractor_3_out), .out(_3), .sel(DU));
  Multiplexer #(.enable("false")) multiplexer_4 (.in0(adder_2_cout), .in1(subtractor_2_bout), .out(not2), .sel(DU));
  Multiplexer #(.enable("false")) multiplexer_5 (.in0(adder_3_cout), .in1(subtractor_1_bout), .out(not1), .sel(DU));
  Multiplexer #(.enable("false")) multiplexer_6 (.in0(adder_1_cout), .in1(subtractor_3_bout), .out(not3), .sel(DU));
  Multiplexer #(.select(3), .width(8)) multiplexer_7 (
    .in0(x0), .in1(x1), .in2(x2), .in3(x3), .in4(x4), .in5(x5), .in6(x6), .in7(x7), .out(multiplexer_7_out),
    .sel(_3));  // open: en
  Multiplexer #(.select(3), .width(8)) multiplexer_8 (
    .in0(x0), .in1(x1), .in2(x2), .in3(x3), .in4(x4), .in5(x5), .in6(x6), .in7(x7), .out(multiplexer_8_out),
    .sel(_2));  // open: en
  Multiplexer #(.select(3), .width(8)) multiplexer_9 (
    .in0(x0), .in1(x1), .in2(x2), .in3(x3), .in4(x4), .in5(x5), .in6(x6), .in7(x7), .out(multiplexer_9_out),
    .sel(_1));  // open: en
  Multiplexer #(.select(3), .width(8)) multiplexer_10 (
    .in0(x0), .in1(x1), .in2(x2), .in3(x3), .in4(x4), .in5(x5), .in6(x6), .in7(x7), .out(out3),
    .sel(posY[2:0]));  // open: en
  assign out1 = not2 ? {8{1'b0}} : 8'bz;  // Controlled_Buffer controlled_buffer_1
  assign out1 = not_1_out ? multiplexer_8_out : 8'bz;  // Controlled_Buffer controlled_buffer_2
  not not_1 (not_1_out, not2);
  assign out2 = not_2_out ? multiplexer_9_out : 8'bz;  // Controlled_Buffer controlled_buffer_3
  not not_2 (not_2_out, not1);
  assign out0 = not_3_out ? multiplexer_7_out : 8'bz;  // Controlled_Buffer controlled_buffer_4
  not not_3 (not_3_out, not3);
  assign out0 = not3 ? {8{1'b0}} : 8'bz;  // Controlled_Buffer controlled_buffer_5
  assign out2 = not1 ? {8{1'b0}} : 8'bz;  // Controlled_Buffer controlled_buffer_6

  // Other names for the same wires on the sheet: _0[2:0] = posY[2:0]; UD = DU
endmodule

module Take_3_by_X_UD (
  input  [7:0] in0,
  input  [7:0] in1,
  input  [7:0] in2,
  input  [7:0] in3,
  input  [7:0] posX,
  input  DU,
  output [2:0] out0,
  output [2:0] out1,
  output [2:0] out2,
  output [2:0] out3
);

  wire [2:0] multiplexer_1_out, multiplexer_2_out, multiplexer_3_out, multiplexer_4_out, subtractor_1_out;

  Subtractor #(.width(3)) subtractor_1 (.a(3'b111), .b(posX[2:0]), .out(subtractor_1_out));  // open: bin, bout
  Multiplexer #(.select(3), .width(3), .enable("false")) multiplexer_1 (
    .in0({in0[1:0], 1'b0}), .in1(in0[2:0]), .in2(in0[3:1]), .in3(in0[4:2]), .in4(in0[5:3]), .in5(in0[6:4]),
    .in6(in0[7:5]), .in7({1'b0, in0[7:6]}), .out(multiplexer_1_out), .sel(subtractor_1_out));
  Multiplexer #(.select(3), .width(3), .enable("false")) multiplexer_2 (
    .in0({in1[1:0], 1'b0}), .in1(in1[2:0]), .in2(in1[3:1]), .in3(in1[4:2]), .in4(in1[5:3]), .in5(in1[6:4]),
    .in6(in1[7:5]), .in7({1'b0, in1[7:6]}), .out(multiplexer_2_out), .sel(subtractor_1_out));
  Multiplexer #(.select(3), .width(3), .enable("false")) multiplexer_3 (
    .in0({in2[1:0], 1'b0}), .in1(in2[2:0]), .in2(in2[3:1]), .in3(in2[4:2]), .in4(in2[5:3]), .in5(in2[6:4]),
    .in6(in2[7:5]), .in7({1'b0, in2[7:6]}), .out(multiplexer_3_out), .sel(subtractor_1_out));
  Multiplexer #(.select(3), .width(3), .enable("false")) multiplexer_4 (
    .in0({in3[1:0], 1'b0}), .in1(in3[2:0]), .in2(in3[3:1]), .in3(in3[4:2]), .in4(in3[5:3]), .in5(in3[6:4]),
    .in6(in3[7:5]), .in7({1'b0, in3[7:6]}), .out(multiplexer_4_out), .sel(subtractor_1_out));
  inverse inverse_1 (.\input (multiplexer_1_out), .DU(DU), .\output (out0));
  inverse inverse_2 (.\input (multiplexer_2_out), .DU(DU), .\output (out1));
  inverse inverse_3 (.\input (multiplexer_3_out), .DU(DU), .\output (out2));
  inverse inverse_4 (.\input (multiplexer_4_out), .DU(DU), .\output (out3));
endmodule

module MyAddress2pin (
  input  [1:0] address,
  input  [1:0] data,
  input  allow,
  output change
);

  wire comparator_1_eq;

  assign change = allow ? comparator_1_eq : 1'bz;  // Controlled_Buffer controlled_buffer_1
  Comparator #(.width(2), .mode("unsigned")) comparator_1 (
    .a(address), .b(data), .eq(comparator_1_eq));  // open: gt, lt
endmodule

module MyAddress3pin (
  input  [2:0] address,
  input  [2:0] data,
  input  allow,
  output change
);

  wire comparator_1_eq;

  Comparator #(.width(3), .mode("unsigned")) comparator_1 (
    .a(address), .b(data), .eq(comparator_1_eq));  // open: gt, lt
  assign change = allow ? comparator_1_eq : 1'bz;  // Controlled_Buffer controlled_buffer_1
endmodule

module inverse (
  input  [2:0] \input ,
  input  DU,
  output [2:0] \output 
);

  Multiplexer #(.width(3), .disabled(0), .enable("false")) multiplexer_1 (
    .in0({\input [0], \input [1], \input [2]}), .in1(\input ), .out(\output ), .sel(DU));
endmodule

module simplestTrigger (
  input  x,
  input  y,
  input  res,
  output out
);

  wire and_1_out;

  and and_1 (and_1_out, x, y);
  J_K_Flip_Flop j_k_ff_1 (.Q(out), .preset(and_1_out), .reset(res));  // open: J, clk, K, Qn, en
endmodule
