// Logisim project Vovan_cosmo-gopnik.circ as structural Verilog
module main (
  input  [6:0] in_1
);

  wire main_1_key_tact, main_1_secret, main_1_use;
  wire [1:0] main_1_compas, main_1_monster_pos;
  wire [2:0] main_1_door, main_1_post_key, main_1_s0, main_1_s1, main_1_s2, main_1_s3;
  wire [4:0] main_1_mult;
  wire [6:0] compas_1_out_2, compas_1_out_3, compas_1_out_4, compas_1_out_5, compas_1_out_6, compas_1_out_7,
       compas_1_out_8, keyboard_1_data;
  wire [15:0] video_sprites_1_out_9, video_sprites_1_out_10, video_sprites_1_out_11, video_sprites_1_out_12,
       video_sprites_1_out_13, video_sprites_1_out_14, video_sprites_1_out_15, video_sprites_1_out_16,
       video_sprites_1_out_17, video_sprites_1_out_18, video_sprites_1_out_19, video_sprites_1_out_20,
       video_sprites_1_out_21, video_sprites_1_out_22, video_sprites_1_out_23, video_sprites_1_out_24,
       video_sprites_1_out_25, video_sprites_1_out_26, video_sprites_1_out_27, video_sprites_1_out_28,
       video_sprites_1_out_29, video_sprites_1_out_30, video_sprites_1_out_31, video_sprites_1_out_32;
  wire [31:0] main_2_out_4, main_2_out_5, main_2_out_6, main_2_out_7, main_2_out_8, main_2_out_9,
       main_2_out_10, main_2_out_11, main_2_out_12, main_2_out_13, main_2_out_14, main_2_out_15,
       main_2_out_16, main_2_out_17, main_2_out_18, main_2_out_19, main_2_out_20, main_2_out_21,
       main_2_out_22, main_2_out_23, main_2_out_24, main_2_out_25, main_2_out_26, main_2_out_27,
       main_2_out_28, main_2_out_29, main_2_out_30, main_2_out_31, main_2_out_32, main_2_out_33,
       main_2_out_34, main_2_out_35;

  name name_1 ();
  DotMatrix #(.inputtype("row"), .matrixcols(16), .matrixrows(12)) dotmatrix_1 (
    .row0(video_sprites_1_out_28), .row1(video_sprites_1_out_26), .row2(video_sprites_1_out_24),
    .row3(video_sprites_1_out_22), .row4(video_sprites_1_out_20), .row5(video_sprites_1_out_18),
    .row6(video_sprites_1_out_16), .row7(video_sprites_1_out_14), .row8(video_sprites_1_out_12),
    .row9(video_sprites_1_out_11), .row10(video_sprites_1_out_10), .row11(video_sprites_1_out_9));
  DotMatrix #(.inputtype("row"), .matrixcols(16), .matrixrows(12)) dotmatrix_2 (
    .row0(video_sprites_1_out_9), .row1(video_sprites_1_out_10), .row2(video_sprites_1_out_11),
    .row3(video_sprites_1_out_12), .row4(video_sprites_1_out_14), .row5(video_sprites_1_out_16),
    .row6(video_sprites_1_out_18), .row7(video_sprites_1_out_20), .row8(video_sprites_1_out_22),
    .row9(video_sprites_1_out_24), .row10(video_sprites_1_out_26), .row11(video_sprites_1_out_28));
  Video_Sprites video_sprites_1 (
    .in_1(main_1_s3), .in_2(main_1_s2), .in_3(main_1_s1), .in_4(main_1_s0), .out_9(video_sprites_1_out_9),
    .out_10(video_sprites_1_out_10), .out_11(video_sprites_1_out_11), .out_12(video_sprites_1_out_12),
    .out_13(video_sprites_1_out_13), .out_14(video_sprites_1_out_14), .out_15(video_sprites_1_out_15),
    .out_16(video_sprites_1_out_16), .out_17(video_sprites_1_out_17), .out_18(video_sprites_1_out_18),
    .out_19(video_sprites_1_out_19), .out_20(video_sprites_1_out_20), .out_21(video_sprites_1_out_21),
    .out_22(video_sprites_1_out_22), .out_23(video_sprites_1_out_23), .out_24(video_sprites_1_out_24),
    .out_25(video_sprites_1_out_25), .out_26(video_sprites_1_out_26), .out_27(video_sprites_1_out_27),
    .out_28(video_sprites_1_out_28), .out_29(video_sprites_1_out_29), .out_30(video_sprites_1_out_30),
    .out_31(video_sprites_1_out_31), .out_32(video_sprites_1_out_32), .MONSTER(main_1_monster_pos),
    .POST(main_1_post_key), .DOOR(main_1_door), .HIDDEN_DOOR(main_1_secret));
  MYPart_main main_1 (
    .KeyBoard(keyboard_1_data), .mult(main_1_mult), .MONSTER_pos(main_1_monster_pos),
    .Key_tact(main_1_key_tact), .POST_KEY(main_1_post_key), .DOOR(main_1_door), .SECRET(main_1_secret),
    .compas(main_1_compas), .S3(main_1_s3), .S2(main_1_s2), .S1(main_1_s1), .S0(main_1_s0), .USE(main_1_use));
  Keyboard #(.buflen(1)) keyboard_1 (.clk(main_1_key_tact), .data(keyboard_1_data));  // open: re, clr, avail
  DotMatrix #(.inputtype("row"), .matrixcols(16), .matrixrows(12)) dotmatrix_3 (
    .row0(video_sprites_1_out_32), .row1(video_sprites_1_out_31), .row2(video_sprites_1_out_30),
    .row3(video_sprites_1_out_29), .row4(video_sprites_1_out_27), .row5(video_sprites_1_out_25),
    .row6(video_sprites_1_out_23), .row7(video_sprites_1_out_21), .row8(video_sprites_1_out_19),
    .row9(video_sprites_1_out_17), .row10(video_sprites_1_out_15), .row11(video_sprites_1_out_13));
  DotMatrix #(.inputtype("row"), .matrixcols(16), .matrixrows(12)) dotmatrix_4 (
    .row0(video_sprites_1_out_13), .row1(video_sprites_1_out_15), .row2(video_sprites_1_out_17),
    .row3(video_sprites_1_out_19), .row4(video_sprites_1_out_21), .row5(video_sprites_1_out_23),
    .row6(video_sprites_1_out_25), .row7(video_sprites_1_out_27), .row8(video_sprites_1_out_29),
    .row9(video_sprites_1_out_30), .row10(video_sprites_1_out_31), .row11(video_sprites_1_out_32));
  DotMatrix #(.matrixcols(7)) dotmatrix_5 (
    .col0(compas_1_out_8), .col1(compas_1_out_7), .col2(compas_1_out_6), .col3(compas_1_out_5),
    .col4(compas_1_out_4), .col5(compas_1_out_3), .col6(compas_1_out_2));
  compas compas_1 (
    .in_1(main_1_compas), .out_8(compas_1_out_8), .out_7(compas_1_out_7), .out_6(compas_1_out_6),
    .out_5(compas_1_out_5), .out_4(compas_1_out_4), .out_3(compas_1_out_3), .out_2(compas_1_out_2));
  DotMatrix #(.inputtype("row"), .matrixcols(32), .matrixrows(32)) dotmatrix_6 (
    .row0(main_2_out_4), .row1(main_2_out_8), .row2(main_2_out_12), .row3(main_2_out_16),
    .row4(main_2_out_20), .row5(main_2_out_24), .row6(main_2_out_28), .row7(main_2_out_32),
    .row8(main_2_out_5), .row9(main_2_out_9), .row10(main_2_out_13), .row11(main_2_out_17),
    .row12(main_2_out_21), .row13(main_2_out_25), .row14(main_2_out_29), .row15(main_2_out_33),
    .row16(main_2_out_6), .row17(main_2_out_10), .row18(main_2_out_14), .row19(main_2_out_18),
    .row20(main_2_out_22), .row21(main_2_out_26), .row22(main_2_out_30), .row23(main_2_out_34),
    .row24(main_2_out_7), .row25(main_2_out_11), .row26(main_2_out_15), .row27(main_2_out_19),
    .row28(main_2_out_23), .row29(main_2_out_27), .row30(main_2_out_31), .row31(main_2_out_35));
  death_mult_main main_2 (
    .out_4(main_2_out_4), .out_8(main_2_out_8), .out_12(main_2_out_12), .out_16(main_2_out_16),
    .out_20(main_2_out_20), .out_24(main_2_out_24), .out_28(main_2_out_28), .out_32(main_2_out_32),
    .out_5(main_2_out_5), .out_9(main_2_out_9), .out_13(main_2_out_13), .out_17(main_2_out_17),
    .out_21(main_2_out_21), .out_25(main_2_out_25), .out_29(main_2_out_29), .out_33(main_2_out_33),
    .out_6(main_2_out_6), .out_10(main_2_out_10), .out_14(main_2_out_14), .out_18(main_2_out_18),
    .out_22(main_2_out_22), .out_26(main_2_out_26), .out_30(main_2_out_30), .out_34(main_2_out_34),
    .out_7(main_2_out_7), .out_11(main_2_out_11), .out_15(main_2_out_15), .out_19(main_2_out_19),
    .out_23(main_2_out_23), .out_27(main_2_out_27), .out_31(main_2_out_31), .out_35(main_2_out_35),
    .VOLUME(in_1), .USE(main_1_use), .mult(main_1_mult));
endmodule

module Video_Sprites (
  input  [2:0] in_1,
  input  [2:0] in_2,
  input  [2:0] in_3,
  input  [2:0] in_4,
  input  [2:0] DOOR,
  input  [2:0] POST,
  input  [1:0] MONSTER,
  input  HIDDEN_DOOR,
  output [15:0] out_9,
  output [15:0] out_10,
  output [15:0] out_11,
  output [15:0] out_12,
  output [15:0] out_13,
  output [15:0] out_14,
  output [15:0] out_15,
  output [15:0] out_16,
  output [15:0] out_17,
  output [15:0] out_18,
  output [15:0] out_19,
  output [15:0] out_20,
  output [15:0] out_21,
  output [15:0] out_22,
  output [15:0] out_23,
  output [15:0] out_24,
  output [15:0] out_25,
  output [15:0] out_26,
  output [15:0] out_27,
  output [15:0] out_28,
  output [15:0] out_29,
  output [15:0] out_30,
  output [15:0] out_31,
  output [15:0] out_32
);

  wire [15:0] door_1_out_28, door_1_out_29, door_1_out_30, door_1_out_31, door_1_out_32, door_1_out_33,
       door_1_out_34, door_1_out_35, door_1_out_36, door_1_out_37, door_1_out_38, door_1_out_39,
       door_1_out_40, door_1_out_41, door_1_out_42, door_1_out_43, door_1_out_44, door_1_out_45,
       door_1_out_46, door_1_out_47, door_1_out_48, door_1_out_49, door_1_out_50, door_1_out_51,
       monster_1_out_43, or_1_out, post_1_out_28, post_1_out_29, post_1_out_30, post_1_out_31, post_1_out_32,
       post_1_out_33, post_1_out_34, post_1_out_35, post_1_out_36, post_1_out_37, post_1_out_38,
       post_1_out_39, post_1_out_40, post_1_out_41, post_1_out_42, post_1_out_43, post_1_out_44,
       post_1_out_45, post_1_out_46, post_1_out_47, post_1_out_48, post_1_out_49, post_1_out_50,
       post_1_out_51, video_1_out_5, video_1_out_6, video_1_out_7, video_1_out_8, video_1_out_9,
       video_1_out_10, video_1_out_11, video_1_out_12, video_1_out_13, video_1_out_14, video_1_out_15,
       video_1_out_16, video_1_out_17, video_1_out_18, video_1_out_19, video_1_out_20, video_1_out_21,
       video_1_out_22, video_1_out_23, video_1_out_24, video_1_out_25, video_1_out_26, video_1_out_27,
       video_1_out_28;

  Video video_1 (
    .out_6(video_1_out_6), .out_8(video_1_out_8), .out_10(video_1_out_10), .out_12(video_1_out_12),
    .out_14(video_1_out_14), .out_16(video_1_out_16), .out_18(video_1_out_18), .out_20(video_1_out_20),
    .out_22(video_1_out_22), .out_24(video_1_out_24), .out_26(video_1_out_26), .out_28(video_1_out_28),
    .out_5(video_1_out_5), .out_7(video_1_out_7), .out_9(video_1_out_9), .out_11(video_1_out_11),
    .out_13(video_1_out_13), .out_15(video_1_out_15), .out_17(video_1_out_17), .out_19(video_1_out_19),
    .out_21(video_1_out_21), .out_23(video_1_out_23), .out_25(video_1_out_25), .out_27(video_1_out_27),
    .in_1(in_1), .in_2(in_2), .in_3(in_3), .in_4(in_4));
  post post_1 (
    .in_1(door_1_out_28), .out_29(post_1_out_29), .in_3(door_1_out_30), .out_31(post_1_out_31),
    .in_5(door_1_out_32), .out_33(post_1_out_33), .in_7(door_1_out_34), .out_35(post_1_out_35),
    .in_9(door_1_out_36), .out_37(post_1_out_37), .in_11(door_1_out_38), .out_39(post_1_out_39),
    .in_13(door_1_out_40), .out_41(post_1_out_41), .in_15(door_1_out_42), .out_43(post_1_out_43),
    .in_17(door_1_out_44), .out_45(post_1_out_45), .in_19(door_1_out_46), .out_47(post_1_out_47),
    .in_21(door_1_out_48), .out_49(post_1_out_49), .in_23(door_1_out_50), .out_51(post_1_out_51),
    .POST(POST[0]), .FAR(POST[1]), .KEY(POST[2]), .out_28(post_1_out_28), .in_2(door_1_out_29),
    .out_30(post_1_out_30), .in_4(door_1_out_31), .out_32(post_1_out_32), .in_6(door_1_out_33),
    .out_34(post_1_out_34), .in_8(door_1_out_35), .out_36(post_1_out_36), .in_10(door_1_out_37),
    .out_38(post_1_out_38), .in_12(door_1_out_39), .out_40(post_1_out_40), .in_14(door_1_out_41),
    .out_42(post_1_out_42), .in_16(door_1_out_43), .out_44(post_1_out_44), .in_18(door_1_out_45),
    .out_46(post_1_out_46), .in_20(door_1_out_47), .out_48(post_1_out_48), .in_22(door_1_out_49),
    .out_50(post_1_out_50), .in_24(door_1_out_51));
  door door_1 (
    .in_1(video_1_out_5), .out_29(door_1_out_29), .in_3(video_1_out_7), .out_31(door_1_out_31),
    .in_5(video_1_out_9), .out_33(door_1_out_33), .in_7(video_1_out_11), .out_35(door_1_out_35),
    .in_9(video_1_out_13), .out_37(door_1_out_37), .in_11(video_1_out_15), .out_39(door_1_out_39),
    .in_13(video_1_out_17), .out_41(door_1_out_41), .in_15(video_1_out_19), .out_43(door_1_out_43),
    .in_17(video_1_out_21), .out_45(door_1_out_45), .in_19(video_1_out_23), .out_47(door_1_out_47),
    .in_21(video_1_out_25), .out_49(door_1_out_49), .in_23(video_1_out_27), .out_51(door_1_out_51),
    .DOOR(DOOR[0]), .FAR(DOOR[1]), .CLOSED(DOOR[2]), .out_28(door_1_out_28), .in_2(video_1_out_6),
    .out_30(door_1_out_30), .in_4(video_1_out_8), .out_32(door_1_out_32), .in_6(video_1_out_10),
    .out_34(door_1_out_34), .in_8(video_1_out_12), .out_36(door_1_out_36), .in_10(video_1_out_14),
    .out_38(door_1_out_38), .in_12(video_1_out_16), .out_40(door_1_out_40), .in_14(video_1_out_18),
    .out_42(door_1_out_42), .in_16(video_1_out_20), .out_44(door_1_out_44), .in_18(video_1_out_22),
    .out_46(door_1_out_46), .in_20(video_1_out_24), .out_48(door_1_out_48), .in_22(video_1_out_26),
    .out_50(door_1_out_50), .in_24(video_1_out_28));
  monster monster_1 (
    .in_1(post_1_out_28), .out_28(out_13), .in_3(post_1_out_30), .out_30(out_15), .in_5(post_1_out_32),
    .out_32(out_17), .in_7(post_1_out_34), .out_34(out_19), .in_9(post_1_out_36), .out_36(out_21),
    .in_11(post_1_out_38), .out_38(out_23), .in_13(post_1_out_40), .out_40(out_25), .in_15(post_1_out_42),
    .out_42(out_27), .in_17(post_1_out_44), .out_44(out_29), .out_46(out_30), .out_48(out_31),
    .out_27(out_9), .in_2(post_1_out_29), .out_29(out_10), .in_4(post_1_out_31), .out_31(out_11),
    .in_6(post_1_out_33), .out_33(out_12), .in_8(post_1_out_35), .out_35(out_14), .in_10(post_1_out_37),
    .out_37(out_16), .in_12(post_1_out_39), .out_39(out_18), .in_14(post_1_out_41), .out_41(out_20),
    .in_16(post_1_out_43), .out_43(monster_1_out_43), .in_18(post_1_out_45), .in_20(post_1_out_47),
    .in_22(post_1_out_49), .in_19(post_1_out_46), .in_21(post_1_out_48), .in_23(post_1_out_50),
    .out_45(out_24), .out_47(out_26), .out_49(out_28), .in_24(post_1_out_51), .out_50(out_32),
    .MONSTER(MONSTER[0]), .FAR(MONSTER[1]));
  assign or_1_out = monster_1_out_43 | 16'h1000;  // OR_Gate or_1, 16 bits wide
  Multiplexer #(.width(16), .disabled(0), .enable("false")) multiplexer_1 (
    .in0(monster_1_out_43), .in1(or_1_out), .out(out_22), .sel(HIDDEN_DOOR));

  // Notes on the sheet:
  //   DOOR
  //   FAR_DOOR?
  //   CLOSED?
  //   POST!
  //   FAR_POST?
  //   KEY?
  //   MONSTER
  //   FAR_MONSTER
endmodule

module compas (
  input  [1:0] in_1,
  output [6:0] out_2,
  output [6:0] out_3,
  output [6:0] out_4,
  output [6:0] out_5,
  output [6:0] out_6,
  output [6:0] out_7,
  output [6:0] out_8
);

  Multiplexer #(.select(2), .width(7), .disabled(0), .enable("false")) multiplexer_1 (
    .in0({7{1'b0}}), .in1(7'b0001000), .in2({7{1'b0}}), .in3(7'b0001000), .out(out_8), .sel(in_1));
  Multiplexer #(.select(2), .width(7), .disabled(0), .enable("false")) multiplexer_2 (
    .in0(7'b0010000), .in1(7'b0001000), .in2(7'b0000100), .in3(7'b0011100), .out(out_7), .sel(in_1));
  Multiplexer #(.select(2), .width(7), .disabled(0), .enable("false")) multiplexer_3 (
    .in0(7'b0110000), .in1(7'b0001000), .in2(7'b0000110), .in3(7'b0111110), .out(out_6), .sel(in_1));
  Multiplexer #(.select(2), .width(7), .disabled(0), .enable("false")) multiplexer_4 (
    .in0({7{1'b1}}), .in1(7'b0001000), .in2({7{1'b1}}), .in3(7'b0001000), .out(out_5), .sel(in_1));
  Multiplexer #(.select(2), .width(7), .disabled(0), .enable("false")) multiplexer_5 (
    .in0(7'b0110000), .in1(7'b0111110), .in2(7'b0000110), .in3(7'b0001000), .out(out_4), .sel(in_1));
  Multiplexer #(.select(2), .width(7), .disabled(0), .enable("false")) multiplexer_6 (
    .in0(7'b0010000), .in1(7'b0011100), .in2(7'b0000100), .in3(7'b0001000), .out(out_3), .sel(in_1));
  Multiplexer #(.select(2), .width(7), .disabled(0), .enable("false")) multiplexer_7 (
    .in0({7{1'b0}}), .in1(7'b0001000), .in2({7{1'b0}}), .in3(7'b0001000), .out(out_2), .sel(in_1));
endmodule

module monster (
  input  [15:0] in_1,
  input  [15:0] in_2,
  input  [15:0] in_3,
  input  [15:0] in_4,
  input  [15:0] in_5,
  input  [15:0] in_6,
  input  [15:0] in_7,
  input  [15:0] in_8,
  input  [15:0] in_9,
  input  [15:0] in_10,
  input  [15:0] in_11,
  input  [15:0] in_12,
  input  [15:0] in_13,
  input  [15:0] in_14,
  input  [15:0] in_15,
  input  [15:0] in_16,
  input  [15:0] in_17,
  input  [15:0] in_18,
  input  [15:0] in_19,
  input  [15:0] in_20,
  input  [15:0] in_21,
  input  [15:0] in_22,
  input  [15:0] in_23,
  input  [15:0] in_24,
  input  MONSTER,
  input  FAR,
  output [15:0] out_27,
  output [15:0] out_28,
  output [15:0] out_29,
  output [15:0] out_30,
  output [15:0] out_31,
  output [15:0] out_32,
  output [15:0] out_33,
  output [15:0] out_34,
  output [15:0] out_35,
  output [15:0] out_36,
  output [15:0] out_37,
  output [15:0] out_38,
  output [15:0] out_39,
  output [15:0] out_40,
  output [15:0] out_41,
  output [15:0] out_42,
  output [15:0] out_43,
  output [15:0] out_44,
  output [15:0] out_45,
  output [15:0] out_46,
  output [15:0] out_47,
  output [15:0] out_48,
  output [15:0] out_49,
  output [15:0] out_50
);

  error_maker error_maker_1 (
    .Close_Error(16'h2671), .In(in_1), .out_8(out_27), .Far_To_zero(16'he2), .MONSTER(MONSTER), .FAR(FAR),
    .Far_Error(16'h11d), .Close_To_zero(16'h198e));
  error_maker error_maker_2 (
    .Close_Error(16'h2058), .In(in_3), .out_8(out_29), .Far_To_zero(16'ha1), .MONSTER(MONSTER), .FAR(FAR),
    .Far_Error(16'h156), .Close_To_zero(16'h1f87));
  error_maker error_maker_3 (
    .Close_Error(16'h264e), .In(in_5), .out_8(out_31), .Far_To_zero({16{1'b0}}), .MONSTER(MONSTER),
    .FAR(FAR), .Far_Error(16'h1f3), .Close_To_zero(16'h1981));
  error_maker error_maker_4 (
    .Close_Error(16'h2f47), .In(in_7), .out_8(out_33), .Far_To_zero(16'he0), .MONSTER(MONSTER), .FAR(FAR),
    .Far_Error(16'h112), .Close_To_zero(16'h1080));
  error_maker error_maker_5 (
    .Close_Error(16'h2047), .In(in_9), .out_8(out_35), .Far_To_zero({16{1'b0}}), .MONSTER(MONSTER),
    .FAR(FAR), .Far_Error(16'he6), .Close_To_zero(16'h1f80));
  error_maker error_maker_6 (
    .Close_Error(16'h30c2), .In(in_11), .out_8(out_37), .Far_To_zero({16{1'b0}}), .MONSTER(MONSTER),
    .FAR(FAR), .Far_Error({16{1'b0}}), .Close_To_zero(16'hf00));
  error_maker error_maker_7 (
    .Close_Error(16'h1982), .In(in_13), .out_8(out_39), .Far_To_zero({16{1'b0}}), .MONSTER(MONSTER),
    .FAR(FAR), .Far_Error({16{1'b0}}), .Close_To_zero(16'h600));
  error_maker error_maker_8 (
    .Close_Error(16'hf06), .In(in_15), .out_8(out_41), .Far_To_zero({16{1'b0}}), .MONSTER(MONSTER),
    .FAR(FAR), .Far_Error({16{1'b0}}), .Close_To_zero({16{1'b0}}));
  error_maker error_maker_9 (
    .Close_Error(16'he), .In(in_17), .out_8(out_43), .Far_To_zero({16{1'b0}}), .MONSTER(MONSTER), .FAR(FAR),
    .Far_Error({16{1'b0}}), .Close_To_zero({16{1'b0}}));
  error_maker error_maker_10 (
    .Close_Error(16'h8c00), .In(in_2), .out_8(out_28), .Far_To_zero(16'h4000), .MONSTER(MONSTER), .FAR(FAR),
    .Far_Error(16'hb000), .Close_To_zero(16'h7000));
  error_maker error_maker_11 (
    .Close_Error(16'h1800), .In(in_4), .out_8(out_30), .Far_To_zero(16'h8000), .MONSTER(MONSTER), .FAR(FAR),
    .Far_Error(16'h6c00), .Close_To_zero(16'he000));
  error_maker error_maker_12 (
    .Close_Error(16'h7800), .In(in_6), .out_8(out_32), .Far_To_zero({16{1'b0}}), .MONSTER(MONSTER),
    .FAR(FAR), .Far_Error(16'hc600), .Close_To_zero(16'h8000));
  error_maker error_maker_13 (
    .Close_Error(16'hed00), .In(in_8), .out_8(out_34), .Far_To_zero({16{1'b0}}), .MONSTER(MONSTER),
    .FAR(FAR), .Far_Error(16'h4b00), .Close_To_zero({16{1'b0}}));
  error_maker error_maker_14 (
    .Close_Error(16'hef80), .In(in_10), .out_8(out_36), .Far_To_zero({16{1'b0}}), .MONSTER(MONSTER),
    .FAR(FAR), .Far_Error(16'h6100), .Close_To_zero({16{1'b0}}));
  error_maker error_maker_15 (
    .Close_Error(16'h43c0), .In(in_12), .out_8(out_38), .Far_To_zero({16{1'b0}}), .MONSTER(MONSTER),
    .FAR(FAR), .Far_Error({16{1'b0}}), .Close_To_zero({16{1'b0}}));
  error_maker error_maker_16 (
    .Close_Error(16'h4560), .In(in_14), .out_8(out_40), .Far_To_zero({16{1'b0}}), .MONSTER(MONSTER),
    .FAR(FAR), .Far_Error({16{1'b0}}), .Close_To_zero(16'h80));
  error_maker error_maker_17 (
    .Close_Error(16'h60b0), .In(in_16), .out_8(out_42), .Far_To_zero({16{1'b0}}), .MONSTER(MONSTER),
    .FAR(FAR), .Far_Error({16{1'b0}}), .Close_To_zero(16'h40));
  error_maker error_maker_18 (
    .Close_Error(16'h7050), .In(in_18), .out_8(out_44), .Far_To_zero({16{1'b0}}), .MONSTER(MONSTER),
    .FAR(FAR), .Far_Error({16{1'b0}}), .Close_To_zero(16'h20));
  error_maker error_maker_19 (
    .Close_Error(16'h30), .In(in_20), .out_8(out_46), .Far_To_zero({16{1'b0}}), .MONSTER(MONSTER), .FAR(FAR),
    .Far_Error({16{1'b0}}), .Close_To_zero({16{1'b0}}));
  error_maker error_maker_20 (
    .Close_Error(16'h10), .In(in_22), .out_8(out_48), .Far_To_zero({16{1'b0}}), .MONSTER(MONSTER), .FAR(FAR),
    .Far_Error({16{1'b0}}), .Close_To_zero({16{1'b0}}));
  DotMatrix #(.inputtype("row"), .matrixcols(16), .matrixrows(12)) dotmatrix_1 (
    .row0(16'h2671), .row1(16'h2058), .row2(16'h264e), .row3(16'h2f47), .row4(16'h2047), .row5(16'h30c2),
    .row6(16'h1982), .row7(16'hf06), .row8(16'he), .row9({16{1'b0}}), .row10({16{1'b0}}), .row11({16{1'b0}}));
  DotMatrix #(.inputtype("row"), .matrixcols(16), .matrixrows(12)) dotmatrix_2 (
    .row0(16'h8c00), .row1(16'h1800), .row2(16'h7800), .row3(16'hed00), .row4(16'hef80), .row5(16'h43c0),
    .row6(16'h4560), .row7(16'h60b0), .row8(16'h7050), .row9(16'h30), .row10(16'h10), .row11({16{1'b0}}));

  assign out_45 = in_19;
  assign out_47 = in_21;
  assign out_49 = in_23;
  assign out_50 = in_24;

  // Notes on the sheet:
  //   Близко
  //   Далеко
  //   Обнуление
  //   Левая часть
  //   Код ошибки
  //   Код ошибки
  //   Правая часть
  //   Обнуление
endmodule

module error_maker (
  input  [15:0] Close_Error,
  input  [15:0] Far_Error,
  input  FAR,
  input  [15:0] In,
  input  [15:0] Close_To_zero,
  input  MONSTER,
  input  [15:0] Far_To_zero,
  output [15:0] out_8
);

  wire [15:0] multiplexer_1_out, multiplexer_2_out, not_1_out, sub_error_1_out_9, sub_error_3_out_9;

  sub_error sub_error_1 (
    .in_1(Close_Error[0]), .out_9(sub_error_1_out_9[0]), .in_2(Close_Error[1]),
    .out_10(sub_error_1_out_9[1]), .in_3(Close_Error[2]), .out_11(sub_error_1_out_9[2]),
    .in_4(Close_Error[3]), .out_12(sub_error_1_out_9[3]), .in_5(Close_Error[4]),
    .out_13(sub_error_1_out_9[4]), .in_6(Close_Error[5]), .out_14(sub_error_1_out_9[5]),
    .in_7(Close_Error[6]), .out_15(sub_error_1_out_9[6]), .in_8(Close_Error[7]), .out_16(sub_error_1_out_9[7]));
  sub_error sub_error_2 (
    .in_1(Close_Error[8]), .out_9(sub_error_1_out_9[8]), .in_2(Close_Error[9]),
    .out_10(sub_error_1_out_9[9]), .in_3(Close_Error[10]), .out_11(sub_error_1_out_9[10]),
    .in_4(Close_Error[11]), .out_12(sub_error_1_out_9[11]), .in_5(Close_Error[12]),
    .out_13(sub_error_1_out_9[12]), .in_6(Close_Error[13]), .out_14(sub_error_1_out_9[13]),
    .in_7(Close_Error[14]), .out_15(sub_error_1_out_9[14]), .in_8(Close_Error[15]),
    .out_16(sub_error_1_out_9[15]));
  sub_error sub_error_3 (
    .in_1(Far_Error[0]), .out_9(sub_error_3_out_9[0]), .in_2(Far_Error[1]), .out_10(sub_error_3_out_9[1]),
    .in_3(Far_Error[2]), .out_11(sub_error_3_out_9[2]), .in_4(Far_Error[3]), .out_12(sub_error_3_out_9[3]),
    .in_5(Far_Error[4]), .out_13(sub_error_3_out_9[4]), .in_6(Far_Error[5]), .out_14(sub_error_3_out_9[5]),
    .in_7(Far_Error[6]), .out_15(sub_error_3_out_9[6]), .in_8(Far_Error[7]), .out_16(sub_error_3_out_9[7]));
  sub_error sub_error_4 (
    .in_1(Far_Error[8]), .out_9(sub_error_3_out_9[8]), .in_2(Far_Error[9]), .out_10(sub_error_3_out_9[9]),
    .in_3(Far_Error[10]), .out_11(sub_error_3_out_9[10]), .in_4(Far_Error[11]),
    .out_12(sub_error_3_out_9[11]), .in_5(Far_Error[12]), .out_13(sub_error_3_out_9[12]),
    .in_6(Far_Error[13]), .out_14(sub_error_3_out_9[13]), .in_7(Far_Error[14]),
    .out_15(sub_error_3_out_9[14]), .in_8(Far_Error[15]), .out_16(sub_error_3_out_9[15]));
  assign not_1_out = ~multiplexer_1_out;  // NOT_Gate not_1, 16 bits wide
  Multiplexer #(.width(16), .enable("false")) multiplexer_1 (
    .in0(Close_To_zero), .in1(Far_To_zero), .out(multiplexer_1_out), .sel(FAR));
  Multiplexer #(.width(16), .enable("false")) multiplexer_2 (
    .in0(sub_error_1_out_9), .in1(sub_error_3_out_9), .out(multiplexer_2_out), .sel(FAR));
  assign multiplexer_2_out = In & not_1_out;  // AND_Gate and_1, 16 bits wide
  Multiplexer #(.width(16), .enable("false")) multiplexer_3 (
    .in0(In), .in1(multiplexer_2_out), .out(out_8), .sel(MONSTER));
endmodule

module sub_error (
  input  in_1,
  input  in_2,
  input  in_3,
  input  in_4,
  input  in_5,
  input  in_6,
  input  in_7,
  input  in_8,
  output out_9,
  output out_10,
  output out_11,
  output out_12,
  output out_13,
  output out_14,
  output out_15,
  output out_16
);

  Multiplexer #(.enable("false")) multiplexer_1 (.in1(1'b0), .out(out_9), .sel(in_1));  // open: in0
  Multiplexer #(.enable("false")) multiplexer_2 (.in1(1'b0), .out(out_10), .sel(in_2));  // open: in0
  Multiplexer #(.enable("false")) multiplexer_3 (.in1(1'b0), .out(out_11), .sel(in_3));  // open: in0
  Multiplexer #(.enable("false")) multiplexer_4 (.in1(1'b0), .out(out_12), .sel(in_4));  // open: in0
  Multiplexer #(.enable("false")) multiplexer_5 (.in1(1'b0), .out(out_13), .sel(in_5));  // open: in0
  Multiplexer #(.enable("false")) multiplexer_6 (.in1(1'b0), .out(out_14), .sel(in_6));  // open: in0
  Multiplexer #(.enable("false")) multiplexer_7 (.in1(1'b0), .out(out_15), .sel(in_7));  // open: in0
  Multiplexer #(.enable("false")) multiplexer_8 (.in1(1'b0), .out(out_16), .sel(in_8));  // open: in0
endmodule

module post (
  input  [15:0] in_1,
  input  [15:0] in_2,
  input  [15:0] in_3,
  input  [15:0] in_4,
  input  [15:0] in_5,
  input  [15:0] in_6,
  input  [15:0] in_7,
  input  [15:0] in_8,
  input  [15:0] in_9,
  input  [15:0] in_10,
  input  [15:0] in_11,
  input  [15:0] in_12,
  input  [15:0] in_13,
  input  [15:0] in_14,
  input  [15:0] in_15,
  input  [15:0] in_16,
  input  [15:0] in_17,
  input  [15:0] in_18,
  input  [15:0] in_19,
  input  [15:0] in_20,
  input  [15:0] in_21,
  input  [15:0] in_22,
  input  [15:0] in_23,
  input  [15:0] in_24,
  input  POST,
  input  FAR,
  input  KEY,
  output [15:0] out_28,
  output [15:0] out_29,
  output [15:0] out_30,
  output [15:0] out_31,
  output [15:0] out_32,
  output [15:0] out_33,
  output [15:0] out_34,
  output [15:0] out_35,
  output [15:0] out_36,
  output [15:0] out_37,
  output [15:0] out_38,
  output [15:0] out_39,
  output [15:0] out_40,
  output [15:0] out_41,
  output [15:0] out_42,
  output [15:0] out_43,
  output [15:0] out_44,
  output [15:0] out_45,
  output [15:0] out_46,
  output [15:0] out_47,
  output [15:0] out_48,
  output [15:0] out_49,
  output [15:0] out_50,
  output [15:0] out_51
);

  post_maker post_maker_1 (
    .Close_Post({16{1'b0}}), .Far_Post({16{1'b0}}), .FAR(FAR), .In(in_1), .Close_To_zero({16{1'b0}}),
    .POST(POST), .Far_To_zero({16{1'b0}}), .out_10(out_28), .KEY_2(KEY), .Key(16'h1));
  post_maker post_maker_2 (
    .Close_Post(16'h1), .Far_Post(16'h1), .FAR(FAR), .In(in_5), .Close_To_zero({16{1'b0}}), .POST(POST),
    .Far_To_zero({16{1'b0}}), .out_10(out_32), .KEY_2(KEY), .Key({16{1'b0}}));
  post_maker post_maker_3 (
    .Close_Post(16'h2), .Far_Post(16'h2), .FAR(FAR), .In(in_7), .Close_To_zero(16'h1), .POST(POST),
    .Far_To_zero(16'h1), .out_10(out_34), .KEY_2(KEY), .Key({16{1'b0}}));
  post_maker post_maker_4 (
    .Close_Post(16'h4), .Far_Post(16'h4), .FAR(FAR), .In(in_9), .Close_To_zero(16'h3), .POST(POST),
    .Far_To_zero(16'h3), .out_10(out_36), .KEY_2(KEY), .Key({16{1'b0}}));
  post_maker post_maker_5 (
    .Close_Post(16'h8), .Far_Post(16'h3), .FAR(FAR), .In(in_11), .Close_To_zero(16'h7), .POST(POST),
    .Far_To_zero({16{1'b0}}), .out_10(out_38), .KEY_2(KEY), .Key({16{1'b0}}));
  post_maker post_maker_6 (
    .Close_Post(16'h8), .Far_Post({16{1'b0}}), .FAR(FAR), .In(in_13), .Close_To_zero(16'h7), .POST(POST),
    .Far_To_zero({16{1'b0}}), .out_10(out_40), .KEY_2(KEY), .Key({16{1'b0}}));
  post_maker post_maker_7 (
    .Close_Post(16'h8), .Far_Post({16{1'b0}}), .FAR(FAR), .In(in_15), .Close_To_zero(16'h7), .POST(POST),
    .Far_To_zero({16{1'b0}}), .out_10(out_42), .KEY_2(KEY), .Key({16{1'b0}}));
  post_maker post_maker_8 (
    .Close_Post(16'h7), .Far_Post({16{1'b0}}), .FAR(FAR), .In(in_17), .Close_To_zero({16{1'b0}}),
    .POST(POST), .Far_To_zero({16{1'b0}}), .out_10(out_44), .KEY_2(KEY), .Key({16{1'b0}}));
  post_maker post_maker_9 (
    .Close_Post({16{1'b0}}), .Far_Post({16{1'b0}}), .FAR(FAR), .In(in_2), .Close_To_zero({16{1'b0}}),
    .POST(POST), .Far_To_zero({16{1'b0}}), .out_10(out_29), .KEY_2(KEY), .Key(16'h8000));
  post_maker post_maker_10 (
    .Close_Post(16'h8000), .Far_Post(16'h8000), .FAR(FAR), .In(in_6), .Close_To_zero({16{1'b0}}),
    .POST(POST), .Far_To_zero({16{1'b0}}), .out_10(out_33), .KEY_2(KEY), .Key({16{1'b0}}));
  post_maker post_maker_11 (
    .Close_Post(16'h4000), .Far_Post(16'h4000), .FAR(FAR), .In(in_8), .Close_To_zero(16'h8000), .POST(POST),
    .Far_To_zero(16'h8000), .out_10(out_35), .KEY_2(KEY), .Key({16{1'b0}}));
  post_maker post_maker_12 (
    .Close_Post(16'h2000), .Far_Post(16'h2000), .FAR(FAR), .In(in_10), .Close_To_zero({16{1'b0}}),
    .POST(POST), .Far_To_zero(16'hc000), .out_10(out_37), .KEY_2(KEY), .Key({16{1'b0}}));
  post_maker post_maker_13 (
    .Close_Post(16'h1000), .Far_Post(16'hc000), .FAR(FAR), .In(in_12), .Close_To_zero(16'hc000), .POST(POST),
    .Far_To_zero({16{1'b0}}), .out_10(out_39), .KEY_2(KEY), .Key({16{1'b0}}));
  post_maker post_maker_14 (
    .Close_Post(16'h1000), .Far_Post({16{1'b0}}), .FAR(FAR), .In(in_14), .Close_To_zero(16'he000),
    .POST(POST), .Far_To_zero({16{1'b0}}), .out_10(out_41), .KEY_2(KEY), .Key({16{1'b0}}));
  post_maker post_maker_15 (
    .Close_Post(16'h1000), .Far_Post({16{1'b0}}), .FAR(FAR), .In(in_16), .Close_To_zero(16'he000),
    .POST(POST), .Far_To_zero({16{1'b0}}), .out_10(out_43), .KEY_2(KEY), .Key({16{1'b0}}));
  post_maker post_maker_16 (
    .Close_Post(16'he000), .Far_Post({16{1'b0}}), .FAR(FAR), .In(in_18), .Close_To_zero(16'he000),
    .POST(POST), .Far_To_zero({16{1'b0}}), .out_10(out_45), .KEY_2(KEY), .Key({16{1'b0}}));

  assign out_30 = in_3;
  assign out_31 = in_4;
  assign out_46 = in_19;
  assign out_47 = in_20;
  assign out_48 = in_21;
  assign out_49 = in_22;
  assign out_50 = in_23;
  assign out_51 = in_24;

  // Notes on the sheet:
  //   Близко
  //   Далеко
  //   Обнуление
  //   Левая часть
  //   Код ошибки
  //   Код ошибки
  //   Правая часть
  //   Обнуление
endmodule

module post_maker (
  input  [15:0] Close_Post,
  input  [15:0] Far_Post,
  input  FAR,
  input  [15:0] In,
  input  [15:0] Close_To_zero,
  input  POST,
  input  [15:0] Far_To_zero,
  input  [15:0] Key,
  input  KEY_2,
  output [15:0] out_10
);

  wire [15:0] and_1_out, multiplexer_1_out, multiplexer_2_out, multiplexer_3_out, not_1_out, or_1_out;

  Multiplexer #(.width(16), .enable("false")) multiplexer_1 (
    .in0(Close_To_zero), .in1(Far_To_zero), .out(multiplexer_1_out), .sel(FAR));
  assign and_1_out = In & not_1_out;  // AND_Gate and_1, 16 bits wide
  assign not_1_out = ~multiplexer_1_out;  // NOT_Gate not_1, 16 bits wide
  Multiplexer #(.width(16), .enable("false")) multiplexer_2 (
    .in0(Close_Post), .in1(Far_Post), .out(multiplexer_2_out), .sel(FAR));
  Multiplexer #(.width(16), .enable("false")) multiplexer_3 (
    .in0({16{1'b0}}), .in1(Key), .out(multiplexer_3_out), .sel(KEY_2));
  assign or_1_out = and_1_out | multiplexer_3_out | multiplexer_2_out;  // OR_Gate or_1, 16 bits wide
  Multiplexer #(.width(16), .enable("false")) multiplexer_4 (.in0(In), .in1(or_1_out), .out(out_10), .sel(POST));
endmodule

module door (
  input  [15:0] in_1,
  input  [15:0] in_2,
  input  [15:0] in_3,
  input  [15:0] in_4,
  input  [15:0] in_5,
  input  [15:0] in_6,
  input  [15:0] in_7,
  input  [15:0] in_8,
  input  [15:0] in_9,
  input  [15:0] in_10,
  input  [15:0] in_11,
  input  [15:0] in_12,
  input  [15:0] in_13,
  input  [15:0] in_14,
  input  [15:0] in_15,
  input  [15:0] in_16,
  input  [15:0] in_17,
  input  [15:0] in_18,
  input  [15:0] in_19,
  input  [15:0] in_20,
  input  [15:0] in_21,
  input  [15:0] in_22,
  input  [15:0] in_23,
  input  [15:0] in_24,
  input  DOOR,
  input  FAR,
  input  CLOSED,
  output [15:0] out_28,
  output [15:0] out_29,
  output [15:0] out_30,
  output [15:0] out_31,
  output [15:0] out_32,
  output [15:0] out_33,
  output [15:0] out_34,
  output [15:0] out_35,
  output [15:0] out_36,
  output [15:0] out_37,
  output [15:0] out_38,
  output [15:0] out_39,
  output [15:0] out_40,
  output [15:0] out_41,
  output [15:0] out_42,
  output [15:0] out_43,
  output [15:0] out_44,
  output [15:0] out_45,
  output [15:0] out_46,
  output [15:0] out_47,
  output [15:0] out_48,
  output [15:0] out_49,
  output [15:0] out_50,
  output [15:0] out_51
);

  door_maker door_maker_1 (
    .DOOR(DOOR), .FAR(FAR), .In(in_1), .Close_closed(16'h16), .Far_closed(16'h6), .Out(out_28),
    .CLOSED(CLOSED), .Close_open(16'h1f), .Far_open(16'h7));
  door_maker door_maker_2 (
    .DOOR(DOOR), .FAR(FAR), .In(in_3), .Close_closed(16'h10), .Far_closed(16'h4), .Out(out_30),
    .CLOSED(CLOSED), .Close_open(16'h1f), .Far_open(16'h7));
  door_maker door_maker_3 (
    .DOOR(DOOR), .FAR(FAR), .In(in_5), .Close_closed(16'h1f), .Far_closed(16'h7), .Out(out_32),
    .CLOSED(CLOSED), .Close_open(16'h1f), .Far_open(16'h7));
  door_maker door_maker_4 (
    .DOOR(DOOR), .FAR(FAR), .In(in_7), .Close_closed(16'h10), .Far_closed(16'h4), .Out(out_34),
    .CLOSED(CLOSED), .Close_open(16'h1f), .Far_open(16'h7));
  door_maker door_maker_5 (
    .DOOR(DOOR), .FAR(FAR), .In(in_9), .Close_closed(16'h1f), .Far_closed(16'h7), .Out(out_36),
    .CLOSED(CLOSED), .Close_open(16'h1f), .Far_open(16'h7));
  door_maker door_maker_6 (
    .DOOR(DOOR), .FAR(FAR), .In(in_11), .Close_closed(16'h10), .Far_closed({16{1'b0}}), .Out(out_38),
    .CLOSED(CLOSED), .Close_open(16'h1f), .Far_open({16{1'b0}}));
  door_maker door_maker_7 (
    .DOOR(DOOR), .FAR(FAR), .In(in_13), .Close_closed(16'h1f), .Far_closed({16{1'b0}}), .Out(out_40),
    .CLOSED(CLOSED), .Close_open(16'h1f), .Far_open({16{1'b0}}));
  door_maker door_maker_8 (
    .DOOR(DOOR), .FAR(FAR), .In(in_15), .Close_closed(16'h10), .Far_closed({16{1'b0}}), .Out(out_42),
    .CLOSED(CLOSED), .Close_open(16'h1f), .Far_open({16{1'b0}}));
  door_maker door_maker_9 (
    .DOOR(DOOR), .FAR(FAR), .In(in_17), .Close_closed(16'h1f), .Far_closed({16{1'b0}}), .Out(out_44),
    .CLOSED(CLOSED), .Close_open(16'h1f), .Far_open({16{1'b0}}));
  door_maker door_maker_10 (
    .DOOR(DOOR), .FAR(FAR), .In(in_2), .Close_closed(16'h800), .Far_closed(16'h2000), .Out(out_29),
    .CLOSED(CLOSED), .Close_open(16'hf800), .Far_open(16'he000));
  door_maker door_maker_11 (
    .DOOR(DOOR), .FAR(FAR), .In(in_4), .Close_closed(16'h800), .Far_closed(16'h2000), .Out(out_31),
    .CLOSED(CLOSED), .Close_open(16'hf800), .Far_open(16'he000));
  door_maker door_maker_12 (
    .DOOR(DOOR), .FAR(FAR), .In(in_6), .Close_closed(16'hf800), .Far_closed(16'he000), .Out(out_33),
    .CLOSED(CLOSED), .Close_open(16'hf800), .Far_open(16'he000));
  door_maker door_maker_13 (
    .DOOR(DOOR), .FAR(FAR), .In(in_8), .Close_closed(16'h800), .Far_closed(16'h2000), .Out(out_35),
    .CLOSED(CLOSED), .Close_open(16'hf800), .Far_open(16'he000));
  door_maker door_maker_14 (
    .DOOR(DOOR), .FAR(FAR), .In(in_10), .Close_closed(16'hf800), .Far_closed(16'he000), .Out(out_37),
    .CLOSED(CLOSED), .Close_open(16'hf800), .Far_open(16'he000));
  door_maker door_maker_15 (
    .DOOR(DOOR), .FAR(FAR), .In(in_12), .Close_closed(16'h800), .Far_closed({16{1'b0}}), .Out(out_39),
    .CLOSED(CLOSED), .Close_open(16'hf800), .Far_open({16{1'b0}}));
  door_maker door_maker_16 (
    .DOOR(DOOR), .FAR(FAR), .In(in_14), .Close_closed(16'hf800), .Far_closed({16{1'b0}}), .Out(out_41),
    .CLOSED(CLOSED), .Close_open(16'hf800), .Far_open({16{1'b0}}));
  door_maker door_maker_17 (
    .DOOR(DOOR), .FAR(FAR), .In(in_16), .Close_closed(16'h800), .Far_closed({16{1'b0}}), .Out(out_43),
    .CLOSED(CLOSED), .Close_open(16'hf800), .Far_open({16{1'b0}}));
  door_maker door_maker_18 (
    .DOOR(DOOR), .FAR(FAR), .In(in_18), .Close_closed(16'hf800), .Far_closed({16{1'b0}}), .Out(out_45),
    .CLOSED(CLOSED), .Close_open(16'hf800), .Far_open({16{1'b0}}));

  assign out_46 = in_19;
  assign out_47 = in_20;
  assign out_48 = in_21;
  assign out_49 = in_22;
  assign out_50 = in_23;
  assign out_51 = in_24;

  // Notes on the sheet:
  //   Близко
  //   Далеко
  //   Обнуление
  //   Левая часть
  //   Код ошибки
  //   Код ошибки
  //   Правая часть
  //   Обнуление
endmodule

module door_maker (
  input  DOOR,
  input  FAR,
  input  CLOSED,
  input  [15:0] In,
  input  [15:0] Close_closed,
  input  [15:0] Far_closed,
  input  [15:0] Close_open,
  input  [15:0] Far_open,
  output [15:0] Out
);

  wire [15:0] multiplexer_1_out, multiplexer_2_out, multiplexer_3_out, or_1_out;

  Multiplexer #(.width(16), .disabled(0), .enable("false")) multiplexer_1 (
    .in0(Close_closed), .in1(Far_closed), .out(multiplexer_1_out), .sel(CLOSED));
  Multiplexer #(.width(16), .disabled(0), .enable("false")) multiplexer_2 (
    .in0(Close_open), .in1(Far_open), .out(multiplexer_2_out), .sel(CLOSED));
  Multiplexer #(.width(16), .disabled(0), .enable("false")) multiplexer_3 (
    .in0(multiplexer_1_out), .in1(multiplexer_2_out), .out(multiplexer_3_out), .sel(FAR));
  Multiplexer #(.width(16), .disabled(0), .enable("false")) multiplexer_4 (
    .in0(In), .in1(or_1_out), .out(Out), .sel(DOOR));
  assign or_1_out = In | multiplexer_3_out;  // OR_Gate or_1, 16 bits wide
endmodule
