// Logisim project death_mult.circ as structural Verilog: 1 circuit, main circuit main
module main (
  input  [4:0] mult,
  input  USE,
  input  [6:0] VOLUME,
  output [31:0] out_4,
  output [31:0] out_5,
  output [31:0] out_6,
  output [31:0] out_7,
  output [31:0] out_8,
  output [31:0] out_9,
  output [31:0] out_10,
  output [31:0] out_11,
  output [31:0] out_12,
  output [31:0] out_13,
  output [31:0] out_14,
  output [31:0] out_15,
  output [31:0] out_16,
  output [31:0] out_17,
  output [31:0] out_18,
  output [31:0] out_19,
  output [31:0] out_20,
  output [31:0] out_21,
  output [31:0] out_22,
  output [31:0] out_23,
  output [31:0] out_24,
  output [31:0] out_25,
  output [31:0] out_26,
  output [31:0] out_27,
  output [31:0] out_28,
  output [31:0] out_29,
  output [31:0] out_30,
  output [31:0] out_31,
  output [31:0] out_32,
  output [31:0] out_33,
  output [31:0] out_34,
  output [31:0] out_35
);

  wire and_1_out, clock_1_out, counter_1_carry, counter_4_q, counter_5_carry, counter_6_carry,
       counter_7_carry, or_1_out;
  wire [7:0] adder_1_out, counter_2_q, counter_3_q, multiplexer_1_out, multiplexer_2_out;
  wire [8:0] adder_2_out, adder_3_out, counter_8_q, counter_9_q, multiplexer_3_out;
  wire [15:0] rom_1_data;

  Clock clock_1 (.out(clock_1_out));
  Counter #(.max('h50)) counter_1 (.carry(counter_1_carry), .clk(clock_1_out));  // open: load, D, count, Q, clr
  Counter #(.max('h10)) counter_2 (
    .count(counter_1_carry), .Q(counter_2_q), .clk(clock_1_out));  // open: load, D, carry, clr
  Counter #(.max('hb)) counter_3 (
    .count(counter_1_carry), .Q(counter_3_q), .clk(clock_1_out));  // open: load, D, carry, clr
  Adder adder_1 (.a(counter_3_q), .b(8'h11), .out(adder_1_out));  // open: cin, cout
  Counter #(.width(1), .max('h1)) counter_4 (
    .count(USE), .Q(counter_4_q), .clk(USE), .clr(counter_7_carry));  // open: load, D, carry
  Counter #(.width(9)) counter_5 (
    .count(mult[3]), .carry(counter_5_carry), .clk(clock_1_out));  // open: load, D, Q, clr
  Counter #(.width(9)) counter_6 (
    .count(mult[4]), .carry(counter_6_carry), .clk(clock_1_out));  // open: load, D, Q, clr
  Counter #(.max('h40)) counter_7 (
    .count(or_1_out), .carry(counter_7_carry), .clk(clock_1_out));  // open: load, D, Q, clr
  or or_1 (or_1_out, counter_4_q, counter_7_carry);
  Counter #(.width(9), .max('h5c), .ongoal("stay")) counter_8 (
    .count(counter_5_carry), .Q(counter_8_q), .clk(clock_1_out));  // open: load, D, carry, clr
  Counter #(.width(9), .max('hbd), .ongoal("stay")) counter_9 (
    .count(counter_6_carry), .Q(counter_9_q), .clk(clock_1_out));  // open: load, D, carry, clr
  Multiplexer #(.width(8), .disabled(0), .enable("false")) multiplexer_1 (
    .in0(counter_2_q), .in1(adder_1_out), .out(multiplexer_1_out), .sel(mult[0]));
  Multiplexer #(.width(8), .disabled(0), .enable("false")) multiplexer_2 (
    .in0(multiplexer_1_out), .in1(8'h30), .out(multiplexer_2_out), .sel(counter_4_q));
  Adder #(.width(9)) adder_2 (.a(counter_8_q), .b(9'h4), .out(adder_2_out));  // open: cin, cout
  Adder #(.width(9)) adder_3 (.a(counter_9_q), .b(9'h61), .out(adder_3_out));  // open: cin, cout
  Multiplexer #(.select(5), .width(9), .enable("false")) multiplexer_3 (
    .in0({9{1'b0}}), .in1(9'h1), .in2(9'h2), .in3(9'h2), .in4(9'h3), .in5(9'h3), .in6(9'h3), .in7(9'h3),
    .in8(adder_2_out), .in9(adder_2_out), .in10(adder_2_out), .in11(adder_2_out), .in12(adder_2_out),
    .in13(adder_2_out), .in14(adder_2_out), .in15(adder_2_out), .in16(adder_3_out), .in17(adder_3_out),
    .in18(adder_3_out), .in19(adder_3_out), .in20(adder_3_out), .in21(adder_3_out), .in22(adder_3_out),
    .in23(adder_3_out), .in24(adder_3_out), .in25(adder_3_out), .in26(adder_3_out), .in27(adder_3_out),
    .in28(adder_3_out), .in29(adder_3_out), .in30(adder_3_out), .in31(adder_3_out), .out(multiplexer_3_out),
    .sel(mult));
  // Probe on multiplexer_3_out
  ROM #(.dataWidth(16)) rom_1 (.addr(multiplexer_2_out), .data(rom_1_data));  // open: sel
  and and_1 (and_1_out, ~mult[2], ~mult[3], ~mult[4]);  // AND_Gate
  // Advanced_buzzer advanced_buzzer_1: pin names not known; wires that end beside it: rom_1_data, and_1_out, VOLUME
  ROM #(.addrWidth(9), .dataWidth(32)) rom_2 (.addr(multiplexer_3_out), .data(out_4));  // open: sel
  ROM #(.addrWidth(9), .dataWidth(32)) rom_3 (.addr(multiplexer_3_out), .data(out_8));  // open: sel
  ROM #(.addrWidth(9), .dataWidth(32)) rom_4 (.addr(multiplexer_3_out), .data(out_12));  // open: sel
  ROM #(.addrWidth(9), .dataWidth(32)) rom_5 (.addr(multiplexer_3_out), .data(out_16));  // open: sel
  ROM #(.addrWidth(9), .dataWidth(32)) rom_6 (.addr(multiplexer_3_out), .data(out_20));  // open: sel
  ROM #(.addrWidth(9), .dataWidth(32)) rom_7 (.addr(multiplexer_3_out), .data(out_24));  // open: sel
  ROM #(.addrWidth(9), .dataWidth(32)) rom_8 (.addr(multiplexer_3_out), .data(out_28));  // open: sel
  ROM #(.addrWidth(9), .dataWidth(32)) rom_9 (.addr(multiplexer_3_out), .data(out_32));  // open: sel
  ROM #(.addrWidth(9), .dataWidth(32)) rom_10 (.addr(multiplexer_3_out), .data(out_5));  // open: sel
  ROM #(.addrWidth(9), .dataWidth(32)) rom_11 (.addr(multiplexer_3_out), .data(out_9));  // open: sel
  ROM #(.addrWidth(9), .dataWidth(32)) rom_12 (.addr(multiplexer_3_out), .data(out_13));  // open: sel
  ROM #(.addrWidth(9), .dataWidth(32)) rom_13 (.addr(multiplexer_3_out), .data(out_17));  // open: sel
  ROM #(.addrWidth(9), .dataWidth(32)) rom_14 (.addr(multiplexer_3_out), .data(out_21));  // open: sel
  ROM #(.addrWidth(9), .dataWidth(32)) rom_15 (.addr(multiplexer_3_out), .data(out_25));  // open: sel
  ROM #(.addrWidth(9), .dataWidth(32)) rom_16 (.addr(multiplexer_3_out), .data(out_29));  // open: sel
  ROM #(.addrWidth(9), .dataWidth(32)) rom_17 (.addr(multiplexer_3_out), .data(out_33));  // open: sel
  ROM #(.addrWidth(9), .dataWidth(32)) rom_18 (.addr(multiplexer_3_out), .data(out_6));  // open: sel
  ROM #(.addrWidth(9), .dataWidth(32)) rom_19 (.addr(multiplexer_3_out), .data(out_10));  // open: sel
  ROM #(.addrWidth(9), .dataWidth(32)) rom_20 (.addr(multiplexer_3_out), .data(out_14));  // open: sel
  ROM #(.addrWidth(9), .dataWidth(32)) rom_21 (.addr(multiplexer_3_out), .data(out_18));  // open: sel
  ROM #(.addrWidth(9), .dataWidth(32)) rom_22 (.addr(multiplexer_3_out), .data(out_22));  // open: sel
  ROM #(.addrWidth(9), .dataWidth(32)) rom_23 (.addr(multiplexer_3_out), .data(out_26));  // open: sel
  ROM #(.addrWidth(9), .dataWidth(32)) rom_24 (.addr(multiplexer_3_out), .data(out_30));  // open: sel
  ROM #(.addrWidth(9), .dataWidth(32)) rom_25 (.addr(multiplexer_3_out), .data(out_34));  // open: sel
  ROM #(.addrWidth(9), .dataWidth(32)) rom_26 (.addr(multiplexer_3_out), .data(out_7));  // open: sel
  ROM #(.addrWidth(9), .dataWidth(32)) rom_27 (.addr(multiplexer_3_out), .data(out_11));  // open: sel
  ROM #(.addrWidth(9), .dataWidth(32)) rom_28 (.addr(multiplexer_3_out), .data(out_15));  // open: sel
  ROM #(.addrWidth(9), .dataWidth(32)) rom_29 (.addr(multiplexer_3_out), .data(out_19));  // open: sel
  ROM #(.addrWidth(9), .dataWidth(32)) rom_30 (.addr(multiplexer_3_out), .data(out_23));  // open: sel
  ROM #(.addrWidth(9), .dataWidth(32)) rom_31 (.addr(multiplexer_3_out), .data(out_27));  // open: sel
  ROM #(.addrWidth(9), .dataWidth(32)) rom_32 (.addr(multiplexer_3_out), .data(out_31));  // open: sel
  ROM #(.addrWidth(9), .dataWidth(32)) rom_33 (.addr(multiplexer_3_out), .data(out_35));  // open: sel

  // Other names for the same wires on the sheet: key = mult[0]; monster = mult[1]; death = mult[2]; hungry = mult[3];
  //   win = mult[4]

  // Notes on the sheet:
  //   Sound of USE
  //   GOP_GOOD
  //   Background music
  //   Alarm music
  //   GOP_OK
  //   GOP_BAD
  //   DEATH
  //   HUNGRY_DEATH
  //   WIN
  //   contents of rom_1 (hex, n*v repeats v):
  //   a5 c4 a5 f7 1 c4 dc c4 a5 83 a5 c4 a5 f7 a5 83 1 f7 dc 126 1 7c 1 7c 1 7c 7*1 15*0 52
  //   contents of rom_2 (hex, n*v repeats v):
  //   53*0 800 2085040 2085040 4229020 2085040 4229020 2085040 4229020 33*0 39ca9254 39ca9254 5*0
  //   5*7ffffc0 66*0 27*7ffffc0 14*ffffffff 0 0 18*5087f085 24*0 10*7ffe00 10*3f
  //   contents of rom_3 (hex, n*v repeats v):
  //   24*0 10*70381c0 19*0 1000 2089040 2089040 21c5020 2089040 21c5020 2089040 21c5020 33*0 2a2abf54
  //   2a2abf54 5*0 5*3ffff80 16*0 30*e0000007 10*0 10*a00 27*3ffff80 12*ffffffff ff8001ff ff8001ff 0 0
  //   18*f0849087 24*0 10*ffff00 4*1bf bf bf 4*1bf
  //   contents of rom_4 (hex, n*v repeats v):
  //   6bc00 6bc00 6bc00 700fe00e 20*6bc00 10*8844220 19*0 2000 4000040 4000040 2143740 4000040 2143740
  //   4000040 2143740 9*0 22*6bc00 0 0 2a2ca164 2a2ca164 0 4*6bc00 5*1ffff00 10*0 6*6bc00 30*a0000005
  //   10*e718e70 10*0 27*1ffff00 12*ffffffff 4*0 18*5087f085 24*0 10*1ffff80 e1f e1f 21f 21f 1f 1f 21f 21f
  //   e1f e1f
  //   contents of rom_5 (hex, n*v repeats v):
  //   3adf00 3adf00 3adf00 88301811 20*3adf00 10*804020 19*0 8000 4000020 4000020 2085040 4000020 2085040
  //   4000020 2085040 9*0 22*3adf00 5*0 4*3adf00 fffe00 fffe00 fffe00 ffff00 fffe00 10*0 6*3adf00
  //   30*ffffffff 10*94a4a40 10*1ceeaef8 27*fffe00 12*ffffffff 4*0 18*50849085 10*aef3000 14*0 10*3ffffc0
  //   10*1f 10*d914400
  //   contents of rom_6 (hex, n*v repeats v):
  //   fb5f80 fb5f80 fb5f80 88400411 20*fb5f80 10*7b3d9e0 19*0 10180 40abb20 40abb20 2089040 40abb20
  //   2089040 40abb20 2089040 9*0 22*fb5f80 5*0 4*fb5f80 1ff000 1ff000 1ff800 1ff100 1ff000 10*0 6*fb5f80
  //   30*20000004 10*e724a70 10*128aa820 27*1ff000 10*ffffffff fff00fff fff00fff 4*0 18*5087f085
  //   10*a884800 0 0 80000000 80000000 0 0 6*80000000 0 0 10*3ffffc0 10*5f 10*124a2800
  //   contents of rom_7 (hex, n*v repeats v):
  //   3fd6fc0 3fd6fc0 3fd6fc0 a8800211 20*3fd6fc0 10*804020 18*0 1e1 200c0 40d88a0 40d88a0 4000040 40d88a0
  //   4000040 40d88a0 4000040 9*0 22*3fd6fc0 5*0 4*3fd6fc0 0 800 80800 408100 1000 10*1cfe300 6*3fd6fc0
  //   30*3914adb4 10*9424a40 10*1ceeee20 27*0 10*ffffffff e0000007 e0000007 4*0 18*f0800087 10*ae84800 0 0
  //   40000000 40000000 80000000 80000000 4*e0000000 c0000000 c0000000 80000000 80000000 10*7fffffc 4*18f
  //   f f 4*18f 10*124a2800
  //   contents of rom_8 (hex, n*v repeats v):
  //   7fdafc0 7fdafc0 7fdafc0 6080020e 20*7fdafc0 10*884422c 18*0 7e1e 20380 2edb8a0 2edb8a0 4000020
  //   2edb8a0 4000020 2edb8a0 4000020 9*0 22*7fdafc0 e338448 e338448 10000004 10000004 300000 4*7fdafc0
  //   800 80800 80000 401000 80000 10*2610480 6*7fdafc0 30*2d14ed9c 10*9425f40 10*1288a820 27*0
  //   10*ffffffff 6*0 18*800080 10*e8f4800 0 0 a0000000 a0000000 e0000000 e0000000 f8000000 f8000000
  //   f0000000 f0000000 e0000000 e0000000 c0000000 c0000000 10*1bffffc3 603 603 6*3 603 603 10*12441000
  //   contents of rom_9 (hex, n*v repeats v):
  //   ffebfc0 ffebfc0 ffebfc0 21000100 20*ffebfc0 10*70381cc 18*0 18000 40200 2088890 2088890 40abb20
  //   2088890 40abb20 2088890 40abb20 9*0 22*ffebfc0 94a4448 94a4448 8000008 8000008 480000 4*ffebfc0
  //   80800 80800 8100 401000 80400 10*210840 6*ffebfc0 30*29b6ad94 10*e419170 10*1ce8ae20 27*0 8*ffffffff
  //   f000000f f000000f 6*0 18*ffffff8 10*a894800 0 0 40000000 40000000 d0000000 d0000000 fe000000
  //   fe000000 fc000000 fc000000 f8000000 f8000000 e0000000 e0000000 10*23ffffc0 10*11 10*12441000
  //   contents of rom_10 (hex, n*v repeats v):
  //   1ffef7c0 1ffef7c0 1ffef7c0 1000100 20*1ffef7c0 10*4 18*0 20200 88018 208bb10 208bb10 40d88a0 208bb10
  //   40d88a0 208bb10 40d88a0 9*0 10*1ffef7c0 8*1ffef3c0 4*1ffef1c0 e4b8a48 e4b8a48 7fffff0 7fffff0 400000
  //   4*1ffef7c0 80800 80000 8100 1000 88400 10*3e10840 6*1ffef7c0 30*2934ad14 42*0 10000 10000 0 0 0
  //   8*ffffffff c0000003 c0000003 6*0 18*8000008 10*aef32a0 0 0 a0000000 a0000000 a8000000 a8000000
  //   fd000000 fd000000 7f000000 7f000000 fc000000 fc000000 f0000000 f0000000 10*43fffffc 4*20 0 0 4*20
  //   10*f882800
  //   contents of rom_11 (hex, n*v repeats v):
  //   3fff8780 3fff8780 3fff8780 c1000107 20*3fff8780 10*8 18*0 20200 105824 2000010 2000010 2edb8a0
  //   2000010 2edb8a0 2000010 2edb8a0 9*0 8*3fff8780 3fff8380 3fff8380 8*3fff8180 4*3fff8080 94a4a78
  //   94a4a78 6000010 6000010 400000 4*3fff8380 80000 8100 408100 80000 8400 10*210840 6*3fff8380
  //   30*29b6ad14 42*0 10000 10000 0 0 0 8*ffffffff 80000001 80000001 6*0 18*ffffff8 12*0 40000000
  //   40000000 50000000 50000000 fa800000 fa800000 3fc00000 3fc00000 3f000000 3f000000 f8000000 f8000000
  //   10*43ffffc3 7c00042 7c00042 6*7c00002 7c00042 7c00042 10*2082800
  //   contents of rom_12 (hex, n*v repeats v):
  //   3e000380 3e000380 3e000380 7100010c 20*3e000380 26*0 800000 7000 30201 3c2c 2000410 2000410 2088890
  //   2000410 2088890 2000410 2088890 9*0 8*3e000380 3e000180 3e000180 12*3e000080 94a4e48 94a4e48 4000010
  //   4000010 705f273e 4*3e000180 8100 8100 401000 80400 808000 10*2610480 6*3e000180 30*20000004
  //   10*e8819d0 31*0 10000 111000 10000 0 0 0 8*ffffffff 8*0 18*fc00001f 12*0 a0000000 a0000000 a8000000
  //   a8000000 75000000 75000000 1fa00000 1fa00000 1fc00000 1fc00000 fc000000 fc000000 10*83ffffc0
  //   3f818082 3f818082 3f818002 3f818002 3f818000 3f818000 3f818002 3f818002 3f818082 3f818082 10*21044a8
  //   contents of rom_13 (hex, n*v repeats v):
  //   4f83dc0 4f83dc0 4f801c0 4a000098 20*4f83dc0 10*49713fa0 16*0 1c88000 69400 70006 307018 2044f10
  //   2044f10 208bb10 2044f10 208bb10 2044f10 208bb10 9*0 8*4f83dc0 47839c0 47839c0 43830c0 43830c0
  //   41830c0 41830c0 4*41010c0 4*40000c0 94a5148 94a5148 4000010 4000010 4b442488 4*4f83dc0 8100 408100
  //   401000 88400 800000 10*1c10300 6*4f83dc0 30*ffffffff 10*8880490 10*8bab80 18*f0000 0 0 0 10000 92000
  //   92000 0 0 0 6*ffffffff c0000003 c0000003 8*0 18*2020020 14*0 50000000 50000000 4a800000 4a800000
  //   1f500000 1f500000 ff00000 ff00000 7e000000 7e000000 10*200007c ef878004 ef878004 6*ef878000 ef878004
  //   ef878004
  //   contents of rom_14 (hex, n*v repeats v):
  //   40441c0 40441c0 50406c0 72600c8c 20*40441c0 10*2a490420 14*0 800000 800000 3fdd000 78200 f8f9a
  //   204612 10effc8 10effc8 2000010 10effc8 2000010 10effc8 2000010 9*0 8*40441c0 40440c0 40440c0 4044040
  //   4044040 10*4000040 e339148 e339148 4000010 4000010 4a445488 4*40441c0 408100 401000 1000 8400 800000
  //   10*0 6*40441c0 30*a0000005 10*ee81ca8 10*8a2a80 16*f0000 70000 4*0 10000 7c000 54000 54000 0 0
  //   6*ffffffff 80000001 80000001 8*0 18*3ffffe0 14*0 28000000 28000000 25000000 25000000 ea00000 ea00000
  //   7e80000 7e80000 3f800000 3f800000 10*2e96743 b74fc004 b74fc004 6*b74fc000 b74fc004 b74fc004
  //   contents of rom_15 (hex, n*v repeats v):
  //   4701dc0 4701dc0 43218c0 c2f01e87 18*4701dc0 40001c0 40001c0 10*1c4a8420 14*0 1c88000 1c88000 7fff800
  //   3f0100 7c306 200481 13ffff8 13ffff8 2000410 13ffff8 2000410 13ffff8 2000410 f000000 f03c000 f03c1e0
  //   f000000 f03c000 f03c1e0 f000000 f03c000 f03c1e0 8*4701dc0 4701cc0 4701cc0 12*4701c40 0 0 4000010
  //   4000010 73445708 4*4701cc0 401000 401000 80000 808000 11*0 4*4701cc0 40000c0 40000c0 30*e0aa6407
  //   10*aab04b8 10*dbab80 16*70000 4*0 38000 38000 7c000 38000 38000 0 0 4*ffffffff 80000001 80000001
  //   10*0 18*30680a0 16*0 12800000 12800000 9500000 9500000 7d40000 7d40000 fc00000 fc00000 10*2a95540
  //   10*dc73c000
  //   contents of rom_16 (hex, n*v repeats v):
  //   48822c0 48822c0 4483cc0 2f83e80 10*48822c0 4c826c0 4c826c0 4e82ec0 4e82ec0 4*4f83ec0 4f83cc0 4f83cc0
  //   10*8728438 12*0 800000 800000 3fdd000 3fdd000 fffff00 3f80c0 f8081 1a0840 fffff0 fffff0 2044f10
  //   fffff0 2044f10 fffff0 2044f10 f000000 f03c000 f03c1e0 f000000 f03c000 f03c1e0 f000000 f03c000
  //   f03c1e0 4c826c0 4c826c0 8*4f83ec0 12*4f83e40 0 0 4000010 4000010 62447608 4*48822c0 401000 1000
  //   80400 800000 11*0 4*48822c0 4f83ec0 4f83ec0 30*ca6480 10*eeb18a8 10*da3980 15*70000 4*0 10000 38000
  //   1ff000 7ffc00 3ff800 7c000 10000 0 ffffffff ffffffff 80000001 80000001 12*0 18*f2fabea7 18*0 4a00000
  //   4a00000 3a80000 3a80000 3f00000 3f00000 10*2ad657c 10*706bc000
  //   contents of rom_17 (hex, n*v repeats v):
  //   59552c0 59552c0 58562c0 2fc7e80 16*59552c0 4*5fd7ec0 10*1c438424 12*0 1c88000 1c88000 7fff800
  //   7fff800 1ffffc80 13f0020 1f0300 f0140 1fffe0 1fffe0 10effc8 1fffe0 10effc8 1fffe0 10effc8 f000000
  //   f03c000 f03c1e0 f000000 f03c000 f03c1e0 f000000 f03c000 f03c1e0 4*59552c0 6*5fd7ec0 5fc7ec0 5fc7ec0
  //   10*5fc7e40 0 0 4000010 4000010 53445508 4*59552c0 1000 80000 88400 800000 80000 10*0 59552c0 59552c0
  //   4*5954ac0 30*c46400 10*10000 10*aa2a80 14*20000 6*0 38000 38000 7c000 38000 38000 0 0 ffffffff
  //   ffffffff 14*0 6*528aa2a5 52faa2a5 52faa2a5 10*528aa2a5 18*0 2500000 2500000 2540000 2540000 1fc0000
  //   1fc0000 10*2ab5543 10*a07f0000 10*c
  //   contents of rom_18 (hex, n*v repeats v):
  //   5c542c0 5c542c0 59552c0 f2fc7e80 5c542c0 5c542c0 5c546c0 5c546c0 5e546c0 5e546c0 5f55ec0 5f55ec0
  //   10*5fd7ec0 5fd3cc0 5fd3cc0 10*2a444424 10*0 800000 800000 3fdd000 3fdd000 fffff00 fffff00 13ff7080
  //   1fa0210 f8f91 1f8491 bbfc0 bbfc0 13ffff8 bbfc0 13ffff8 bbfc0 13ffff8 f000000 f03c000 f03c1e0 f000000
  //   f03c000 f03c1e0 f000000 f03c000 f03c1e0 12*5fd7ec0 10*4fc7e40 0 0 4000010 4000010 48445488 4*5c542c0
  //   80000 80400 8400 0 80400 10*a0e0 4*5c542c0 5fd3cc0 5fd3cc0 30*c4e480 10*20000 10*abaa80 13*f8000 8*0
  //   10000 7c000 54000 54000 0 0 ffffffff ffffffff 14*0 f29ea2a7 f29ea2a7 f29aa2a7 f29aa2a7 f2eaa2a7
  //   f2eaa2a7 f2aaa2a7 f2aaa2a7 10*f28aa2a7 10*3818c890 10*0 1280000 1280000 ff0000 ff0000 10*2af777c
  //   10*e07f0000
  //   contents of rom_19 (hex, n*v repeats v):
  //   5f93cc0 5f93cc0 5c57cc0 1a783c9f 18*5f93cc0 4f900c0 4f900c0 10*49444438 10*0 1c88000 1c88000 7fff800
  //   7fff800 1ffffc80 1ffffc80 8f22040 1fc3400 7c00a 1f6300 11380 11380 fffff0 11380 fffff0 11380 fffff0
  //   9*0 8*5f93cc0 4*4f93cc0 4793c40 4793c40 8*4783c40 0 0 4000010 4000010 400000 4*5f93cc0 80400 88400
  //   808000 0 88400 10*110 4*5f93cc0 5f900c0 5f900c0 30*c4aa00 20*0 12*f8000 9*0 10000 92000 92000 0 0 0
  //   ffffffff ffffffff 80000001 80000001 12*0 529ea6a5 529ea6a5 52baa6a5 52baa6a5 4*52faa6a5 52baa6a5
  //   52baa6a5 8*528aa6a5 10*48292890 10*0 940000 940000 7e8000 7e8000 10*c2000043 10*e0fb8000 10*2a49c392
  //   contents of rom_20 (hex, n*v repeats v):
  //   6f901c0 6f901c0 6f901c0 71010115 20*6f901c0 20*0 3fdd000 3fdd000 fffff00 fffff00 13ff7080 13ff7080
  //   8200040 ff81808 f8a84 7e01b 100 100 1fffe0 100 1fffe0 100 1fffe0 9*0 8*6f901c0 67101c0 67101c0
  //   62100c0 62100c0 10*60100c0 0 0 4000010 4000010 400000 4*6f901c0 88400 8400 800000 80000 8400
  //   10*121f110 6*6f901c0 40*0 10*30 11*f8000 10*0 10000 111000 10000 0 0 0 4*ffffffff 80000001 80000001
  //   10*0 528ea2a5 528ea2a5 529ea2a5 529ea2a5 52baa2a5 52baa2a5 52faa2a5 52faa2a5 52baa2a5 52baa2a5
  //   8*528aa2a5 10*48292d90 12*3c000 7d4000 7d4000 10*3ffffc0 10*c8cbc000 10*2a492452
  //   contents of rom_21 (hex, n*v repeats v):
  //   2720380 2720380 2727b80 81838315 20*2720380 18*0 800000 800000 7fff800 7fff800 1ffffc80 1ffffc80
  //   8f22040 8f22040 8000040 1ff01c04 1f8a9f 7f2b6 0 0 bbfc0 0 bbfc0 0 bbfc0 9*0 8*2720380 2220180
  //   2220180 2020180 2020180 6*2020080 2030080 2030080 2038080 2038080 0 0 4000010 4000010 400000
  //   4*2720180 8400 808000 800000 80400 808000 10*1210090 6*2720180 50*0 10*f8000 12*0 10000 10000 0 0 0
  //   6*ffffffff 80000001 80000001 8*0 4*528ea2a5 529aa2a5 529aa2a5 52faa2a5 52faa2a5 529aa2a5 529aa2a5
  //   8*528aa2a5 10*38292da8 12*7e000 3aa000 3aa000 10*3fffffc 10*6c39e000 10*2a592456
  //   contents of rom_22 (hex, n*v repeats v):
  //   3040380 3040380 3040380 71438515 20*3040380 18*0 1c88000 1c88000 fffff00 fffff00 13ff7080 13ff7080
  //   8200040 8200040 8dd1040 fe18c03 fcf80 7fe2c 0 0 11380 0 11380 0 11380 9*0 8*3040380 4*3040180
  //   3040080 3040080 4*3020080 3030080 3030080 3038080 3038080 f99e600 f99e600 4000010 4000010 2400000
  //   4*3040180 808000 800000 0 88400 800000 10*1210020 6*3040180 30*7ffffc0 10*8be8a48 10*6322648 9*f8000
  //   13*0 10000 4*0 6*ffffffff c0000003 c0000003 8*0 4*f28ebea7 f2babea7 f2babea7 f2dabea7 f2dabea7
  //   f2babea7 f2babea7 8*f28abea7 10*18292db8 12*7e000 256000 256000 10*3ffffc3 10*3ff0f000 10*2a59c456
  //   contents of rom_23 (hex, n*v repeats v):
  //   1080780 1080780 1080780 18a28a00 20*1080780 16*0 200000 200000 3fdd000 3fdd000 1ffffc80 1ffffc80
  //   8f22040 8f22040 8000040 8000040 9111040 fe2e800 fe004 fe00 0 0 100 0 100 0 100 9*0 8*1080780 1080380
  //   1080380 4*1040180 1020080 1020080 1030080 1030080 1020080 1020080 1038080 1038080 2250900 2250900
  //   4000010 4000010 181c000 4*1080180 800000 800000 0 8400 800000 10*121c040 6*1080180 30*4000040
  //   10*8888a88 10*a4a2948 8*70000 19*0 8*ffffffff 8*0 4*29effa0 2deffa0 2deffa0 12*2faffa0 10*287d2aa8
  //   12*7e0f8 16e0f8 16e0f8 10*3fffffc 10*2187800 10*1c69245a
  //   contents of rom_24 (hex, n*v repeats v):
  //   1080700 1080700 1080700 f0a00a00 20*1880700 10*89c8a20 6*0 722000 722000 7fff800 7fff800 13ff7080
  //   13ff7080 8200040 8200040 8dd1040 8dd1040 51db740 1ff46180 1fc884 fe08 16*0 8*1880700 4*1880300
  //   1840100 1840100 1820100 1820100 1830100 1830100 4*1800100 2250900 2250900 6000010 6000010 22000
  //   4*1080300 800000 0 80000 808000 0 10*e10040 6*1080300 10*4000040 6*4500040 6*4400040 8*4c00040
  //   10*8889308 10*a4a2958 7*70000 20*0 8*ffffffff 80000001 80000001 6*0 6*37f0060 4*3570060 3970060
  //   3970060 6*3070060 10*4844caa8 12*fc4af07 fcdaf07 fcdaf07 10*3ffffc3 10*fffbc00 10*1c69245a
  //   contents of rom_25 (hex, n*v repeats v):
  //   1060700 1460700 1060700 aaaa00 20*1460f00 10*5228940 6*0 ff7400 ff7400 fffff00 fffff00 8f22040
  //   8f22040 8000040 8000040 9111040 9111040 511b020 f0520a0 3fc884 1ff10 16*0 8*1460f00 1460700 1460700
  //   1460300 1460300 1420100 1420100 1400100 1400100 6*1400300 2250900 2250900 7fffff0 7fffff0 22000
  //   4*1060300 1ff000 1ff000 1ff400 9ff000 1ff000 10*210060 6*1060300 10*4000040 6*4526c40 6*4554840
  //   8*45a9640 10*8885208 10*a4b6958 27*1ff000 8*ffffffff c0000003 c0000003 6*0 18*ffffffff 10*0
  //   14*f87d3801 10*3ffffc0 10*f97dc00 10*2a69245a
  //   contents of rom_26 (hex, n*v repeats v):
  //   1000700 1601700 1800700 f8aaaa1f 20*1200f00 10*5228940 4*0 40000 40000 1fffe00 1fffe00 1ffffc80
  //   1ffffc80 8200040 8200040 8dd1040 8dd1040 51db740 51db740 4dd5020 81240e0 1f8700 3f20 16*0 8*1200f00
  //   1200700 1200700 1200300 1200300 4*1200100 6*1200500 2250900 2250900 8000008 8000008 4000 4*1000700
  //   e00e00 e00e00 e80e00 e00e00 e00e00 10*210000 6*1000700 10*400005c 6*452685c 6*4d5485c 8*492965c
  //   10*a886314 10*a4b6968 5*e50e00 22*e00e00 8*ffffffff f000000f f000000f 6*0 10*4000010 4380010 4380010
  //   4140010 4140010 4*4000010 10*0 14*7e000 10*3fffffc 10*3fb7fc00 10*2a492452
  //   contents of rom_27 (hex, n*v repeats v):
  //   187e700 1bfe700 878700 a89ff205 20*1a7ef00 10*2227880 4*0 e4400 e4400 3ffffc0 3ffffc0 13ff7080
  //   13ff7080 8000040 8000040 9111040 9111040 511b020 511b020 4000020 8018840 f803c 3f00 16*0 6*1a7ef00
  //   1a00f00 1a00f00 1a00700 1a00700 4*1a00300 1a00500 1a00500 1a10500 1a10500 1a14500 1a14500 1a54500
  //   1a54500 2190654 2190654 10000004 10000004 8000 4*187e700 1000100 1000100 1008500 1800100 1800100
  //   10*21f060 6*187e700 8*4000054 400005c 400005c 452685c 452685c 4526854 4526854 452685c 452685c
  //   4c9c85c 4c9c85c 4c9c854 4c9c854 4c9c85c 4c9c85c 45ab65c 45ab65c 6*45ab654 10*a882294 10*1f4aa968
  //   4*1050100 23*1000100 10*ffffffff 6*0 18*ffffff8 10*0 14*7e000 10*3ffffc3 10*6fbbf800 10*2a49c392
  //   contents of rom_28 (hex, n*v repeats v):
  //   885700 6572700 cfc700 a84aa40d a85f00 a85f00 4*ab5f00 ab7f00 ab7f00 12*ab3f00 10*2220880 4*0 1fee80
  //   1fee80 7ffff20 7ffff20 8f22040 8f22040 8dd1040 8dd1040 51db740 51db740 4dd5020 4dd5020 2000020
  //   2300840 703c3 3fc0 16*0 6*ab3f00 4*afef00 afe700 afe700 afe300 afe300 8*afe500 4*0 10000 4*885700
  //   fe0000ff fe0800ff fe0080ff fe0000ff fe0800ff 10*60 6*885700 6*400005c 400005e 400005e 400005a
  //   400005a 472485a 472485a 4*472485e 6*4c9485e 4*453b25e 4*453b25c 10*a88429c 10*1132a648 fe0500ff
  //   fe0500ff fe0500ff 24*fe0000ff 10*ffffffff e0000007 e0000007 4*0 10*8000008 4*81c0008 8028008 8028008
  //   8000008 8000008 10*0 14*1c07e000 10*c3fffff8 10*efbbe000
  //   contents of rom_29 (hex, n*v repeats v):
  //   c02e00 39cfce00 4fce00 a92aa91b e02e00 e02e00 e62e00 e62e00 e7ee00 e7ee00 e7fe00 e7fe00 12*e7ee00
  //   10*5220900 0 0 8000 8000 3fffc0 3fffc0 4ffdc20 4ffdc20 8200040 8200040 9111040 9111040 511b020
  //   511b020 4000020 4000020 2091040 11a3000 37c00 1200 16*0 8*e7ee00 e78e00 e78e00 e18600 e18600
  //   4*e00600 e10600 e10600 e50600 e50600 e54600 e54600 4*0 18000 4*c02e00 4000040 4080440 4008040
  //   4000040 4088440 10*0 6*c02e00 4*4000040 4000043 4000043 4*4000045 6*4554c45 6*4c95445 4*4dab645
  //   4*4dab640 10*a884294 10*0 40d8040 40d8040 25*4000040 10*ffffffff fff00fff fff00fff 4*0 18*1ffffffc
  //   10*3030300 14*3e07e000 10*33ffffc4 10*efbf8000
  //   contents of rom_30 (hex, n*v repeats v):
  //   601400 76601c00 601c00 3a00b80 6*601400 602c00 602c00 12*600c00 10*5220900 0 0 1c880 1c880 7ffff8
  //   7ffff8 23c8810 23c8810 8000040 8000040 51db740 51db740 4dd5020 4dd5020 2000020 2000020 20a1040
  //   a81b00 18000 17*0 14*600c00 8*600400 5*0 4*601400 4000040 4000440 4000040 4000040 4808440 10*0
  //   6*601400 4000040 4000040 4000041 4000041 22*4000042 4000041 4000041 4000040 4000040 10*f888254 10*0
  //   41dc040 26*4000040 12*ffffffff 4*0 12*10000004 100c0004 100c0004 100f0004 100f0004 10000004 10000004
  //   10*3030300 14*3c03c000 10*fffffc4 10*efbe0000
  //   contents of rom_31 (hex, n*v repeats v):
  //   203e00 38203800 203800 1101100 6*7e03ef0 7e017f0 7e017f0 7e03ff0 7e03ff0 10*7e01ff0 10*89c0a2a 0 0
  //   3fdd0 3fdd0 ffffe4 ffffe4 2080010 2080010 8dd1040 8dd1040 511b020 511b020 4000020 4000020 2091040
  //   2091040 2ec2840 300c00 18*0 14*7e01ff0 8*7e00ff0 4*0 18000 4*7e03ef0 4*4000040 4800040 10*0
  //   6*7e03ef0 7ffffc0 7ffffc0 26*7ffffc1 7ffffc0 7ffffc0 10*0 10*18c600 27*4000040 12*ffffffff 4*0
  //   18*ffffffff 10*0 14*f 10*3fffffc 10*ffbe0000
  //   contents of rom_32 (hex, n*v repeats v):
  //   1ff600 1ff000 1ff000 10fe100 6*3ffff6fc 3ffff7fc 3ffff7fc 3fffeffc 3fffeffc 10*3ffffffc 10*0 800 800
  //   7fff8 7fff8 9ffb84 9ffb84 2000010 2000010 9111040 9111040 4dd5020 4dd5020 2000020 2000020 20a1040
  //   20a1040 40a3840 182400 18*0 22*3ffffffc 0 0 1b56dc0 1b56dc0 18000 4*3ffff6fc 5*60000c0 10*0
  //   6*3ffff6fc 40*0 10*18c600 27*60000c0 12*ffffffff ff8001ff ff8001ff 14*0 4*1c0000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
  //   contents of rom_33 (hex, n*v repeats v):
  //   4*0 6*7ffab9fe 7ffabbfe 7ffabbfe 7ffab7fe 7ffab7fe 7ffaaffe 7ffaaffe 8*7ffabffe 10*0 1c88 1c88 fffff
  //   fffff 479102 479102 2374410 2374410 51db740 51db740 4000020 4000020 2091040 2091040 2ec2840 2ec2840
  //   4094420 a4000 18*0 22*7ffaaffe 0 0 1266880 1266880 0 4*7ffab9fe 5*70001c0 10*0 6*7ffab9fe 50*0 27*7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
endmodule
