// Logisim project video_lib.circ as structural Verilog: 8 circuits, main circuit Video
module Video (
  input  [2:0] in_1,
  input  [2:0] in_2,
  input  [2:0] in_3,
  input  [2:0] in_4,
  output [15:0] out_5,
  output [15:0] out_6,
  output [15:0] out_7,
  output [15:0] out_8,
  output [15:0] out_9,
  output [15:0] out_10,
  output [15:0] out_11,
  output [15:0] out_12,
  output [15:0] out_13,
  output [15:0] out_14,
  output [15:0] out_15,
  output [15:0] out_16,
  output [15:0] out_17,
  output [15:0] out_18,
  output [15:0] out_19,
  output [15:0] out_20,
  output [15:0] out_21,
  output [15:0] out_22,
  output [15:0] out_23,
  output [15:0] out_24,
  output [15:0] out_25,
  output [15:0] out_26,
  output [15:0] out_27,
  output [15:0] out_28
);

  wire [1:0] n4_6_str_1_out_4, n4_6_str_2_out_4, n7_str_1_out_4, n7_str_2_out_4;
  wire [2:0] n8_10_str_1_out_6, n8_10_str_2_out_6, n11_str_1_out_6, n11_str_2_out_6, n12_str_1_out_6,
       n12_str_2_out_6;
  wire [15:0] dop_1_out_2, dop_1_out_3, dop_1_out_4, dop_1_out_5, dop_1_out_6, dop_1_out_7,
       dop_another_1_out_2, dop_another_1_out_3, dop_another_1_out_4, dop_another_1_out_5,
       dop_another_1_out_6, dop_another_1_out_7;

  dop dop_1 (
    .in_1(in_1), .out_2(dop_1_out_2), .out_3(dop_1_out_3), .out_4(dop_1_out_4), .out_5(dop_1_out_5),
    .out_6(dop_1_out_6), .out_7(dop_1_out_7));
  _12_str u_12_str_1 (._4(in_2[1]), ._3(in_2[2]), ._1(in_3[2]), ._0(in_4[2]), ._2(in_3[1]), .out_6(n12_str_1_out_6));
  _11_str u_11_str_1 (._4(in_2[1]), ._3(in_2[2]), ._1(in_3[2]), ._0(in_4[2]), ._2(in_3[1]), .out_6(n11_str_1_out_6));
  _8_10_str u_8_10_str_1 (
    ._4(in_2[1]), ._3(in_2[2]), ._1(in_3[2]), ._0(in_4[2]), ._2(in_3[1]), .out_6(n8_10_str_1_out_6));
  _7_str u_7_str_1 (._0(in_4[2]), ._1(in_3[2]), ._2(in_3[1]), .out_4(n7_str_1_out_4));
  _4_6_str u_4_6_str_1 (._0(in_4[2]), ._1(in_3[2]), ._2(in_3[1]), .out_4(n4_6_str_1_out_4));
  Multiplexer #(.select(3), .width(16), .enable("false")) multiplexer_1 (
    .in0(16'h2000), .in1(16'h2200), .in2(dop_1_out_2), .in3(dop_1_out_3), .in4(dop_1_out_4),
    .in5(dop_1_out_5), .in6(dop_1_out_6), .in7(dop_1_out_7), .out(out_5), .sel(n12_str_1_out_6));
  Multiplexer #(.select(3), .width(16), .enable("false")) multiplexer_2 (
    .in0(16'h2000), .in1(16'h2200), .in2(16'h223f), .in3(16'h23ff), .in4(16'h200), .in5(16'h23f),
    .in6(16'h3fff), .in7({16{1'b1}}), .out(out_7), .sel(n11_str_1_out_6));
  Multiplexer #(.select(3), .width(16), .enable("false")) multiplexer_3 (
    .in0(16'h2000), .in1(16'h2200), .in2(16'h2240), .in3(16'h200), .in4(16'h240), .in5(16'h2040),
    .in6(16'h40), .out(out_9), .sel(n8_10_str_1_out_6));  // open: in7
  Multiplexer #(.select(3), .width(16), .enable("false")) multiplexer_4 (
    .in0(16'h2000), .in1(16'h2200), .in2(16'h2280), .in3(16'h200), .in4(16'h280), .in5(16'h2080),
    .in6(16'h80), .out(out_11), .sel(n8_10_str_1_out_6));  // open: in7
  Multiplexer #(.select(3), .width(16), .enable("false")) multiplexer_5 (
    .in0(16'h2000), .in1(16'h2200), .in2(16'h2300), .in3(16'h200), .in4(16'h300), .in5(16'h2100),
    .in6(16'h100), .out(out_13), .sel(n8_10_str_1_out_6));  // open: in7
  Multiplexer #(.select(2), .width(16), .enable("false")) multiplexer_6 (
    .in0(16'h2000), .in1(16'h23ff), .in2(16'h3fff), .in3({16{1'b1}}), .out(out_15), .sel(n7_str_1_out_4));
  Multiplexer #(.select(2), .width(16), .enable("false")) multiplexer_7 (
    .in0(16'h2000), .in1(16'h2400), .in2(16'h400), .out(out_17), .sel(n4_6_str_1_out_4));  // open: in3
  Multiplexer #(.select(2), .width(16), .enable("false")) multiplexer_8 (
    .in0(16'h2000), .in1(16'h2800), .in2(16'h800), .out(out_19), .sel(n4_6_str_1_out_4));  // open: in3
  Multiplexer #(.select(2), .width(16), .enable("false")) multiplexer_9 (
    .in0(16'h2000), .in1(16'h3000), .in2(16'h1000), .out(out_21), .sel(n4_6_str_1_out_4));  // open: in3
  Multiplexer #(.width(16), .enable("false")) multiplexer_10 (
    .in0(16'h3fff), .in1({16{1'b1}}), .out(out_23), .sel(in_4[2]));
  Multiplexer #(.select(3), .width(16), .enable("false")) multiplexer_11 (
    .in0(16'h4), .in1(16'h44), .in2(dop_another_1_out_2), .in3(dop_another_1_out_3),
    .in4(dop_another_1_out_4), .in5(dop_another_1_out_5), .in6(dop_another_1_out_6),
    .in7(dop_another_1_out_7), .out(out_6), .sel(n12_str_2_out_6));
  Multiplexer #(.select(3), .width(16), .enable("false")) multiplexer_12 (
    .in0(16'h4), .in1(16'h44), .in2(16'hfc44), .in3(16'hffc4), .in4(16'h40), .in5(16'hfc40), .in6(16'hfffc),
    .in7({16{1'b1}}), .out(out_8), .sel(n11_str_2_out_6));
  Multiplexer #(.select(3), .width(16), .enable("false")) multiplexer_13 (
    .in0(16'h4), .in1(16'h44), .in2(16'h244), .in3(16'h40), .in4(16'h240), .in5(16'h204), .in6(16'h200),
    .out(out_10), .sel(n8_10_str_2_out_6));  // open: in7
  Multiplexer #(.select(3), .width(16), .enable("false")) multiplexer_14 (
    .in0(16'h4), .in1(16'h44), .in2(16'h144), .in3(16'h40), .in4(16'h140), .in5(16'h104), .in6(16'h100),
    .out(out_12), .sel(n8_10_str_2_out_6));  // open: in7
  Multiplexer #(.select(3), .width(16), .enable("false")) multiplexer_15 (
    .in0(16'h4), .in1(16'h44), .in2(16'hc4), .in3(16'h40), .in4(16'hc0), .in5(16'h84), .in6(16'h80),
    .out(out_14), .sel(n8_10_str_2_out_6));  // open: in7
  Multiplexer #(.select(2), .width(16), .enable("false")) multiplexer_16 (
    .in0(16'h4), .in1(16'hffc4), .in2(16'hfffc), .in3({16{1'b1}}), .out(out_16), .sel(n7_str_2_out_4));
  Multiplexer #(.select(2), .width(16), .enable("false")) multiplexer_17 (
    .in0(16'h4), .in1(16'h24), .in2(16'h20), .out(out_18), .sel(n4_6_str_2_out_4));  // open: in3
  Multiplexer #(.select(2), .width(16), .enable("false")) multiplexer_18 (
    .in0(16'h4), .in1(16'h14), .in2(16'h10), .out(out_20), .sel(n4_6_str_2_out_4));  // open: in3
  Multiplexer #(.select(2), .width(16), .enable("false")) multiplexer_19 (
    .in0(16'h4), .in1(16'hc), .in2(16'h8), .out(out_22), .sel(n4_6_str_2_out_4));  // open: in3
  dop_another dop_another_1 (
    .in_1(in_1), .out_2(dop_another_1_out_2), .out_3(dop_another_1_out_3), .out_4(dop_another_1_out_4),
    .out_5(dop_another_1_out_5), .out_6(dop_another_1_out_6), .out_7(dop_another_1_out_7));
  Multiplexer #(.width(16), .enable("false")) multiplexer_20 (
    .in0(16'hfffc), .in1({16{1'b1}}), .out(out_24), .sel(in_4[0]));
  _12_str u_12_str_2 (._4(in_2[1]), ._3(in_2[0]), ._1(in_3[0]), ._0(in_4[0]), ._2(in_3[1]), .out_6(n12_str_2_out_6));
  _11_str u_11_str_2 (._4(in_2[1]), ._3(in_2[0]), ._1(in_3[0]), ._0(in_4[0]), ._2(in_3[1]), .out_6(n11_str_2_out_6));
  _8_10_str u_8_10_str_2 (
    ._4(in_2[1]), ._3(in_2[0]), ._1(in_3[0]), ._0(in_4[0]), ._2(in_3[1]), .out_6(n8_10_str_2_out_6));
  _7_str u_7_str_2 (._0(in_4[0]), ._1(in_3[0]), ._2(in_3[1]), .out_4(n7_str_2_out_4));
  _4_6_str u_4_6_str_2 (._0(in_4[0]), ._1(in_3[0]), ._2(in_3[1]), .out_4(n4_6_str_2_out_4));

  assign out_25 = 16'h4000;
  assign out_26 = 16'h2;
  assign out_27 = 16'h8000;
  assign out_28 = 16'h1;

  // Notes on the sheet:
  //   Левая:
  //   Простая стена, тупик
  //   Тупик вблизи
  //   Простая стена, тупик
  //   Ближний квадрат
  //   Дальний квадрат
  //   Ближний квадрат
  //   Тупик вблизи
  //   Ближний квадрат
  //   Тупик вблизи
  //   Ближний квадрат
  //   Отрисовка нижних четвертей
  //   Постоянные нижние строки
  //   Тупик вблизи
  //   Поворот
  //   Проход дальше или поворот у след. клетки
  //   Ближний квадрат
  //   Проход дальше или поворот у след. клетки
  //   Ближний квадрат
  //   Проход дальше или поворот у след. клетки
  //   Тупик вблизи
  //   Следующая клетка - тупик
  //   Проход дальше или поворот у след. клетки
  //   Следующая клетка - тупик
  //   Нет квадрата, есть проход на 2 вперёд
  //   Ближний квадрат
  //   Нет прохода на 2 вперёд
  //   Проход на 2 вперёд
  //   Дальний квадрат
  //   Большой квадрат
  //   Следующая клетка - тупик
  //   Нет квадрата, есть проход на 2 вперёд
  //   Ближний квадрат
  //   Нет прохода на 2 вперёд
  //   Дальний квадрат
  //   Большой квадрат
  //   Правая:
  //   Подсчёт снизу вверх
  //   Первая и вторая строки
  //   Третья строка
  //   Четвёртая строка
  //   Пятая строка
  //   Шестая строка
  //   Седьмая строка
  //   Восьмая строка
  //   Девятая строка
  //   Полная строка, когда есть поворот
  //   Ближний квадрат
  //   Ближний квадрат
  //   Ближний квадрат
  //   Ближний квадрат
  //   Тупик вблизи
  //   Следующая клетка - тупик
  //   Нет квадрата, есть проход на 2 вперёд
  //   Ближний квадрат
  //   Нет прохода на 2 вперёд
  //   Ближний квадрат
  //   Дальний квадрат
  //   Большой квадрат
  //   Тупик вблизи
  //   Следующая клетка - тупик
  //   Нет квадрата, есть проход на 2 вперёд
  //   Нет поворота
  //   Нет квадрата, проход на 2 вперёд
  //   Есть поворот
  //   И только он
  //   И проход вперёд
  //   Дальний квадрат
  //   Большой квадрат
  //   Тупик вблизи
  //   Следующая клетка - тупик
  //   Нет квадрата, есть проход на 2 вперёд
  //   Нет поворота
  //   Нет квадрата, проход на 2 вперёд
  //   Есть поворот
  //   И только он
  //   И проход вперёд
  //   Дальний квадрат
  //   Большой квадрат
  //   Десятая строка
  //   Одиннадцатая строка
  //   Двенадцатая строка
endmodule

module _12_str (
  input  _4,
  input  _3,
  input  _1,
  input  _0,
  input  _2,
  output [2:0] out_6
);

  wire [2:0] multiplexer_1_out;

  Multiplexer #(.select(4), .width(3), .enable("false")) multiplexer_1 (
    .in0(3'b001), .in1(3'b010), .in2(3'b001), .in3(3'b011), .in4(3'b001), .in5(3'b010), .in6(3'b001),
    .in7(3'b110), .in8(3'b001), .in9(3'b010), .in10(3'b001), .in11(3'b011), .in12(3'b100), .in13(3'b101),
    .in14(3'b100), .in15(3'b111), .out(multiplexer_1_out), .sel({_0, _1, _3, _4}));
  Multiplexer #(.width(3), .disabled(0), .enable("false")) multiplexer_2 (
    .in0(3'b000), .in1(multiplexer_1_out), .out(out_6), .sel(_2));

  // Notes on the sheet:
  //   3
  //   1
  //   0
  //   4
  //   2
  //   x
  //   Тупик вблизи
  //   Следующая клетка - тупик
  //   Нет квадрата, есть проход на 2 вперёд
  //   Нет поворота
  //   Нет квадрата, проход на 2 вперёд
  //   Есть поворот
  //   Ближний квадрат
  //   Ближний квадрат
  //   Дальний квадрат
  //   Большой квадрат
  //   И только он
  //   И проход вперёд
  //   Двенадцатая строка
endmodule

module _11_str (
  input  _4,
  input  _3,
  input  _1,
  input  _0,
  input  _2,
  output [2:0] out_6
);

  wire [2:0] multiplexer_1_out;

  Multiplexer #(.select(4), .width(3), .enable("false")) multiplexer_1 (
    .in0(3'b001), .in1(3'b010), .in2(3'b001), .in3(3'b011), .in4(3'b001), .in5(3'b010), .in6(3'b001),
    .in7(3'b110), .in8(3'b001), .in9(3'b010), .in10(3'b001), .in11(3'b011), .in12(3'b100), .in13(3'b101),
    .in14(3'b100), .in15(3'b111), .out(multiplexer_1_out), .sel({_0, _1, _3, _4}));
  Multiplexer #(.width(3), .disabled(0), .enable("false")) multiplexer_2 (
    .in0(3'b000), .in1(multiplexer_1_out), .out(out_6), .sel(_2));

  // Notes on the sheet:
  //   3
  //   1
  //   0
  //   4
  //   2
  //   x
  //   Тупик вблизи
  //   Следующая клетка - тупик
  //   Нет квадрата, есть проход на 2 вперёд
  //   Нет поворота
  //   Нет квадрата, проход на 2 вперёд
  //   Есть поворот
  //   Ближний квадрат
  //   Ближний квадрат
  //   Дальний квадрат
  //   Большой квадрат
  //   И только он
  //   И проход вперёд
  //   Одиннадцатая строка
endmodule

module _8_10_str (
  input  _4,
  input  _3,
  input  _1,
  input  _0,
  input  _2,
  output [2:0] out_6
);

  wire [2:0] multiplexer_1_out;

  Multiplexer #(.select(4), .width(3), .enable("false")) multiplexer_1 (
    .in0(3'b001), .in1(3'b010), .in2(3'b001), .in3(3'b010), .in4(3'b001), .in5(3'b010), .in6(3'b001),
    .in7(3'b101), .in8(3'b001), .in9(3'b010), .in10(3'b001), .in11(3'b010), .in12(3'b011), .in13(3'b100),
    .in14(3'b011), .in15(3'b110), .out(multiplexer_1_out), .sel({_0, _1, _3, _4}));
  Multiplexer #(.width(3), .disabled(0), .enable("false")) multiplexer_2 (
    .in0(3'b000), .in1(multiplexer_1_out), .out(out_6), .sel(_2));

  // Notes on the sheet:
  //   3
  //   1
  //   0
  //   4
  //   2
  //   x
  //   Ближний квадрат
  //   Тупик
  //   Следующая клетка - тупик
  //   Нет квадрата, есть проход на 2 вперёд
  //   Ближний квадрат
  //   Нет прохода на 2 вперёд
  //   Дальний квадрат
  //   Большой квадрат
  //   Проход на 2 вперёд
  //   Восьмая строка
endmodule

module _7_str (
  input  _0,
  input  _1,
  input  _2,
  output [1:0] out_4
);

  wire [1:0] multiplexer_1_out;

  Multiplexer #(.select(2), .width(2), .enable("false")) multiplexer_1 (
    .in0(2'b01), .in1(2'b01), .in2(2'b10), .in3(2'b11), .out(multiplexer_1_out), .sel({_1, _0}));
  Multiplexer #(.width(2), .disabled(0), .enable("false")) multiplexer_2 (
    .in0(2'b00), .in1(multiplexer_1_out), .out(out_4), .sel(_2));

  // Notes on the sheet:
  //   3
  //   1
  //   0
  //   4
  //   2
  //   x
endmodule

module _4_6_str (
  input  _0,
  input  _1,
  input  _2,
  output [1:0] out_4
);

  wire nand_1_out;

  and and_1 (out_4[1], _0, _1, _2);
  nand nand_1 (nand_1_out, _1, _0, _2);
  and and_2 (out_4[0], _2, nand_1_out);

  // Notes on the sheet:
  //   3
  //   1
  //   0
  //   4
  //   2
  //   x
endmodule

module dop (
  input  [2:0] in_1,
  output [15:0] out_2,
  output [15:0] out_3,
  output [15:0] out_4,
  output [15:0] out_5,
  output [15:0] out_6,
  output [15:0] out_7
);

  Multiplexer #(.width(16), .disabled(0), .enable("false")) multiplexer_1 (
    .in0(16'h2220), .in1(16'h223f), .out(out_2), .sel(in_1[1]));
  Multiplexer #(.select(2), .width(16), .disabled(0), .enable("false")) multiplexer_2 (
    .in0(16'h2220), .in1(16'h223f), .in2(16'h23e0), .in3(16'h23ff), .out(out_3), .sel(in_1[2:1]));
  Multiplexer #(.width(16), .disabled(0), .enable("false")) multiplexer_3 (
    .in0(16'h220), .in1(16'h23f), .out(out_5), .sel(in_1[1]));
  Multiplexer #(.select(2), .width(16), .disabled(0), .enable("false")) multiplexer_4 (
    .in0(16'h2020), .in1(16'h203f), .in2(16'h3fe0), .in3(16'h3fff), .out(out_6), .sel(in_1[2:1]));
  Multiplexer #(.select(2), .width(16), .disabled(0), .enable("false")) multiplexer_5 (
    .in0(16'h20), .in1(16'h3f), .in2(16'hffe0), .in3({16{1'b1}}), .out(out_7), .sel(in_1[2:1]));

  assign out_4 = 16'h200;
endmodule

module dop_another (
  input  [2:0] in_1,
  output [15:0] out_2,
  output [15:0] out_3,
  output [15:0] out_4,
  output [15:0] out_5,
  output [15:0] out_6,
  output [15:0] out_7
);

  Multiplexer #(.width(16), .disabled(0), .enable("false")) multiplexer_1 (
    .in0(16'h444), .in1(16'hfc44), .out(out_2), .sel(in_1[1]));
  Multiplexer #(.select(2), .width(16), .disabled(0), .enable("false")) multiplexer_2 (
    .in0(16'h444), .in1(16'h7c4), .in2(16'hfc44), .in3(16'hffc4), .out(out_3), .sel(in_1[1:0]));
  Multiplexer #(.width(16), .disabled(0), .enable("false")) multiplexer_3 (
    .in0(16'h440), .in1(16'hfc40), .out(out_5), .sel(in_1[1]));
  Multiplexer #(.select(2), .width(16), .disabled(0), .enable("false")) multiplexer_4 (
    .in0(16'h404), .in1(16'h7fc), .in2(16'hfc04), .in3(16'hfffc), .out(out_6), .sel(in_1[1:0]));
  Multiplexer #(.select(2), .width(16), .disabled(0), .enable("false")) multiplexer_5 (
    .in0(16'h400), .in1(16'h7ff), .in2(16'hfc00), .in3({16{1'b1}}), .out(out_7), .sel(in_1[1:0]));

  assign out_4 = 16'h40;
endmodule
